// Logisim project 74xx Libary.circ as structural Verilog: 53 circuits, main circuit 7400 show place
module _7400_show_place (
);

  _7400 u_7400_1 ();  // open: _1__1A, _2__1B, _3__1Y, _4__2A, _5__2B, _6__2Y, _7__GND, _14__Vcc, _13__4B, _12__4A, _11__4Y, _10__3B, _9__3A, _8__3Y
  _7425 u_7425_1 ();  // open: _1__1A, _2__1B, _3__NC, _4__1C, _5__1D, _6__1Y, _7__GND, _14__Vcc, _13__2D, _12__2C, _11__NC, _10__2B, _9__2A, _8__2Y
  _7486 u_7486_1 ();  // open: _1__1A, _2__1B, _3__1Y, _4__2A, _5__2B, _6__2Y, _7__GND, _14__Vcc, _13__4B, _12__4A, _11__4Y, _10__3B, _9__3A, _8__3Y
  _74150 u_74150_1 ();  // open: _1__E7, _2__E6, _3__E5, _4__E4, _5__E3, _6__E2, _7__E1, _8__E0, _9__nG, _10__W, _11__D, _12__GND, _24__Vcc, _23__E8, _22__E9, _21__E10, _20__E11, _19__E12, _18__E13, _17__E14, _16__E15, _15__A, _14__B, _13__C
  _74174 u_74174_1 ();  // open: _1__MR_prime, _2__Q0, _3__D0, _4__D1, _5__Q1, _6__D2, _7__Q2, _8__GND, _16__Vcc, _15__Q5, _14__D5, _13__D4, _12__Q4, _11__D3, _10__Q3, _9__CP
  _744075 u_744075_1 ();  // open: _1__1A, _2__1B, _3__2A, _4__2B, _5__2C, _6__2Y, _7__GND, _14__Vcc, _13__1C, _12__1Y, _11__3C, _10__3B, _9__3A, _8__3Y
  _74595 u_74595_1 ();  // open: _1__QB, _2__QC, _3__QD, _4__QE, _5__QF, _6__QG, _7__QH, _8__GND, _16__Vcc, _15__QA, _14__SER, _13__nOE, _12__RCLK, _11__SRCLK, _10__nSRCLR, _9__QH_prime
  _7402 u_7402_1 ();  // open: _1__1Y, _2__1A, _3__1B, _4__2Y, _5__2A, _6__2B, _7__GND, _14__Vcc, _13__4Y, _12__4B, _11__4A, _10__3Y, _9__3B, _8__3A
  _7427 u_7427_1 ();  // open: _1__1A, _2__1B, _3__2A, _4__2B, _5__2C, _6__2Y, _7__GND, _14__Vcc, _13__1C, _12__1Y, _11__3C, _10__3B, _9__3A, _8__3Y
  _7489 u_7489_1 ();  // open: _1__A0, _2__nCS, _3__nWE, _4__D1, _5__nO1, _6__D2, _7__nO2, _8__GND, _16__Vcc, _15__A1, _14__A2, _13__A3, _12__D4, _11__nO4, _10__D3, _9__nO3
  _74574 u_74574_1 ();  // open: _1__nOE, _2__D1, _3__D2, _4__D3, _5__D4, _6__D5, _7__D6, _8__D7, _9__D8, _10__GND, _20__Vcc, _19__Q0, _18__Q1, _17__Q2, _16__Q3, _15__Q4, _14__Q5, _13__Q6, _12__Q7, _11__CP
  _7404 u_7404_1 ();  // open: _1__1A, _2__1Y, _3__2A, _4__2Y, _5__3A, _6__3Y, _7__GND, _14__Vcc, _13__6A, _12__6Y, _11__5A, _10__5Y, _9__4A, _8__4Y
  _7430 u_7430_1 ();  // open: _1__1A, _2__1B, _3__1C, _4__1D, _5__1E, _6__1F, _7__GND, _14__Vcc, _13__NC, _12__1H, _11__1G, _10__NC, _9__NC, _8__3Y
  _74151 u_74151_1 ();  // open: _1__D3, _2__D2, _3__D1, _4__D0, _5__Y, _6__W, _7__nG, _8__GND, _16__Vcc, _15__D4, _14__D5, _13__D6, _12__D7, _11__A, _10__B, _9__C
  _74198 u_74198_1 ();  // open: _1__S0, _2__Dsr, _3__P0, _4__Q0, _5__P1, _6__Q1, _7__P2, _8__Q2, _9__P3, _10__Q3, _11__CP, _12__GND, _24__Vcc, _23__S1, _22__Dsl, _21__P7, _20__Q7, _19__P6, _18__Q6, _17__P5, _16__Q5, _15__P4, _14__Q4, _13__nMR
  _74181 u_74181_1 ();  // open: _1__nB0, _2__nA0, _3__S3, _4__S2, _5__S1, _6__S0, _7__Cn, _8__M, _9__nF0, _10__nF1, _11__nF2, _12__GND, _24__Vcc, _23__nA1, _22__nB1, _21__nA2, _20__nB2, _19__nA3, _18__nB3, _17__nG, _16__Cn_4, _15__nP, _14__A_B, _13__nF3
  _7407 u_7407_1 ();  // open: _1__1A, _2__1Y, _3__2A, _4__2Y, _5__3A, _6__3Y, _7__GND, _14__Vcc, _13__6A, _12__6Y, _11__5A, _10__5Y, _9__4A, _8__4Y
  _7432 u_7432_1 ();  // open: _1__1A, _2__1B, _3__1Y, _4__2A, _5__2B, _6__2Y, _7__GND, _14__Vcc, _13__4B, _12__4A, _11__4Y, _10__3B, _9__3A, _8__3Y
  _74116 u_74116_1 ();  // open: _1__nMRa, _2__nE0a, _3__nE1a, _4__D0a, _5__Q0a, _6__D1a, _7__Q1a, _8__D2a, _9__Q2a, _10__D3a, _11__Q3a, _12__GND, _24__Vcc, _23__Q3b, _22__D3b, _21__Q2b, _20__D2b, _19__Q1b, _18__D1b, _17__Q0b, _16__D0b, _15__nE1b, _14__nE0b, _13__nMRb
  _74153 u_74153_1 ();  // open: _1__nG1, _2__B, _3__1C3, _4__1C2, _5__1C1, _6__1C0, _7__Y1, _8__GND, _16__Vcc, _15__nG2, _14__A, _13__2C3, _12__2C2, _11__2C1, _10__2C0, _9__Y2
  _74238 u_74238_1 ();  // open: _1__A0, _2__A1, _3__A2, _4__E1_prime, _5__E2_prime, _6__E3, _7__Y7, _8__GND, _16__Vcc, _15__Y0, _14__Y1, _13__Y2, _12__Y3, _11__Y4, _10__Y5, _9__Y6
  _74377 u_74377_1 ();  // open: _1__nE, _2__Q0, _3__D0, _4__D1, _5__Q1, _6__Q2, _7__D2, _8__D3, _9__Q3, _10__GND, _20__Vcc, _19__Q7, _18__D7, _17__D6, _16__Q6, _15__Q5, _14__D5, _13__D4, _12__Q4, _11__CP
  _7408 u_7408_1 ();  // open: _1__1A, _2__1B, _3__1Y, _4__2A, _5__2B, _6__2Y, _7__GND, _14__Vcc, _13__4B, _12__4A, _11__4Y, _10__3B, _9__3A, _8__3Y
  _7448 u_7448_1 ();  // open: _1__B, _2__C, _3__nLT, _4__NC, _5__nRBI, _6__D, _7__A, _8__GND, _16__Vcc, _15__f, _14__g, _13__a, _12__b, _11__c, _10__d, _9__e
  _74133 u_74133_1 ();  // open: _1__A, _2__B, _3__C, _4__D, _5__E, _6__F, _7__G, _8__GND, _16__Vcc, _15__M, _14__L, _13__K, _12__J, _11__I, _10__H, _9__Y
  _74253 u_74253_1 ();  // open: _1__1G, _2__Sb, _3__1C3, _4__1C2, _5__1C1, _6__1C0, _7__1Y, _8__GND, _16__Vcc, _15__2G, _14__Sa, _13__2C3, _12__2C2, _11__2C1, _10__2C0, _9__2Y
  _74273 u_74273_1 ();  // open: _1__nCLR, _2__Q0, _3__D0, _4__D1, _5__Q1, _6__Q2, _7__D2, _8__D3, _9__Q3, _10__GND, _20__Vcc, _19__Q7, _18__D7, _17__D6, _16__Q6, _15__Q5, _14__D5, _13__D4, _12__Q4, _11__CP
  _27C512_1 u_27c512_1_1 ();  // open: _1__A15, _2__A12, _3__A7, _4__A6, _5__A5, _6__A4, _7__A3, _8__A2, _9__A1, _10__A0, _11__O0, _12__O1, _13__O2, _14__GND, _28__Vcc, _27__A14, _26__A13, _25__A8, _24__A9, _23__A11, _22__nOE_Vpp, _21__A10, _20__nCE, _19__O7, _18__O6, _17__O5, _16__O4, _15__O3
  _7410 u_7410_1 ();  // open: _1__1A, _2__1B, _3__2A, _4__2B, _5__2C, _6__2Y, _7__GND, _14__Vcc, _13__1C, _12__1Y, _11__3C, _10__3B, _9__3A, _8__3Y
  _7451 u_7451_1 ();  // open: _1__1A, _2__2A, _3__2B, _4__2C, _5__2D, _6__2Y, _7__GND, _14__Vcc, _13__1B, _12__NC, _11__NC, _10__1D, _9__1C, _8__1Y
  _74138 u_74138_1 ();  // open: _1__A, _2__B, _3__C, _4__G2A, _5__G2B, _6__G1, _7__Y7, _8__GND, _16__Vcc, _15__Y0, _14__Y1, _13__Y2, _12__Y3, _11__Y4, _10__Y5, _9__Y6
  _74154 u_74154_1 ();  // open: _1__Y0, _2__Y1, _3__Y2, _4__Y3, _5__Y4, _6__Y5, _7__Y6, _8__Y7, _9__Y8, _10__Y9, _11__Y10, _12__GND, _24__Vcc, _23__A, _22__B, _21__C, _20__D, _19__G2, _18__G1, _17__Y15, _16__Y14, _15__Y13, _14__Y12, _13__Y11
  _7411 u_7411_1 ();  // open: _1__1A, _2__1B, _3__2A, _4__2B, _5__2C, _6__2Y, _7__GND, _14__Vcc, _13__1C, _12__1Y, _11__3C, _10__3B, _9__3A, _8__3Y
  _74139 u_74139_1 ();  // open: _1__1G, _2__1A, _3__1B, _4__1Y0, _5__1Y1, _6__1Y2, _7__1Y3, _8__GND, _16__Vcc, _15__2G, _14__2A, _13__2B, _12__2Y0, _11__2Y1, _10__2Y2, _9__2Y3
  _74157 u_74157_1 ();  // open: _1__S, _2__A1, _3__B1, _4__Y1, _5__A2, _6__B2, _7__Y2, _8__GND, _16__Vcc, _15__G, _14__A4, _13__B4, _12__Y4, _11__A3, _10__B3, _9__Y3
  _74260 u_74260_1 ();  // open: _1__1A, _2__1B, _3__1E, _4__1C, _5__1D, _6__1Y, _7__GND, _14__Vcc, _13__2D, _12__2C, _11__2E, _10__2B, _9__2A, _8__2Y
  _74283 u_74283_1 ();  // open: _1__S2, _2__B2, _3__A2, _4__S1, _5__A1, _6__B1, _7__C0, _8__GND, _16__Vcc, _15__B3, _14__A3, _13__S3, _12__A4, _11__B4, _10__S4, _9__C4
  _7474 u_7474_1 ();  // open: _1__CLR1, _2__D1, _3__CLK1, _4__PR1, _5__Q1, _6__nQ1, _7__GND, _14__Vcc, _13__CLR2, _12__D2, _11__CLK2, _10__PR2, _9__Q2, _8__nQ2
  _74161 u_74161_1 ();  // open: _1__nMR, _2__CP, _3__D0, _4__D1, _5__D2, _6__D3, _7__CEP, _8__GND, _16__Vcc, _15__TC, _14__Q0, _13__Q1, _12__Q2, _11__O3, _10__CET, _9__nPE
  _74371 u_74371_1 ();  // open: _1__AD_A, _2__AD_B, _3__AD_C, _4__AD_D, _5__AD_E, _6__DO_1, _7__DO_2, _8__DO_3, _9__DO_4, _10__GND, _20__Vcc, _19__AD_H, _18__AD_G, _17__AD_F, _16__nS_2, _15__nS_1, _14__DO_8, _13__DO_7, _12__DO_6, _11__DO_5
  _74240 u_74240_1 ();  // open: _1___1G, _2__1A1, _3__2Y4, _4__1A2, _5__2Y3, _6__1A3, _7__2Y2, _8__1A4, _9__2Y1, _10__GND, _20__Vcc, _19___2G, _18__1Y1, _17__2A4, _16__1Y2, _15__2A3, _14__1Y3, _13__2A2, _12__1Y4, _11__2A1
  _7420 u_7420_1 ();  // open: _1__1A, _2__1B, _3__NC, _4__1C, _5__1D, _6__1Y, _7__GND, _14__Vcc, _13__2D, _12__2C, _11__NC, _10__2B, _9__2A, _8__2Y
  _7476 u_7476_1 ();  // open: _1__CLK1, _2__PR1, _3__CLR1, _4__J1, _5__VCC, _6__CLK2, _7__PR2, _8__CLR2, _16__K1, _15__Q1, _14__nQ1, _13__GND, _12__K2, _11__Q2, _10__nQ2, _9__J2
  _74147 u_74147_1 ();  // open: _1__I4, _2__I5, _3__I6, _4__I7, _5__I8, _6__A2, _7__A1, _8__GND, _16__Vcc, _15__NC, _14__A3, _13__I3, _12__I2, _11__I1, _10__I9, _9__A0
  _74163 u_74163_1 ();  // open: _1__nMR, _2__CP, _3__D0, _4__D1, _5__D2, _6__D3, _7__CEP, _8__GND, _16__Vcc, _15__TC, _14__Q0, _13__Q1, _12__Q2, _11__O3, _10__CET, _9__nPE
  _7421 u_7421_1 ();  // open: _1__1A, _2__1B, _3__NC, _4__1C, _5__1D, _6__1Y, _7__GND, _14__Vcc, _13__2D, _12__2C, _11__NC, _10__2B, _9__2A, _8__2Y
  _7483 u_7483_1 ();  // open: _1__A4, _2__S3, _3__A3, _4__B3, _5__Vcc, _6__S2, _7__B2, _8__A2, _16__B4, _15__S4, _14__Cout, _13__Cin, _12__GND, _11__B1, _10__A1, _9__S1
  _74148 u_74148_1 ();  // open: _1__I4, _2__I5, _3__I6, _4__I7, _5__nEI__NC, _6__A2, _7__A1, _8__GND, _16__Vcc, _15__nEO__NC, _14__nGS__NC, _13__I3, _12__I2, _11__I1, _10__I0, _9__A0
  _74682 u_74682_1 ();  // open: _1__A___B, _2__A0, _3__B0, _4__A1, _5__B1, _6__A2, _7__B2, _8__A3, _9__B3, _10__GND, _20__Vcc, _19__A___B, _18__B7, _17__A7, _16__B6, _15__A6, _14__B5, _13__A5, _12__B4, _11__A4
  _74244 u_74244_1 ();  // open: _1___1G, _2__1A1, _3__2Y4, _4__1A2, _5__2Y3, _6__1A3, _7__2Y2, _8__1A4, _9__2Y1, _10__GND, _20__Vcc, _19___2G, _18__1Y1, _17__2A4, _16__1Y2, _15__2A3, _14__1Y3, _13__2A2, _12__1Y4, _11__2A1

  // Notes on the sheet:
  //   Ben Oztalay, 2010
  //   benoztalay.wordpress.com
  //   This collection excludes duplicate integrated circuits, such as the 7401, since it has the same function as the 7400, it just has open-collector outputs
  //   quad 2-input
  //   NAND
  //   dual 4-input
  //   NOR
  //   quad 2-input
  //   XOR
  //   16 to 1 MUX
  //   hex D-type flip-flop
  //   with reset; positive-edge
  //   triple 3-input
  //   8-Bit Shifter 
  //   Serial-in to parallel-out
  //   This is obviously an incomplete collection, although I believe it covers many applications. Feel free to add to it, I just ask that you follow the same
  //   conventions I've used and give credit where credit is due. Thanks!
  //   This is a library of 7400 series integrated circuits
  //   quad 2-input
  //   NOR
  //   triple 3-input
  //   NOR
  //   64-bit RAM
  //   8-bit bidirectional
  //   universal shift register
  //   Octal D-type flip-flop
  //   positive edge-trigger
  //   3-states
  //   hex inverter
  //   8-input NAND
  //   dual 4-bit latches
  //   8 to 1 MUX
  //   4-Bit ALU
  //   hex buffer
  //   quad 2-input
  //   dual 4 to 1 MUX
  //   3-to-8 line
  //   decoder/demultiplexer
  //   Octal D-type flip-flop
  //   positive edge-trigger
  //   write enable
  //   Pin placement reflects the arrangement of the actual integrated circuits, and power and ground pins are just dummy pins
  //   quad 2-input
  //   BCD to 7-segment
  //   OR
  //   13-input NAND
  //   4 to 16 decoder
  //   dual 4 to 1 MUX
  //   Octal D-FlipFlop
  //   w/ CLEAR
  //   64K x 8-bit EPROM
  //   triple 3-input
  //   AND
  //   decoder
  //   3 to 8 decoder
  //   NAND
  //   dual 2-wide
  //   2-input AOI
  //   quad 2 to 1
  //   MUX
  //   dual 5-input
  //   NOR
  //   4-Bit Binary Adder
  //   w/ Fast Carry
  //   triple 3-input
  //   AND
  //   dual D
  //   flip-flop
  //   dual 2 to 4 
  //   decoder
  //   sync. 4-bit
  //   binary counter
  //   w/ async. clear
  //   256x8 ROM
  //   Octal Inverted
  //   Tristate Buffer
  //   dual 4-input
  //   NAND
  //   dual JK
  //   flip-flop
  //   10 to 4 priority
  //   encoder
  //   sync. 4-bit
  //   binary counter
  //   w/ sync. clear
  //   8-bit magnitude
  //   comparator
  //   Octal Tristate Buffer
  //   dual 4-input
  //   AND
  //   4-bit binary
  //   full adder
  //   8 to 3 priority
  //   encoder
endmodule

module _7400 (
  input  _1__1A,
  input  _14__Vcc,
  input  _2__1B,
  input  _13__4B,
  input  _12__4A,
  input  _4__2A,
  input  _5__2B,
  input  _10__3B,
  input  _9__3A,
  input  _7__GND,
  output _3__1Y,
  output _11__4Y,
  output _6__2Y,
  output _8__3Y
);

  nand nand_1 (_3__1Y, _2__1B, _1__1A);
  nand nand_2 (_6__2Y, _5__2B, _4__2A);
  nand nand_3 (_11__4Y, _13__4B, _12__4A);
  nand nand_4 (_8__3Y, _10__3B, _9__3A);

  // Notes on the sheet:
  //   7400: quad NAND
endmodule

module _7402 (
  input  _14__Vcc,
  input  _2__1A,
  input  _3__1B,
  input  _12__4B,
  input  _11__4A,
  input  _5__2A,
  input  _6__2B,
  input  _9__3B,
  input  _7__GND,
  input  _8__3A,
  output _1__1Y,
  output _13__4Y,
  output _4__2Y,
  output _10__3Y
);

  nor nor_1 (_1__1Y, _2__1A, _3__1B);
  nor nor_2 (_4__2Y, _5__2A, _6__2B);
  nor nor_3 (_13__4Y, _11__4A, _12__4B);
  nor nor_4 (_10__3Y, _8__3A, _9__3B);

  // Notes on the sheet:
  //   7402: quad NOR
endmodule

module _7404 (
  input  _1__1A,
  input  _14__Vcc,
  input  _13__6A,
  input  _3__2A,
  input  _11__5A,
  input  _5__3A,
  input  _9__4A,
  input  _7__GND,
  output _2__1Y,
  output _12__6Y,
  output _4__2Y,
  output _10__5Y,
  output _6__3Y,
  output _8__4Y
);

  not not_1 (_2__1Y, _1__1A);
  not not_2 (_4__2Y, _3__2A);
  not not_3 (_6__3Y, _5__3A);
  not not_4 (_12__6Y, _13__6A);
  not not_5 (_10__5Y, _11__5A);
  not not_6 (_8__4Y, _9__4A);

  // Notes on the sheet:
  //   7407: hex inverter
endmodule

module _7407 (
  input  _1__1A,
  input  _14__Vcc,
  input  _13__6A,
  input  _3__2A,
  input  _11__5A,
  input  _5__3A,
  input  _9__4A,
  input  _7__GND,
  output _2__1Y,
  output _12__6Y,
  output _4__2Y,
  output _10__5Y,
  output _6__3Y,
  output _8__4Y
);

  buf buffer_1 (_2__1Y, _1__1A);
  buf buffer_2 (_4__2Y, _3__2A);
  buf buffer_3 (_6__3Y, _5__3A);
  buf buffer_4 (_12__6Y, _13__6A);
  buf buffer_5 (_10__5Y, _11__5A);
  buf buffer_6 (_8__4Y, _9__4A);

  // Notes on the sheet:
  //   7407: hex buffer
endmodule

module _7408 (
  input  _1__1A,
  input  _14__Vcc,
  input  _2__1B,
  input  _13__4B,
  input  _12__4A,
  input  _4__2A,
  input  _5__2B,
  input  _10__3B,
  input  _9__3A,
  input  _7__GND,
  output _3__1Y,
  output _11__4Y,
  output _6__2Y,
  output _8__3Y
);

  and and_1 (_3__1Y, _2__1B, _1__1A);
  and and_2 (_6__2Y, _5__2B, _4__2A);
  and and_3 (_11__4Y, _13__4B, _12__4A);
  and and_4 (_8__3Y, _10__3B, _9__3A);

  // Notes on the sheet:
  //   7408: quad AND
endmodule

module _7410 (
  input  _1__1A,
  input  _14__Vcc,
  input  _2__1B,
  input  _13__1C,
  input  _3__2A,
  input  _4__2B,
  input  _11__3C,
  input  _5__2C,
  input  _10__3B,
  input  _9__3A,
  input  _7__GND,
  output _12__1Y,
  output _6__2Y,
  output _8__3Y
);

  nand nand_1 (_6__2Y, _5__2C, _4__2B, _3__2A);
  nand nand_2 (_12__1Y, _2__1B, _1__1A, _13__1C);
  nand nand_3 (_8__3Y, _11__3C, _10__3B, _9__3A);

  // Notes on the sheet:
  //   7410: triple 3-input NAND 
endmodule

module _7411 (
  input  _1__1A,
  input  _14__Vcc,
  input  _2__1B,
  input  _13__1C,
  input  _3__2A,
  input  _4__2B,
  input  _11__3C,
  input  _5__2C,
  input  _10__3B,
  input  _9__3A,
  input  _7__GND,
  output _12__1Y,
  output _6__2Y,
  output _8__3Y
);

  and and_1 (_6__2Y, _5__2C, _3__2A);
  and and_2 (_12__1Y, _2__1B, _13__1C);
  and and_3 (_8__3Y, _11__3C, _9__3A);

  // Notes on the sheet:
  //   7411: triple 3-input AND 
endmodule

module _7420 (
  input  _1__1A,
  input  _14__Vcc,
  input  _2__1B,
  input  _13__2D,
  input  _3__NC,
  input  _12__2C,
  input  _4__1C,
  input  _11__NC,
  input  _5__1D,
  input  _10__2B,
  input  _9__2A,
  input  _7__GND,
  output _6__1Y,
  output _8__2Y
);

  nand nand_1 (_6__1Y, _5__1D, _4__1C, _2__1B, _1__1A);
  nand nand_2 (_8__2Y, _13__2D, _12__2C, _10__2B, _9__2A);

  // Notes on the sheet:
  //   7420: dual 4-input NAND
endmodule

module _7421 (
  input  _1__1A,
  input  _14__Vcc,
  input  _2__1B,
  input  _13__2D,
  input  _3__NC,
  input  _12__2C,
  input  _4__1C,
  input  _11__NC,
  input  _5__1D,
  input  _10__2B,
  input  _9__2A,
  input  _7__GND,
  output _6__1Y,
  output _8__2Y
);

  and and_1 (_6__1Y, _5__1D, _4__1C, _2__1B, _1__1A);
  and and_2 (_8__2Y, _13__2D, _12__2C, _10__2B, _9__2A);

  // Notes on the sheet:
  //   7421: dual 4-input AND
endmodule

module _7425 (
  input  _1__1A,
  input  _14__Vcc,
  input  _2__1B,
  input  _13__2D,
  input  _3__NC,
  input  _12__2C,
  input  _4__1C,
  input  _11__NC,
  input  _5__1D,
  input  _10__2B,
  input  _9__2A,
  input  _7__GND,
  output _6__1Y,
  output _8__2Y
);

  nor nor_1 (_6__1Y, _5__1D, _4__1C, _2__1B, _1__1A);
  nor nor_2 (_8__2Y, _13__2D, _12__2C, _10__2B, _9__2A);

  // Notes on the sheet:
  //   7425: dual 4-input NOR
endmodule

module _7427 (
  input  _1__1A,
  input  _14__Vcc,
  input  _2__1B,
  input  _13__1C,
  input  _3__2A,
  input  _4__2B,
  input  _11__3C,
  input  _5__2C,
  input  _10__3B,
  input  _9__3A,
  input  _7__GND,
  output _12__1Y,
  output _6__2Y,
  output _8__3Y
);

  nor nor_1 (_6__2Y, _5__2C, _4__2B, _3__2A);
  nor nor_2 (_12__1Y, _2__1B, _1__1A, _13__1C);
  nor nor_3 (_8__3Y, _11__3C, _10__3B, _9__3A);

  // Notes on the sheet:
  //   7427: triple 3-input NOR 
endmodule

module _7430 (
  input  _1__1A,
  input  _14__Vcc,
  input  _2__1B,
  input  _13__NC,
  input  _3__1C,
  input  _12__1H,
  input  _4__1D,
  input  _11__1G,
  input  _5__1E,
  input  _10__NC,
  input  _6__1F,
  input  _9__NC,
  input  _7__GND,
  output _8__3Y
);

  nand nand_1 (_8__3Y, _6__1F, _5__1E, _4__1D, _3__1C, _2__1B, _1__1A, _12__1H, _11__1G);

  // Notes on the sheet:
  //   7430: 8-input NAND 
endmodule

module _7432 (
  input  _1__1A,
  input  _14__Vcc,
  input  _2__1B,
  input  _13__4B,
  input  _12__4A,
  input  _4__2A,
  input  _5__2B,
  input  _10__3B,
  input  _9__3A,
  input  _7__GND,
  output _3__1Y,
  output _11__4Y,
  output _6__2Y,
  output _8__3Y
);

  or or_1 (_3__1Y, _2__1B, _1__1A);
  or or_2 (_6__2Y, _5__2B, _4__2A);
  or or_3 (_11__4Y, _13__4B, _12__4A);
  or or_4 (_8__3Y, _10__3B, _9__3A);

  // Notes on the sheet:
  //   7432: quad OR
endmodule

module _7448 (
  input  _1__B,
  input  _16__Vcc,
  input  _2__C,
  input  _3__nLT,
  input  _4__NC,
  input  _5__nRBI,
  input  _6__D,
  input  _7__A,
  input  _8__GND,
  output _15__f,
  output _14__g,
  output _13__a,
  output _12__b,
  output _11__c,
  output _10__d,
  output _9__e
);

  wire nand_1_out, nand_2_out, nand_3_out, nand_4_out, nand_5_out, nand_6_out, nand_7_out, nand_8_out,
       nand_9_out, nand_10_out, nand_11_out, nand_12_out, nand_13_out, nand_14_out, nand_15_out, nand_16_out,
       nand_17_out, nand_18_out, nand_19_out, nand_20_out, nand_21_out, nand_22_out, nand_23_out,
       nand_24_out, nand_25_out, not_1_out, not_2_out, not_3_out;

  nand nand_1 (nand_1_out, _7__A, _3__nLT);
  nand nand_2 (nand_2_out, _1__B, _3__nLT);
  nand nand_3 (nand_3_out, _2__C, _3__nLT);
  not not_1 (not_1_out, _6__D);
  not not_2 (not_2_out, _5__nRBI);
  nand nand_4 (nand_4_out, nand_1_out, nand_8_out);
  nand nand_5 (nand_5_out, nand_2_out, nand_8_out);
  nand nand_6 (nand_6_out, nand_3_out, nand_8_out);
  nand nand_7 (nand_7_out, not_1_out, nand_8_out);
  nand nand_8 (nand_8_out, _3__nLT, not_2_out, not_1_out, nand_3_out, nand_2_out, nand_1_out);
  nand nand_9 (nand_9_out, nand_5_out, nand_7_out);
  nand nand_10 (nand_10_out, nand_1_out, nand_6_out);
  nand nand_11 (nand_11_out, nand_4_out, nand_2_out, nand_3_out, not_1_out);
  nand nand_12 (nand_12_out, nand_5_out, nand_7_out);
  nand nand_13 (nand_13_out, nand_4_out, nand_2_out, nand_6_out);
  nand nand_14 (nand_14_out, nand_1_out, nand_5_out, nand_6_out);
  nand nand_15 (nand_15_out, nand_6_out, nand_7_out);
  nand nand_16 (nand_16_out, nand_1_out, nand_5_out, nand_3_out);
  nand nand_17 (nand_17_out, nand_4_out, nand_2_out, nand_3_out);
  nand nand_18 (nand_18_out, nand_1_out, nand_2_out, nand_6_out);
  nand nand_19 (nand_19_out, nand_4_out, nand_5_out, nand_6_out);
  not not_3 (not_3_out, nand_4_out);
  nand nand_20 (nand_20_out, nand_2_out, nand_6_out);
  nand nand_21 (nand_21_out, nand_4_out, nand_5_out);
  nand nand_22 (nand_22_out, nand_5_out, nand_3_out);
  nand nand_23 (nand_23_out, nand_4_out, nand_3_out, not_1_out);
  nand nand_24 (nand_24_out, nand_4_out, nand_5_out, nand_6_out);
  nand nand_25 (nand_25_out, nand_2_out, nand_3_out, not_1_out, _3__nLT);
  and and_1 (_13__a, nand_9_out, nand_10_out, nand_11_out);
  and and_2 (_12__b, nand_12_out, nand_13_out, nand_14_out);
  and and_3 (_11__c, nand_15_out, nand_16_out);
  and and_4 (_10__d, nand_17_out, nand_18_out, nand_19_out);
  and and_5 (_9__e, not_3_out, nand_20_out);
  and and_6 (_15__f, nand_21_out, nand_22_out, nand_23_out);
  and and_7 (_14__g, nand_24_out, nand_25_out);

  // Notes on the sheet:
  //   7448: BCD to 7-segment decoder
endmodule

module _7451 (
  input  _1__1A,
  input  _14__Vcc,
  input  _2__2A,
  input  _13__1B,
  input  _3__2B,
  input  _12__NC,
  input  _4__2C,
  input  _11__NC,
  input  _5__2D,
  input  _10__1D,
  input  _9__1C,
  input  _7__GND,
  output _6__2Y,
  output _8__1Y
);

  wire and_1_out, and_2_out, and_3_out, and_4_out;

  nor nor_1 (_8__1Y, and_3_out, and_4_out);
  and and_1 (and_1_out, _2__2A, _3__2B);
  and and_2 (and_2_out, _4__2C, _5__2D);
  and and_3 (and_3_out, _1__1A, _13__1B);
  and and_4 (and_4_out, _10__1D, _9__1C);
  nor nor_2 (_6__2Y, and_2_out, and_1_out);

  // Notes on the sheet:
  //   7451: dual 2-wide 2-input AND-OR-Invert gate
endmodule

module _7474 (
  input  _1__CLR1,
  input  _14__Vcc,
  input  _2__D1,
  input  _13__CLR2,
  input  _3__CLK1,
  input  _12__D2,
  input  _4__PR1,
  input  _11__CLK2,
  input  _10__PR2,
  input  _7__GND,
  output _5__Q1,
  output _6__nQ1,
  output _9__Q2,
  output _8__nQ2
);

  D_Flip_Flop d_ff_1 (
    .clk(_3__CLK1), .D(_2__D1), .Q(_5__Q1), .Qn(_6__nQ1), .preset(_4__PR1), .reset(_1__CLR1));  // open: en
  D_Flip_Flop d_ff_2 (
    .clk(_11__CLK2), .D(_12__D2), .Q(_9__Q2), .Qn(_8__nQ2), .preset(_10__PR2), .reset(_13__CLR2));  // open: en

  // Notes on the sheet:
  //   7474: dual D-type flip flop
endmodule

module _7476 (
  input  _1__CLK1,
  input  _16__K1,
  input  _2__PR1,
  input  _3__CLR1,
  input  _4__J1,
  input  _13__GND,
  input  _5__VCC,
  input  _12__K2,
  input  _6__CLK2,
  input  _7__PR2,
  input  _8__CLR2,
  input  _9__J2,
  output _15__Q1,
  output _14__nQ1,
  output _11__Q2,
  output _10__nQ2
);

  J_K_Flip_Flop j_k_ff_1 (
    .J(_4__J1), .clk(_1__CLK1), .K(_16__K1), .Q(_15__Q1), .Qn(_14__nQ1), .preset(_2__PR1), .reset(_3__CLR1));  // open: en
  J_K_Flip_Flop j_k_ff_2 (
    .J(_9__J2), .clk(_6__CLK2), .K(_12__K2), .Q(_11__Q2), .Qn(_10__nQ2), .preset(_7__PR2), .reset(_8__CLR2));  // open: en

  // Notes on the sheet:
  //   7476: dual JK-type flip flop
endmodule

module _7483 (
  input  _1__A4,
  input  _16__B4,
  input  _3__A3,
  input  _14__Cout,
  input  _4__B3,
  input  _13__Cin,
  input  _5__Vcc,
  input  _12__GND,
  input  _11__B1,
  input  _7__B2,
  input  _10__A1,
  input  _8__A2,
  output _2__S3,
  output _15__S4,
  output _6__S2,
  output _9__S1
);

  wire and_1_out, and_2_out, and_3_out, and_4_out, and_5_out, and_6_out, and_7_out, and_8_out, and_9_out,
       and_10_out, and_11_out, and_12_out, and_13_out, and_14_out, nand_1_out, nand_2_out, nand_3_out,
       nand_4_out, nor_1_out, nor_2_out, nor_3_out, nor_4_out, nor_6_out, nor_7_out, nor_8_out, not_1_out,
       not_2_out, not_3_out, not_4_out, not_5_out, not_6_out;

  nand nand_1 (nand_1_out, _16__B4, _1__A4);
  nor nor_1 (nor_1_out, _16__B4, _1__A4);
  nand nand_2 (nand_2_out, _4__B3, _3__A3);
  nor nor_2 (nor_2_out, _4__B3, _3__A3);
  nand nand_3 (nand_3_out, _7__B2, _8__A2);
  nor nor_3 (nor_3_out, _7__B2, _8__A2);
  nand nand_4 (nand_4_out, _11__B1, _10__A1);
  nor nor_4 (nor_4_out, _11__B1, _10__A1);
  and and_1 (and_1_out, nor_2_out, nand_1_out);
  and and_2 (and_2_out, nor_3_out, nand_1_out, nand_2_out);
  and and_3 (and_3_out, nor_4_out, nand_1_out, nand_2_out, nand_3_out);
  and and_4 (and_4_out, nand_1_out, nand_2_out, nand_3_out, nand_4_out, not_2_out);
  not not_1 (not_1_out, nor_1_out);
  and and_5 (and_5_out, nor_3_out, nand_2_out);
  and and_6 (and_6_out, nor_4_out, nand_2_out, nand_3_out);
  and and_7 (and_7_out, nand_2_out, nand_3_out, nand_4_out, not_2_out);
  not not_2 (not_2_out, _13__Cin);
  not not_3 (not_3_out, nor_2_out);
  and and_8 (and_8_out, nor_4_out, nand_3_out);
  and and_9 (and_9_out, nand_3_out, nand_4_out, not_2_out);
  not not_4 (not_4_out, nor_3_out);
  and and_10 (and_10_out, nand_4_out, not_2_out);
  not not_5 (not_5_out, nor_4_out);
  not not_6 (not_6_out, not_2_out);
  nor nor_5 (_14__Cout, nor_1_out, and_1_out, and_2_out, and_3_out, and_4_out);
  and and_11 (and_11_out, nand_1_out, not_1_out);
  and and_12 (and_12_out, nand_2_out, not_3_out);
  and and_13 (and_13_out, nand_3_out, not_4_out);
  and and_14 (and_14_out, nand_4_out, not_5_out);
  xor xor_1 (_15__S4, and_11_out, nor_6_out);
  nor nor_6 (nor_6_out, nor_2_out, and_5_out, and_6_out, and_7_out);
  xor xor_2 (_2__S3, and_12_out, nor_7_out);
  nor nor_7 (nor_7_out, nor_3_out, and_8_out, and_9_out);
  xor xor_3 (_6__S2, and_13_out, nor_8_out);
  nor nor_8 (nor_8_out, nor_4_out, and_10_out);
  xor xor_4 (_9__S1, and_14_out, not_6_out);

  // Notes on the sheet:
  //   7483: 4-bit full adder
endmodule

module _7486 (
  input  _1__1A,
  input  _14__Vcc,
  input  _2__1B,
  input  _13__4B,
  input  _12__4A,
  input  _4__2A,
  input  _5__2B,
  input  _10__3B,
  input  _9__3A,
  input  _7__GND,
  output _3__1Y,
  output _11__4Y,
  output _6__2Y,
  output _8__3Y
);

  xor xor_1 (_3__1Y, _2__1B, _1__1A);
  xor xor_2 (_6__2Y, _5__2B, _4__2A);
  xor xor_3 (_11__4Y, _13__4B, _12__4A);
  xor xor_4 (_8__3Y, _10__3B, _9__3A);

  // Notes on the sheet:
  //   7486: quad XOR
endmodule

module _7489 (
  input  _1__A0,
  input  _16__Vcc,
  input  _2__nCS,
  input  _15__A1,
  input  _3__nWE,
  input  _14__A2,
  input  _4__D1,
  input  _13__A3,
  input  _12__D4,
  input  _6__D2,
  input  _10__D3,
  input  _8__GND,
  output _5__nO1,
  output _11__nO4,
  output _7__nO2,
  output _9__nO3
);

  wire not_1_out, not_2_out, or_1_out;
  wire [3:0] ram_1_data;

  not not_1 (not_1_out, _2__nCS);
  not not_2 (not_2_out, _3__nWE);
  or or_1 (or_1_out, not_2_out, not_1_out);
  RAM #(.addrWidth(4), .dataWidth(4), .bus("separate")) ram_1 (
    .addr({_13__A3, _14__A2, _15__A1, _1__A0}), .din({_12__D4, _10__D3, _6__D2, _4__D1}), .data(ram_1_data),
    .sel(not_1_out), .clk(not_2_out), .ld(or_1_out));  // open: str, clr
  assign {_11__nO4, _9__nO3, _7__nO2, _5__nO1} = ~ram_1_data;  // NOT_Gate not_3, 4 bits wide

  // Notes on the sheet:
  //   7489: 64-bit RAM
endmodule

module _74116 (
  input  _1__nMRa,
  input  _24__Vcc,
  input  _2__nE0a,
  input  _3__nE1a,
  input  _22__D3b,
  input  _4__D0a,
  input  _20__D2b,
  input  _6__D1a,
  input  _18__D1b,
  input  _8__D2a,
  input  _16__D0b,
  input  _10__D3a,
  input  _15__nE1b,
  input  _14__nE0b,
  input  _12__GND,
  input  _13__nMRb,
  output _23__Q3b,
  output _21__Q2b,
  output _5__Q0a,
  output _19__Q1b,
  output _7__Q1a,
  output _17__Q0b,
  output _9__Q2a,
  output _11__Q3a
);

  wire and_1_out, and_2_out, not_1_out, not_2_out;

  not not_1 (not_1_out, _1__nMRa);
  and and_1 (and_1_out, ~_2__nE0a, ~_3__nE1a);  // AND_Gate
  D_Flip_Flop #(.trigger("high")) d_ff_1 (
    .clk(and_1_out), .D(_4__D0a), .Q(_5__Q0a), .reset(not_1_out));  // open: Qn, preset, en
  D_Flip_Flop #(.trigger("high")) d_ff_2 (
    .clk(and_1_out), .D(_6__D1a), .Q(_7__Q1a), .reset(not_1_out));  // open: Qn, preset, en
  D_Flip_Flop #(.trigger("high")) d_ff_3 (
    .clk(and_1_out), .D(_8__D2a), .Q(_9__Q2a), .reset(not_1_out));  // open: Qn, preset, en
  D_Flip_Flop #(.trigger("high")) d_ff_4 (
    .clk(and_1_out), .D(_10__D3a), .Q(_11__Q3a), .reset(not_1_out));  // open: Qn, preset, en
  D_Flip_Flop #(.trigger("high")) d_ff_5 (
    .clk(and_2_out), .D(_22__D3b), .Q(_23__Q3b), .reset(not_2_out));  // open: Qn, preset, en
  D_Flip_Flop #(.trigger("high")) d_ff_6 (
    .clk(and_2_out), .D(_20__D2b), .Q(_21__Q2b), .reset(not_2_out));  // open: Qn, preset, en
  D_Flip_Flop #(.trigger("high")) d_ff_7 (
    .clk(and_2_out), .D(_18__D1b), .Q(_19__Q1b), .reset(not_2_out));  // open: Qn, preset, en
  D_Flip_Flop #(.trigger("high")) d_ff_8 (
    .clk(and_2_out), .D(_16__D0b), .Q(_17__Q0b), .reset(not_2_out));  // open: Qn, preset, en
  and and_2 (and_2_out, ~_15__nE1b, ~_14__nE0b);  // AND_Gate
  not not_2 (not_2_out, _13__nMRb);

  // Notes on the sheet:
  //   74116: dual 4-bit latches
endmodule

module _74133 (
  input  _1__A,
  input  _16__Vcc,
  input  _2__B,
  input  _15__M,
  input  _3__C,
  input  _14__L,
  input  _4__D,
  input  _13__K,
  input  _5__E,
  input  _12__J,
  input  _6__F,
  input  _11__I,
  input  _7__G,
  input  _10__H,
  input  _8__GND,
  output _9__Y
);

  nand nand_1 (_9__Y, _7__G, _6__F, _5__E, _4__D, _3__C, _2__B, _1__A, _15__M, _14__L, _13__K, _12__J, _11__I, _10__H);

  // Notes on the sheet:
  //   74133: 13-input NAND
endmodule

module _74138 (
  input  _1__A,
  input  _16__Vcc,
  input  _2__B,
  input  _3__C,
  input  _4__G2A,
  input  _5__G2B,
  input  _6__G1,
  input  _8__GND,
  output _15__Y0,
  output _14__Y1,
  output _13__Y2,
  output _12__Y3,
  output _11__Y4,
  output _7__Y7,
  output _10__Y5,
  output _9__Y6
);

  wire and_1_out, and_2_out, and_3_out, and_4_out, and_5_out, and_6_out, and_7_out, and_8_out, and_9_out,
       decoder_1_out0, decoder_1_out1, decoder_1_out2, decoder_1_out3, decoder_1_out4, decoder_1_out5,
       decoder_1_out6, decoder_1_out7, not_1_out, not_2_out;

  not not_1 (not_1_out, _4__G2A);
  not not_2 (not_2_out, _5__G2B);
  and and_1 (and_1_out, and_2_out, decoder_1_out7);
  not not_3 (_7__Y7, and_1_out);
  and and_2 (and_2_out, not_1_out, not_2_out, _6__G1);
  Decoder #(.select(3), .enable("false")) decoder_1 (
    .out0(decoder_1_out0), .out1(decoder_1_out1), .out2(decoder_1_out2), .out3(decoder_1_out3),
    .out4(decoder_1_out4), .out5(decoder_1_out5), .out6(decoder_1_out6), .out7(decoder_1_out7),
    .sel({_3__C, _2__B, _1__A}));
  not not_4 (_15__Y0, and_3_out);
  and and_3 (and_3_out, and_2_out, decoder_1_out0);
  and and_4 (and_4_out, and_2_out, decoder_1_out1);
  not not_5 (_14__Y1, and_4_out);
  not not_6 (_13__Y2, and_5_out);
  and and_5 (and_5_out, and_2_out, decoder_1_out2);
  not not_7 (_12__Y3, and_6_out);
  and and_6 (and_6_out, and_2_out, decoder_1_out3);
  and and_7 (and_7_out, and_2_out, decoder_1_out4);
  not not_8 (_11__Y4, and_7_out);
  and and_8 (and_8_out, and_2_out, decoder_1_out5);
  not not_9 (_10__Y5, and_8_out);
  not not_10 (_9__Y6, and_9_out);
  and and_9 (and_9_out, and_2_out, decoder_1_out6);

  // Notes on the sheet:
  //   74138: 3-Line to 8-Line Decoder
endmodule

module _74139 (
  input  _1__1G,
  input  _16__Vcc,
  input  _2__1A,
  input  _15__2G,
  input  _3__1B,
  input  _14__2A,
  input  _13__2B,
  input  _8__GND,
  output _4__1Y0,
  output _5__1Y1,
  output _12__2Y0,
  output _6__1Y2,
  output _11__2Y1,
  output _7__1Y3,
  output _10__2Y2,
  output _9__2Y3
);

  wire and_1_out, and_2_out, and_3_out, and_4_out, and_5_out, and_6_out, and_7_out, and_8_out,
       decoder_1_out0, decoder_1_out1, decoder_1_out2, decoder_1_out3, decoder_2_out0, decoder_2_out1,
       decoder_2_out2, decoder_2_out3, not_1_out, not_6_out;

  not not_1 (not_1_out, _1__1G);
  and and_1 (and_1_out, not_1_out, decoder_1_out0);
  not not_2 (_4__1Y0, and_1_out);
  not not_3 (_5__1Y1, and_2_out);
  and and_2 (and_2_out, not_1_out, decoder_1_out1);
  and and_3 (and_3_out, not_1_out, decoder_1_out2);
  not not_4 (_6__1Y2, and_3_out);
  and and_4 (and_4_out, not_1_out, decoder_1_out3);
  not not_5 (_7__1Y3, and_4_out);
  Decoder #(.select(2), .enable("false")) decoder_1 (
    .out0(decoder_1_out0), .out1(decoder_1_out1), .out2(decoder_1_out2), .out3(decoder_1_out3),
    .sel({_3__1B, _2__1A}));
  Decoder #(.select(2), .enable("false")) decoder_2 (
    .out0(decoder_2_out0), .out1(decoder_2_out1), .out2(decoder_2_out2), .out3(decoder_2_out3),
    .sel({_13__2B, _14__2A}));
  not not_6 (not_6_out, _15__2G);
  and and_5 (and_5_out, not_6_out, decoder_2_out0);
  and and_6 (and_6_out, not_6_out, decoder_2_out1);
  and and_7 (and_7_out, not_6_out, decoder_2_out2);
  and and_8 (and_8_out, not_6_out, decoder_2_out3);
  not not_7 (_12__2Y0, and_5_out);
  not not_8 (_11__2Y1, and_6_out);
  not not_9 (_10__2Y2, and_7_out);
  not not_10 (_9__2Y3, and_8_out);

  // Notes on the sheet:
  //   74139: Dual 2-Line to 4-Line Decoder
endmodule

module _74147 (
  input  _1__I4,
  input  _16__Vcc,
  input  _2__I5,
  input  _15__NC,
  input  _3__I6,
  input  _4__I7,
  input  _13__I3,
  input  _5__I8,
  input  _12__I2,
  input  _11__I1,
  input  _10__I9,
  input  _8__GND,
  output _14__A3,
  output _6__A2,
  output _7__A1,
  output _9__A0
);

  Priority_Encoder #(.select(4)) priority_encoder_1 (
    .in0(_11__I1), .in1(_12__I2), .in2(_13__I3), .in3(_1__I4), .in4(_2__I5), .in5(_3__I6), .in6(_4__I7),
    .in7(_5__I8), .in8(_10__I9), .out({_14__A3, _6__A2, _7__A1, _9__A0}));  // open: in9, in10, in11, in12, in13, in14, in15, gs, en_out, en_in

  // Notes on the sheet:
  //   74147: 9-Line to 4-Line Priority Encoder
endmodule

module _74148 (
  input  _1__I4,
  input  _16__Vcc,
  input  _2__I5,
  input  _15__nEO__NC,
  input  _3__I6,
  input  _14__nGS__NC,
  input  _4__I7,
  input  _13__I3,
  input  _5__nEI__NC,
  input  _12__I2,
  input  _6__A2,
  input  _11__I1,
  input  _7__A1,
  input  _10__I0,
  input  _8__GND,
  input  _9__A0
);

  Priority_Encoder priority_encoder_1 (
    .in0(_10__I0), .in1(_11__I1), .in2(_12__I2), .in3(_13__I3), .in4(_1__I4), .in5(_2__I5), .in6(_3__I6),
    .in7(_4__I7), .out({_7__A1, _6__A2, _9__A0}));  // open: en_in, gs, en_out

  // Notes on the sheet:
  //   74148: 9-Line to 4-Line Priority Encoder
  //   NOTE: Pins 5, 14, and 15 have connections normally, but I chose not to model them
endmodule

module _74150 (
  input  _1__E7,
  input  _24__Vcc,
  input  _2__E6,
  input  _23__E8,
  input  _3__E5,
  input  _22__E9,
  input  _4__E4,
  input  _21__E10,
  input  _5__E3,
  input  _20__E11,
  input  _6__E2,
  input  _19__E12,
  input  _7__E1,
  input  _18__E13,
  input  _8__E0,
  input  _17__E14,
  input  _9__nG,
  input  _16__E15,
  input  _15__A,
  input  _11__D,
  input  _14__B,
  input  _12__GND,
  input  _13__C,
  output _10__W
);

  wire multiplexer_1_out, not_1_out;

  or or_1 (_10__W, _9__nG, not_1_out);
  not not_1 (not_1_out, multiplexer_1_out);
  Multiplexer #(.select(4), .enable("false")) multiplexer_1 (
    .in0(_8__E0), .in1(_7__E1), .in2(_6__E2), .in3(_5__E3), .in4(_4__E4), .in5(_3__E5), .in6(_2__E6),
    .in7(_1__E7), .in8(_23__E8), .in9(_22__E9), .in10(_21__E10), .in11(_20__E11), .in12(_19__E12),
    .in13(_18__E13), .in14(_17__E14), .in15(_16__E15), .out(multiplexer_1_out),
    .sel({_11__D, _13__C, _14__B, _15__A}));

  // Notes on the sheet:
  //   74150: 16-Line to 1-Line Multiplexer
endmodule

module _74151 (
  input  _1__D3,
  input  _16__Vcc,
  input  _2__D2,
  input  _15__D4,
  input  _3__D1,
  input  _14__D5,
  input  _4__D0,
  input  _13__D6,
  input  _12__D7,
  input  _11__A,
  input  _7__nG,
  input  _10__B,
  input  _8__GND,
  input  _9__C,
  output _5__Y,
  output _6__W
);

  wire multiplexer_1_out, not_2_out;

  not not_1 (_5__Y, _6__W);
  or or_1 (_6__W, not_2_out, _7__nG);
  Multiplexer #(.select(3), .enable("false")) multiplexer_1 (
    .in0(_4__D0), .in1(_3__D1), .in2(_2__D2), .in3(_1__D3), .in4(_15__D4), .in5(_14__D5), .in6(_13__D6),
    .in7(_12__D7), .out(multiplexer_1_out), .sel({_9__C, _10__B, _11__A}));
  not not_2 (not_2_out, multiplexer_1_out);

  // Notes on the sheet:
  //   74151: 8-Line to 1-Line Multiplexer
endmodule

module _74153 (
  input  _1__nG1,
  input  _16__Vcc,
  input  _2__B,
  input  _15__nG2,
  input  _3__1C3,
  input  _14__A,
  input  _4__1C2,
  input  _13__2C3,
  input  _5__1C1,
  input  _12__2C2,
  input  _6__1C0,
  input  _11__2C1,
  input  _10__2C0,
  input  _8__GND,
  output _7__Y1,
  output _9__Y2
);

  wire multiplexer_1_out, multiplexer_2_out, not_1_out, not_2_out;

  not not_1 (not_1_out, _1__nG1);
  Multiplexer #(.select(2), .enable("false")) multiplexer_1 (
    .in0(_6__1C0), .in1(_5__1C1), .in2(_4__1C2), .in3(_3__1C3), .out(multiplexer_1_out), .sel({_2__B, _14__A}));
  and and_1 (_7__Y1, multiplexer_1_out, not_1_out);
  not not_2 (not_2_out, _15__nG2);
  Multiplexer #(.select(2), .enable("false")) multiplexer_2 (
    .in0(_10__2C0), .in1(_11__2C1), .in2(_12__2C2), .in3(_13__2C3), .out(multiplexer_2_out),
    .sel({_2__B, _14__A}));
  and and_2 (_9__Y2, multiplexer_2_out, not_2_out);

  // Notes on the sheet:
  //   74153: Dual 4-Line to 1-Line Multiplexer
endmodule

module _74154 (
  input  _24__Vcc,
  input  _23__A,
  input  _22__B,
  input  _21__C,
  input  _20__D,
  input  _19__G2,
  input  _18__G1,
  input  _12__GND,
  output _1__Y0,
  output _2__Y1,
  output _3__Y2,
  output _4__Y3,
  output _5__Y4,
  output _6__Y5,
  output _7__Y6,
  output _8__Y7,
  output _17__Y15,
  output _9__Y8,
  output _16__Y14,
  output _10__Y9,
  output _15__Y13,
  output _11__Y10,
  output _14__Y12,
  output _13__Y11
);

  wire and_12_out, decoder_1_out0, decoder_1_out1, decoder_1_out2, decoder_1_out3, decoder_1_out4,
       decoder_1_out5, decoder_1_out6, decoder_1_out7, decoder_1_out8, decoder_1_out9, decoder_1_out10,
       decoder_1_out11, decoder_1_out12, decoder_1_out13, decoder_1_out14, decoder_1_out15, not_1_out,
       not_2_out, not_3_out, not_4_out, not_5_out, not_6_out, not_7_out, not_8_out, not_9_out, not_10_out,
       not_11_out, not_12_out, not_13_out, not_14_out, not_15_out, not_16_out, not_17_out, not_18_out;

  not not_1 (not_1_out, decoder_1_out0);
  and and_1 (_1__Y0, not_1_out, and_12_out);
  not not_2 (not_2_out, decoder_1_out1);
  and and_2 (_2__Y1, not_2_out, and_12_out);
  not not_3 (not_3_out, decoder_1_out2);
  and and_3 (_3__Y2, not_3_out, and_12_out);
  not not_4 (not_4_out, decoder_1_out3);
  and and_4 (_4__Y3, not_4_out, and_12_out);
  not not_5 (not_5_out, decoder_1_out4);
  and and_5 (_5__Y4, not_5_out, and_12_out);
  not not_6 (not_6_out, decoder_1_out5);
  and and_6 (_6__Y5, not_6_out, and_12_out);
  not not_7 (not_7_out, decoder_1_out6);
  and and_7 (_7__Y6, not_7_out, and_12_out);
  not not_8 (not_8_out, decoder_1_out7);
  and and_8 (_8__Y7, not_8_out, and_12_out);
  not not_9 (not_9_out, decoder_1_out8);
  and and_9 (_9__Y8, not_9_out, and_12_out);
  not not_10 (not_10_out, decoder_1_out9);
  and and_10 (_10__Y9, not_10_out, and_12_out);
  not not_11 (not_11_out, decoder_1_out10);
  and and_11 (_11__Y10, not_11_out, and_12_out);
  and and_12 (and_12_out, not_12_out, not_13_out);
  Decoder #(.select(4), .enable("false")) decoder_1 (
    .out0(decoder_1_out0), .out1(decoder_1_out1), .out2(decoder_1_out2), .out3(decoder_1_out3),
    .out4(decoder_1_out4), .out5(decoder_1_out5), .out6(decoder_1_out6), .out7(decoder_1_out7),
    .out8(decoder_1_out8), .out9(decoder_1_out9), .out10(decoder_1_out10), .out11(decoder_1_out11),
    .out12(decoder_1_out12), .out13(decoder_1_out13), .out14(decoder_1_out14), .out15(decoder_1_out15),
    .sel({_20__D, _21__C, _22__B, _23__A}));
  not not_12 (not_12_out, _19__G2);
  not not_13 (not_13_out, _18__G1);
  not not_14 (not_14_out, decoder_1_out15);
  and and_13 (_17__Y15, not_14_out, and_12_out);
  not not_15 (not_15_out, decoder_1_out14);
  and and_14 (_16__Y14, not_15_out, and_12_out);
  not not_16 (not_16_out, decoder_1_out13);
  and and_15 (_15__Y13, not_16_out, and_12_out);
  not not_17 (not_17_out, decoder_1_out12);
  and and_16 (_14__Y12, not_17_out, and_12_out);
  not not_18 (not_18_out, decoder_1_out11);
  and and_17 (_13__Y11, not_18_out, and_12_out);

  // Notes on the sheet:
  //   74154: 4-Line to 16-Line Decoder
endmodule

module _74157 (
  input  _1__S,
  input  _16__Vcc,
  input  _2__A1,
  input  _15__G,
  input  _3__B1,
  input  _14__A4,
  input  _13__B4,
  input  _5__A2,
  input  _6__B2,
  input  _11__A3,
  input  _10__B3,
  input  _8__GND,
  output _4__Y1,
  output _12__Y4,
  output _7__Y2,
  output _9__Y3
);

  wire multiplexer_1_out, multiplexer_2_out, multiplexer_3_out, multiplexer_4_out, not_1_out;

  Multiplexer #(.enable("false")) multiplexer_1 (.in0(_2__A1), .in1(_3__B1), .out(multiplexer_1_out), .sel(_1__S));
  and and_1 (_4__Y1, multiplexer_1_out, not_1_out);
  Multiplexer #(.enable("false")) multiplexer_2 (.in0(_5__A2), .in1(_6__B2), .out(multiplexer_2_out), .sel(_1__S));
  and and_2 (_7__Y2, multiplexer_2_out, not_1_out);
  not not_1 (not_1_out, _15__G);
  Multiplexer #(.enable("false")) multiplexer_3 (.in0(_14__A4), .in1(_13__B4), .out(multiplexer_3_out), .sel(_1__S));
  and and_3 (_12__Y4, multiplexer_3_out, not_1_out);
  Multiplexer #(.enable("false")) multiplexer_4 (.in0(_11__A3), .in1(_10__B3), .out(multiplexer_4_out), .sel(_1__S));
  and and_4 (_9__Y3, multiplexer_4_out, not_1_out);

  // Notes on the sheet:
  //   74157: Quad 2-Line to 1-Line Multiplexer
endmodule

module _74161 (
  input  _1__nMR,
  input  _16__Vcc,
  input  _2__CP,
  input  _3__D0,
  input  _4__D1,
  input  _5__D2,
  input  _6__D3,
  input  _7__CEP,
  input  _10__CET,
  input  _8__GND,
  input  _9__nPE,
  output _15__TC,
  output _14__Q0,
  output _13__Q1,
  output _12__Q2,
  output _11__O3
);

  wire and_1_out, counter_1_carry, not_1_out, not_2_out;

  not not_1 (not_1_out, _1__nMR);
  and and_1 (and_1_out, _7__CEP, _9__nPE, _10__CET);
  Counter #(.width(4), .max('hf)) counter_1 (
    .load(not_2_out), .D({_6__D3, _5__D2, _4__D1, _3__D0}), .count(and_1_out),
    .Q({_11__O3, _12__Q2, _13__Q1, _14__Q0}), .carry(counter_1_carry), .clk(_2__CP), .clr(not_1_out));
  and and_2 (_15__TC, counter_1_carry, _10__CET);
  not not_2 (not_2_out, _9__nPE);

  // Notes on the sheet:
  //   74161: Synchronous 4-bit Binary Counter with Asynchronous Clear 
endmodule

module _74163 (
  input  _1__nMR,
  input  _16__Vcc,
  input  _2__CP,
  input  _3__D0,
  input  _4__D1,
  input  _5__D2,
  input  _6__D3,
  input  _7__CEP,
  input  _10__CET,
  input  _8__GND,
  input  _9__nPE,
  output _15__TC,
  output _14__Q0,
  output _13__Q1,
  output _12__Q2,
  output _11__O3
);

  wire and_1_out, and_2_out, counter_1_carry, not_1_out, not_2_out;
  wire [3:0] multiplexer_1_out;

  not not_1 (not_1_out, _1__nMR);
  Multiplexer #(.width(4), .enable("false")) multiplexer_1 (
    .in0({_6__D3, _5__D2, _4__D1, _3__D0}), .in1(4'b0000), .out(multiplexer_1_out), .sel(not_1_out));
  and and_1 (and_1_out, _7__CEP, and_2_out, _10__CET);
  not not_2 (not_2_out, and_2_out);
  Counter #(.width(4), .max('hf)) counter_1 (
    .load(not_2_out), .D(multiplexer_1_out), .count(and_1_out), .Q({_11__O3, _12__Q2, _13__Q1, _14__Q0}),
    .carry(counter_1_carry), .clk(_2__CP));  // open: clr
  and and_2 (and_2_out, ~not_1_out, _9__nPE);  // AND_Gate
  and and_3 (_15__TC, counter_1_carry, _10__CET);

  // Notes on the sheet:
  //   74163: Synchronous 4-bit Binary Counter with Synchronous Clear 
endmodule

module _74174 (
  input  _1__MR_prime,
  input  _16__Vcc,
  input  _3__D0,
  input  _14__D5,
  input  _4__D1,
  input  _13__D4,
  input  _6__D2,
  input  _11__D3,
  input  _8__GND,
  input  _9__CP,
  output _2__Q0,
  output _15__Q5,
  output _5__Q1,
  output _12__Q4,
  output _7__Q2,
  output _10__Q3
);

  wire not_1_out;

  not not_1 (not_1_out, _1__MR_prime);
  D_Flip_Flop #(.trigger("high")) d_ff_1 (
    .clk(_9__CP), .D(_3__D0), .Q(_2__Q0), .reset(not_1_out));  // open: Qn, preset, en
  D_Flip_Flop #(.trigger("high")) d_ff_2 (
    .clk(_9__CP), .D(_4__D1), .Q(_5__Q1), .reset(not_1_out));  // open: Qn, preset, en
  D_Flip_Flop #(.trigger("high")) d_ff_3 (
    .clk(_9__CP), .D(_6__D2), .Q(_7__Q2), .reset(not_1_out));  // open: Qn, preset, en
  D_Flip_Flop #(.trigger("high")) d_ff_4 (
    .clk(_9__CP), .D(_14__D5), .Q(_15__Q5), .reset(not_1_out));  // open: Qn, preset, en
  D_Flip_Flop #(.trigger("high")) d_ff_5 (
    .clk(_9__CP), .D(_13__D4), .Q(_12__Q4), .reset(not_1_out));  // open: Qn, preset, en
  D_Flip_Flop #(.trigger("high")) d_ff_6 (
    .clk(_9__CP), .D(_11__D3), .Q(_10__Q3), .reset(not_1_out));  // open: Qn, preset, en

  // Notes on the sheet:
  //   74174: Hex D-type flip-flop with reset; positive-edge trigger
endmodule

module _74181 (
  input  _1__nB0,
  input  _24__Vcc,
  input  _2__nA0,
  input  _23__nA1,
  input  _3__S3,
  input  _22__nB1,
  input  _4__S2,
  input  _21__nA2,
  input  _5__S1,
  input  _20__nB2,
  input  _6__S0,
  input  _19__nA3,
  input  _7__Cn,
  input  _18__nB3,
  input  _8__M,
  input  _12__GND,
  output _17__nG,
  output _9__nF0,
  output _16__Cn_4,
  output _10__nF1,
  output _15__nP,
  output _11__nF2,
  output _14__A_B,
  output _13__nF3
);

  wire and_1_out, and_2_out, and_3_out, and_4_out, and_5_out, and_6_out, and_7_out, and_8_out, and_9_out,
       and_10_out, and_11_out, and_12_out, and_13_out, and_14_out, and_15_out, and_16_out, and_17_out,
       and_18_out, and_19_out, and_20_out, and_21_out, and_22_out, and_23_out, and_24_out, and_26_out,
       and_27_out, and_28_out, and_29_out, and_30_out, and_31_out, and_32_out, and_33_out, and_34_out,
       and_35_out, and_36_out, and_37_out, and_38_out, nand_2_out, nand_4_out, nor_2_out, nor_3_out,
       nor_4_out, nor_5_out, nor_6_out, nor_7_out, nor_8_out, nor_9_out, nor_10_out, nor_11_out, nor_12_out,
       not_1_out, not_2_out, not_3_out, not_4_out, not_5_out, not_6_out, not_7_out, not_8_out, not_9_out;

  and and_1 (and_1_out, nor_3_out, nor_3_out);
  nor nor_1 (_17__nG, and_1_out, and_3_out, and_2_out, and_4_out);
  and and_2 (and_2_out, nor_2_out, nor_4_out, nor_9_out);
  and and_3 (and_3_out, nor_2_out, nor_6_out);
  and and_4 (and_4_out, nor_2_out, nor_4_out, nor_8_out, nor_12_out);
  nor nor_2 (nor_2_out, and_6_out, and_5_out);
  and and_5 (and_5_out, _19__nA3, _4__S2, not_1_out);
  and and_6 (and_6_out, _18__nB3, _3__S3, _19__nA3);
  not not_1 (not_1_out, _18__nB3);
  nand nand_1 (_16__Cn_4, _17__nG, nand_2_out);
  nand nand_2 (nand_2_out, nor_2_out, nor_4_out, nor_8_out, nor_11_out, _7__Cn);
  nor nor_3 (nor_3_out, and_7_out, and_8_out, and_9_out);
  and and_7 (and_7_out, not_1_out, _5__S1);
  and and_8 (and_8_out, _6__S0, _18__nB3);
  nand nand_3 (_15__nP, nor_2_out, nor_4_out, nor_8_out, nor_11_out);
  and and_9 (and_9_out, _19__nA3, _19__nA3);
  and and_10 (and_10_out, nor_2_out, not_2_out);
  and and_11 (and_11_out, nor_4_out, nor_8_out, nor_11_out, _7__Cn, not_9_out);
  not not_2 (not_2_out, nor_3_out);
  nor nor_4 (nor_4_out, and_12_out, and_13_out);
  and and_12 (and_12_out, _20__nB2, _3__S3, _21__nA2);
  and and_13 (and_13_out, _21__nA2, _4__S2, not_3_out);
  xor xor_1 (_13__nF3, and_10_out, nor_5_out);
  nor nor_5 (nor_5_out, and_11_out, and_14_out, and_17_out, and_16_out);
  and and_14 (and_14_out, nor_4_out, nor_8_out, nor_12_out, not_9_out);
  and and_15 (and_15_out, not_3_out, _5__S1);
  not not_3 (not_3_out, _20__nB2);
  and and_16 (and_16_out, nor_6_out, not_9_out);
  and and_17 (and_17_out, nor_4_out, nor_9_out, not_9_out);
  nor nor_6 (nor_6_out, and_15_out, and_19_out, and_18_out);
  and and_18 (and_18_out, _21__nA2, _21__nA2);
  and and_19 (and_19_out, _6__S0, _20__nB2);
  and and_20 (and_20_out, nor_4_out, not_4_out);
  and and_21 (and_21_out, nor_8_out, nor_11_out, _7__Cn, not_9_out);
  not not_4 (not_4_out, nor_6_out);
  and and_22 (and_22_out, _22__nB1, _3__S3, _23__nA1);
  xor xor_2 (_11__nF2, and_20_out, nor_7_out);
  nor nor_7 (nor_7_out, and_21_out, and_23_out, and_27_out);
  and and_23 (and_23_out, nor_8_out, nor_12_out, not_9_out);
  nor nor_8 (nor_8_out, and_22_out, and_24_out);
  and and_24 (and_24_out, _23__nA1, _4__S2, not_5_out);
  not not_5 (not_5_out, _22__nB1);
  and and_25 (_14__A_B, _13__nF3, _11__nF2, _10__nF1, _9__nF0);
  and and_26 (and_26_out, nor_8_out, not_6_out);
  and and_27 (and_27_out, nor_9_out, not_9_out);
  not not_6 (not_6_out, nor_9_out);
  nor nor_9 (nor_9_out, and_28_out, and_29_out, and_30_out);
  and and_28 (and_28_out, not_5_out, _5__S1);
  and and_29 (and_29_out, _6__S0, _22__nB1);
  and and_30 (and_30_out, _23__nA1, _23__nA1);
  xor xor_3 (_10__nF1, and_26_out, nor_10_out);
  nor nor_10 (nor_10_out, and_32_out, and_31_out);
  and and_31 (and_31_out, nor_12_out, not_9_out);
  and and_32 (and_32_out, _7__Cn, nor_11_out, not_9_out);
  nor nor_11 (nor_11_out, and_33_out, and_34_out);
  and and_33 (and_33_out, _1__nB0, _3__S3, _2__nA0);
  and and_34 (and_34_out, _2__nA0, _4__S2, not_7_out);
  not not_7 (not_7_out, _1__nB0);
  and and_35 (and_35_out, nor_11_out, not_8_out);
  not not_8 (not_8_out, nor_12_out);
  nor nor_12 (nor_12_out, and_37_out, and_36_out, and_38_out);
  and and_36 (and_36_out, _6__S0, _1__nB0);
  and and_37 (and_37_out, not_7_out, _5__S1);
  xor xor_4 (_9__nF0, and_35_out, nand_4_out);
  and and_38 (and_38_out, _2__nA0, _2__nA0);
  not not_9 (not_9_out, _8__M);
  nand nand_4 (nand_4_out, not_9_out, _7__Cn);

  // Other names for the same wires on the sheet: A_B = _14__A_B; Cn = _7__Cn; Cn_4 = _16__Cn_4; M = _8__M;
  //   nA0 = _2__nA0; nA1 = _23__nA1; nA2 = _21__nA2; nA3 = _19__nA3; nB0 = _1__nB0; nB1 = _22__nB1; nB2 = _20__nB2;
  //   nB3 = _18__nB3; nF0 = _9__nF0; nF1 = _10__nF1; nF2 = _11__nF2; nF3 = _13__nF3; nG = _17__nG; nP = _15__nP;
  //   S0 = _6__S0; S1 = _5__S1; S2 = _4__S2; S3 = _3__S3

  // Notes on the sheet:
  //   74181: 4-Bit ALU
endmodule

module _74198 (
  input  _1__S0,
  input  _24__Vcc,
  input  _2__Dsr,
  input  _23__S1,
  input  _3__P0,
  input  _22__Dsl,
  input  _21__P7,
  input  _5__P1,
  input  _19__P6,
  input  _7__P2,
  input  _17__P5,
  input  _9__P3,
  input  _15__P4,
  input  _11__CP,
  input  _12__GND,
  input  _13__nMR,
  output _4__Q0,
  output _20__Q7,
  output _6__Q1,
  output _18__Q6,
  output _8__Q2,
  output _16__Q5,
  output _10__Q3,
  output _14__Q4
);

  wire and_1_out, and_2_out, and_3_out, and_4_out, and_5_out, and_6_out, and_7_out, and_8_out, and_9_out,
       and_10_out, and_11_out, and_12_out, and_13_out, and_14_out, and_15_out, and_16_out, and_17_out,
       and_18_out, and_19_out, and_20_out, and_21_out, and_22_out, and_23_out, and_24_out, and_25_out,
       nor_1_out, not_1_out, not_2_out, not_3_out, or_1_out, or_2_out, or_3_out, or_4_out, or_5_out,
       or_6_out, or_7_out, or_8_out, or_9_out;

  not not_1 (not_1_out, _1__S0);
  not not_2 (not_2_out, _23__S1);
  nor nor_1 (nor_1_out, not_1_out, not_2_out);
  and and_1 (and_1_out, not_2_out, not_1_out);
  and and_2 (and_2_out, _22__Dsl, not_1_out);
  and and_3 (and_3_out, _21__P7, nor_1_out);
  and and_4 (and_4_out, _18__Q6, not_2_out);
  and and_5 (and_5_out, _20__Q7, not_1_out);
  and and_6 (and_6_out, _19__P6, nor_1_out);
  and and_7 (and_7_out, _16__Q5, not_2_out);
  and and_8 (and_8_out, _18__Q6, not_1_out);
  and and_9 (and_9_out, _17__P5, nor_1_out);
  and and_10 (and_10_out, _14__Q4, not_2_out);
  and and_11 (and_11_out, _16__Q5, not_1_out);
  and and_12 (and_12_out, _15__P4, nor_1_out);
  and and_13 (and_13_out, _10__Q3, not_2_out);
  and and_14 (and_14_out, _14__Q4, not_1_out);
  and and_15 (and_15_out, _9__P3, nor_1_out);
  and and_16 (and_16_out, _8__Q2, not_2_out);
  and and_17 (and_17_out, _10__Q3, not_1_out);
  and and_18 (and_18_out, _7__P2, nor_1_out);
  and and_19 (and_19_out, _6__Q1, not_2_out);
  and and_20 (and_20_out, _8__Q2, not_1_out);
  and and_21 (and_21_out, _5__P1, nor_1_out);
  and and_22 (and_22_out, _4__Q0, not_2_out);
  and and_23 (and_23_out, _6__Q1, not_1_out);
  and and_24 (and_24_out, _3__P0, nor_1_out);
  and and_25 (and_25_out, _2__Dsr, not_2_out);
  or or_1 (or_1_out, _11__CP, and_1_out);
  or or_2 (or_2_out, and_2_out, and_3_out, and_4_out);
  or or_3 (or_3_out, and_5_out, and_6_out, and_7_out);
  or or_4 (or_4_out, and_8_out, and_9_out, and_10_out);
  or or_5 (or_5_out, and_11_out, and_12_out, and_13_out);
  or or_6 (or_6_out, and_14_out, and_15_out, and_16_out);
  or or_7 (or_7_out, and_17_out, and_18_out, and_19_out);
  or or_8 (or_8_out, and_20_out, and_21_out, and_22_out);
  or or_9 (or_9_out, and_23_out, and_24_out, and_25_out);
  D_Flip_Flop d_ff_1 (.clk(or_1_out), .D(or_2_out), .Q(_20__Q7), .reset(not_3_out));  // open: Qn, preset, en
  D_Flip_Flop d_ff_2 (.clk(or_1_out), .D(or_3_out), .Q(_18__Q6), .reset(not_3_out));  // open: Qn, preset, en
  D_Flip_Flop d_ff_3 (.clk(or_1_out), .D(or_4_out), .Q(_16__Q5), .reset(not_3_out));  // open: Qn, preset, en
  D_Flip_Flop d_ff_4 (.clk(or_1_out), .D(or_5_out), .Q(_14__Q4), .reset(not_3_out));  // open: Qn, preset, en
  not not_3 (not_3_out, _13__nMR);
  D_Flip_Flop d_ff_5 (.clk(or_1_out), .D(or_6_out), .Q(_10__Q3), .reset(not_3_out));  // open: Qn, preset, en
  D_Flip_Flop d_ff_6 (.clk(or_1_out), .D(or_7_out), .Q(_8__Q2), .reset(not_3_out));  // open: Qn, preset, en
  D_Flip_Flop d_ff_7 (.clk(or_1_out), .D(or_8_out), .Q(_6__Q1), .reset(not_3_out));  // open: Qn, preset, en
  D_Flip_Flop d_ff_8 (.clk(or_1_out), .D(or_9_out), .Q(_4__Q0), .reset(not_3_out));  // open: Qn, preset, en

  // Notes on the sheet:
  //   74198: 8-bit universal shift register
endmodule

module _74238 (
  input  _1__A0,
  input  _16__Vcc,
  input  _2__A1,
  input  _3__A2,
  input  _4__E1_prime,
  input  _5__E2_prime,
  input  _6__E3,
  input  _8__GND,
  output _15__Y0,
  output _14__Y1,
  output _13__Y2,
  output _12__Y3,
  output _11__Y4,
  output _7__Y7,
  output _10__Y5,
  output _9__Y6
);

  wire and_1_out;

  and and_1 (and_1_out, ~_4__E1_prime, ~_5__E2_prime, _6__E3);  // AND_Gate
  Demultiplexer #(.select(3), .enable("false")) demultiplexer_1 (
    .out0(_15__Y0), .out1(_14__Y1), .out2(_13__Y2), .out3(_12__Y3), .out4(_11__Y4), .out5(_10__Y5),
    .out6(_9__Y6), .out7(_7__Y7), .in(and_1_out), .sel({_3__A2, _2__A1, _1__A0}));

  // Notes on the sheet:
  //   74238: 3-to-8 line decoder/demultiplexer; non-inverting
endmodule

module _74240 (
  input  _1___1G,
  input  _20__Vcc,
  input  _2__1A1,
  input  _19___2G,
  input  _4__1A2,
  input  _17__2A4,
  input  _6__1A3,
  input  _15__2A3,
  input  _8__1A4,
  input  _13__2A2,
  input  _10__GND,
  input  _11__2A1,
  output _3__2Y4,
  output _18__1Y1,
  output _5__2Y3,
  output _16__1Y2,
  output _7__2Y2,
  output _14__1Y3,
  output _9__2Y1,
  output _12__1Y4
);

  wire not_1_out, not_2_out;

  not not_1 (not_1_out, _1___1G);
  assign _18__1Y1 = not_1_out ? ~_2__1A1 : 1'bz;  // Controlled_Inverter controlled_inverter_1
  assign _3__2Y4 = not_2_out ? ~_17__2A4 : 1'bz;  // Controlled_Inverter controlled_inverter_2
  assign _16__1Y2 = not_1_out ? ~_4__1A2 : 1'bz;  // Controlled_Inverter controlled_inverter_3
  assign _14__1Y3 = not_1_out ? ~_6__1A3 : 1'bz;  // Controlled_Inverter controlled_inverter_4
  assign _5__2Y3 = not_2_out ? ~_15__2A3 : 1'bz;  // Controlled_Inverter controlled_inverter_5
  assign _7__2Y2 = not_2_out ? ~_13__2A2 : 1'bz;  // Controlled_Inverter controlled_inverter_6
  assign _12__1Y4 = not_1_out ? ~_8__1A4 : 1'bz;  // Controlled_Inverter controlled_inverter_7
  assign _9__2Y1 = not_2_out ? ~_11__2A1 : 1'bz;  // Controlled_Inverter controlled_inverter_8
  not not_2 (not_2_out, _19___2G);

  // Notes on the sheet:
  //   74240: Octal Inverted Tristate Buffer
endmodule

module _74244 (
  input  _1___1G,
  input  _20__Vcc,
  input  _2__1A1,
  input  _19___2G,
  input  _4__1A2,
  input  _17__2A4,
  input  _6__1A3,
  input  _15__2A3,
  input  _8__1A4,
  input  _13__2A2,
  input  _10__GND,
  input  _11__2A1,
  output _3__2Y4,
  output _18__1Y1,
  output _5__2Y3,
  output _16__1Y2,
  output _7__2Y2,
  output _14__1Y3,
  output _9__2Y1,
  output _12__1Y4
);

  wire not_1_out, not_2_out;

  not not_1 (not_1_out, _1___1G);
  assign _18__1Y1 = not_1_out ? _2__1A1 : 1'bz;  // Controlled_Buffer controlled_buffer_1
  assign _3__2Y4 = not_2_out ? _17__2A4 : 1'bz;  // Controlled_Buffer controlled_buffer_2
  assign _16__1Y2 = not_1_out ? _4__1A2 : 1'bz;  // Controlled_Buffer controlled_buffer_3
  assign _14__1Y3 = not_1_out ? _6__1A3 : 1'bz;  // Controlled_Buffer controlled_buffer_4
  assign _5__2Y3 = not_2_out ? _15__2A3 : 1'bz;  // Controlled_Buffer controlled_buffer_5
  assign _12__1Y4 = not_1_out ? _8__1A4 : 1'bz;  // Controlled_Buffer controlled_buffer_6
  assign _7__2Y2 = not_2_out ? _13__2A2 : 1'bz;  // Controlled_Buffer controlled_buffer_7
  assign _9__2Y1 = not_2_out ? _11__2A1 : 1'bz;  // Controlled_Buffer controlled_buffer_8
  not not_2 (not_2_out, _19___2G);

  // Notes on the sheet:
  //   74240: Octal Tristate Buffer
endmodule

module _74253 (
  input  _1__1G,
  input  _16__Vcc,
  input  _2__Sb,
  input  _15__2G,
  input  _3__1C3,
  input  _14__Sa,
  input  _4__1C2,
  input  _13__2C3,
  input  _5__1C1,
  input  _12__2C2,
  input  _6__1C0,
  input  _11__2C1,
  input  _10__2C0,
  input  _8__GND,
  output _7__1Y,
  output _9__2Y
);

  wire multiplexer_1_out, multiplexer_2_out, not_1_out, not_3_out;
  wire [1:0] not_4_out;

  not not_1 (not_1_out, _1__1G);
  not not_2 (not_4_out[1], _2__Sb);
  Multiplexer #(.select(2), .enable("false")) multiplexer_1 (
    .in0(_3__1C3), .in1(_4__1C2), .in2(_5__1C1), .in3(_6__1C0), .out(multiplexer_1_out), .sel(not_4_out));
  and and_1 (_7__1Y, multiplexer_1_out, not_1_out);
  Multiplexer #(.select(2), .enable("false")) multiplexer_2 (
    .in0(_13__2C3), .in1(_12__2C2), .in2(_11__2C1), .in3(_10__2C0), .out(multiplexer_2_out), .sel(not_4_out));
  not not_3 (not_3_out, _15__2G);
  not not_4 (not_4_out[0], _14__Sa);
  and and_2 (_9__2Y, multiplexer_2_out, not_3_out);

  // Notes on the sheet:
  //   74253: Dual 4-Lin to 1-Line Multiplexer
endmodule

module _74260 (
  input  _1__1A,
  input  _14__Vcc,
  input  _2__1B,
  input  _13__2D,
  input  _3__1E,
  input  _12__2C,
  input  _4__1C,
  input  _11__2E,
  input  _5__1D,
  input  _10__2B,
  input  _9__2A,
  input  _7__GND,
  output _6__1Y,
  output _8__2Y
);

  nor nor_1 (_6__1Y, _5__1D, _4__1C, _3__1E, _2__1B, _1__1A);
  nor nor_2 (_8__2Y, _13__2D, _12__2C, _11__2E, _10__2B, _9__2A);

  // Notes on the sheet:
  //   74260: dual 5-input NOR
endmodule

module _74273 (
  input  _1__nCLR,
  input  _20__Vcc,
  input  _3__D0,
  input  _18__D7,
  input  _4__D1,
  input  _17__D6,
  input  _7__D2,
  input  _14__D5,
  input  _8__D3,
  input  _13__D4,
  input  _10__GND,
  input  _11__CP,
  output _2__Q0,
  output _19__Q7,
  output _5__Q1,
  output _16__Q6,
  output _6__Q2,
  output _15__Q5,
  output _9__Q3,
  output _12__Q4
);

  wire not_1_out;

  not not_1 (not_1_out, _1__nCLR);
  D_Flip_Flop d_ff_1 (.clk(_11__CP), .D(_3__D0), .Q(_2__Q0), .reset(not_1_out));  // open: Qn, preset, en
  D_Flip_Flop d_ff_2 (.clk(_11__CP), .D(_4__D1), .Q(_5__Q1), .reset(not_1_out));  // open: Qn, preset, en
  D_Flip_Flop d_ff_3 (.clk(_11__CP), .D(_7__D2), .Q(_6__Q2), .reset(not_1_out));  // open: Qn, preset, en
  D_Flip_Flop d_ff_4 (.clk(_11__CP), .D(_8__D3), .Q(_9__Q3), .reset(not_1_out));  // open: Qn, preset, en
  D_Flip_Flop d_ff_5 (.clk(_11__CP), .D(_13__D4), .Q(_12__Q4), .reset(not_1_out));  // open: Qn, preset, en
  D_Flip_Flop d_ff_6 (.clk(_11__CP), .D(_14__D5), .Q(_15__Q5), .reset(not_1_out));  // open: Qn, preset, en
  D_Flip_Flop d_ff_7 (.clk(_11__CP), .D(_17__D6), .Q(_16__Q6), .reset(not_1_out));  // open: Qn, preset, en
  D_Flip_Flop d_ff_8 (.clk(_11__CP), .D(_18__D7), .Q(_19__Q7), .reset(not_1_out));  // open: Qn, preset, en

  // Other names for the same wires on the sheet: D0 = _3__D0; D1 = _4__D1; D2 = _7__D2; D3 = _8__D3; D4 = _13__D4;
  //   D5 = _14__D5; D6 = _17__D6; D7 = _18__D7; Q0 = _2__Q0; Q1 = _5__Q1; Q2 = _6__Q2; Q3 = _9__Q3; Q4 = _12__Q4;
  //   Q5 = _15__Q5; Q6 = _16__Q6; Q7 = _19__Q7

  // Notes on the sheet:
  //   74273: Octal D-FlipFlop w/ CLEAR
endmodule

module _74283 (
  input  _16__Vcc,
  input  _2__B2,
  input  _15__B3,
  input  _3__A2,
  input  _14__A3,
  input  _5__A1,
  input  _12__A4,
  input  _6__B1,
  input  _11__B4,
  input  _7__C0,
  input  _8__GND,
  output _1__S2,
  output _4__S1,
  output _13__S3,
  output _10__S4,
  output _9__C4
);

  wire and_1_out, and_2_out, and_3_out, and_4_out, and_5_out, and_6_out, and_7_out, and_8_out, and_9_out,
       and_10_out, and_11_out, and_12_out, and_13_out, and_14_out, nand_1_out, nand_2_out, nand_3_out,
       nand_4_out, nor_1_out, nor_2_out, nor_3_out, nor_4_out, nor_6_out, nor_7_out, nor_8_out, not_1_out,
       not_2_out;

  nand nand_1 (nand_1_out, _11__B4, _12__A4);
  nor nor_1 (nor_1_out, _11__B4, _12__A4);
  nand nand_2 (nand_2_out, _15__B3, _14__A3);
  nor nor_2 (nor_2_out, _15__B3, _14__A3);
  nand nand_3 (nand_3_out, _2__B2, _3__A2);
  nor nor_3 (nor_3_out, _2__B2, _3__A2);
  nand nand_4 (nand_4_out, _6__B1, _5__A1);
  nor nor_4 (nor_4_out, _6__B1, _5__A1);
  not not_1 (not_1_out, _7__C0);
  and and_1 (and_1_out, nor_2_out, nand_1_out);
  and and_2 (and_2_out, nor_3_out, nand_1_out, nand_2_out);
  and and_3 (and_3_out, nor_4_out, nand_1_out, nand_2_out, nand_3_out);
  and and_4 (and_4_out, nand_1_out, nand_2_out, nand_3_out, nand_4_out, not_1_out);
  and and_5 (and_5_out, nand_1_out, ~nor_1_out);  // AND_Gate
  and and_6 (and_6_out, nor_3_out, nand_2_out);
  and and_7 (and_7_out, nor_4_out, nand_2_out, nand_3_out);
  and and_8 (and_8_out, nand_2_out, nand_3_out, nand_4_out, not_1_out);
  and and_9 (and_9_out, nand_2_out, ~nor_2_out);  // AND_Gate
  and and_10 (and_10_out, nor_4_out, nand_3_out);
  and and_11 (and_11_out, nand_3_out, nand_4_out, not_1_out);
  and and_12 (and_12_out, nand_3_out, ~nor_3_out);  // AND_Gate
  and and_13 (and_13_out, nand_4_out, not_1_out);
  and and_14 (and_14_out, nand_4_out, ~nor_4_out);  // AND_Gate
  not not_2 (not_2_out, not_1_out);
  nor nor_5 (_9__C4, nor_1_out, and_1_out, and_2_out, and_3_out, and_4_out);
  nor nor_6 (nor_6_out, nor_2_out, and_6_out, and_7_out, and_8_out);
  nor nor_7 (nor_7_out, nor_3_out, and_10_out, and_11_out);
  nor nor_8 (nor_8_out, nor_4_out, and_13_out);
  xor xor_1 (_10__S4, and_5_out, nor_6_out);
  xor xor_2 (_13__S3, and_9_out, nor_7_out);
  xor xor_3 (_1__S2, and_12_out, nor_8_out);
  xor xor_4 (_4__S1, and_14_out, not_2_out);

  // Other names for the same wires on the sheet: A1 = _5__A1; A2 = _3__A2; A3 = _14__A3; A4 = _12__A4; B1 = _6__B1;
  //   B2 = _2__B2; B3 = _15__B3; B4 = _11__B4; C0 = _7__C0; C4 = _9__C4; S1 = _4__S1; S2 = _1__S2; S3 = _13__S3;
  //   S4 = _10__S4

  // Notes on the sheet:
  //   74283: 4-Bit Binary Adder w/ Fast Carry
endmodule

module _74371 (
  input  _1__AD_A,
  input  _20__Vcc,
  input  _2__AD_B,
  input  _19__AD_H,
  input  _3__AD_C,
  input  _18__AD_G,
  input  _4__AD_D,
  input  _17__AD_F,
  input  _5__AD_E,
  input  _16__nS_2,
  input  _6__DO_1,
  input  _15__nS_1,
  input  _7__DO_2,
  input  _14__DO_8,
  input  _8__DO_3,
  input  _13__DO_7,
  input  _9__DO_4,
  input  _12__DO_6,
  input  _10__GND,
  input  _11__DO_5
);

  wire or_1_out;

  or or_1 (or_1_out, _16__nS_2, _15__nS_1);
  ROM rom_1 (
    .addr({_19__AD_H, _18__AD_G, _17__AD_F, _5__AD_E, _4__AD_D, _3__AD_C, _2__AD_B, _1__AD_A}),
    .data({_14__DO_8, _13__DO_7, _12__DO_6, _11__DO_5, _9__DO_4, _8__DO_3, _7__DO_2, _6__DO_1}),
    .sel(or_1_out));

  // Notes on the sheet:
  //   74371: 2048-bit ROM, 256x8
endmodule

module _74377 (
  input  _1__nE,
  input  _20__Vcc,
  input  _3__D0,
  input  _18__D7,
  input  _4__D1,
  input  _17__D6,
  input  _7__D2,
  input  _14__D5,
  input  _8__D3,
  input  _13__D4,
  input  _10__GND,
  input  _11__CP,
  output _2__Q0,
  output _19__Q7,
  output _5__Q1,
  output _16__Q6,
  output _6__Q2,
  output _15__Q5,
  output _9__Q3,
  output _12__Q4
);

  wire and_1_out, and_2_out, and_3_out, and_4_out, and_5_out, and_6_out, and_7_out, and_8_out, and_9_out,
       and_10_out, and_11_out, and_12_out, and_13_out, and_14_out, and_15_out, and_16_out, not_1_out,
       or_1_out, or_2_out, or_3_out, or_4_out, or_5_out, or_6_out, or_7_out, or_8_out;

  not not_1 (not_1_out, _1__nE);
  and and_1 (and_1_out, _3__D0, not_1_out);
  and and_2 (and_2_out, ~not_1_out, _2__Q0);  // AND_Gate
  and and_3 (and_3_out, _4__D1, not_1_out);
  and and_4 (and_4_out, ~not_1_out, _5__Q1);  // AND_Gate
  and and_5 (and_5_out, _7__D2, not_1_out);
  and and_6 (and_6_out, ~not_1_out, _6__Q2);  // AND_Gate
  and and_7 (and_7_out, _8__D3, not_1_out);
  and and_8 (and_8_out, ~not_1_out, _9__Q3);  // AND_Gate
  and and_9 (and_9_out, _13__D4, not_1_out);
  and and_10 (and_10_out, ~not_1_out, _12__Q4);  // AND_Gate
  and and_11 (and_11_out, _14__D5, not_1_out);
  and and_12 (and_12_out, ~not_1_out, _15__Q5);  // AND_Gate
  and and_13 (and_13_out, _17__D6, not_1_out);
  and and_14 (and_14_out, ~not_1_out, _16__Q6);  // AND_Gate
  and and_15 (and_15_out, _18__D7, not_1_out);
  and and_16 (and_16_out, ~not_1_out, _19__Q7);  // AND_Gate
  or or_1 (or_1_out, and_1_out, and_2_out);
  or or_2 (or_2_out, and_3_out, and_4_out);
  or or_3 (or_3_out, and_5_out, and_6_out);
  or or_4 (or_4_out, and_7_out, and_8_out);
  or or_5 (or_5_out, and_9_out, and_10_out);
  or or_6 (or_6_out, and_11_out, and_12_out);
  or or_7 (or_7_out, and_13_out, and_14_out);
  or or_8 (or_8_out, and_15_out, and_16_out);
  D_Flip_Flop d_ff_1 (.clk(_11__CP), .D(or_1_out), .Q(_2__Q0));  // open: Qn, preset, en, reset
  D_Flip_Flop d_ff_2 (.clk(_11__CP), .D(or_2_out), .Q(_5__Q1));  // open: Qn, preset, en, reset
  D_Flip_Flop d_ff_3 (.clk(_11__CP), .D(or_3_out), .Q(_6__Q2));  // open: Qn, preset, en, reset
  D_Flip_Flop d_ff_4 (.clk(_11__CP), .D(or_4_out), .Q(_9__Q3));  // open: Qn, preset, en, reset
  D_Flip_Flop d_ff_5 (.clk(_11__CP), .D(or_5_out), .Q(_12__Q4));  // open: Qn, preset, en, reset
  D_Flip_Flop d_ff_6 (.clk(_11__CP), .D(or_6_out), .Q(_15__Q5));  // open: Qn, preset, en, reset
  D_Flip_Flop d_ff_7 (.clk(_11__CP), .D(or_7_out), .Q(_16__Q6));  // open: Qn, preset, en, reset
  D_Flip_Flop d_ff_8 (.clk(_11__CP), .D(or_8_out), .Q(_19__Q7));  // open: Qn, preset, en, reset

  // Other names for the same wires on the sheet: D0 = _3__D0; D1 = _4__D1; D2 = _7__D2; D3 = _8__D3; D4 = _13__D4;
  //   D5 = _14__D5; D6 = _17__D6; D7 = _18__D7; Q0 = _2__Q0; Q1 = _5__Q1; Q2 = _6__Q2; Q3 = _9__Q3; Q4 = _12__Q4;
  //   Q5 = _15__Q5; Q6 = _16__Q6; Q7 = _19__Q7

  // Notes on the sheet:
  //   74377: Octal D-type flip-flop; positive edge-trigger; write enable
endmodule

module _74574 (
  input  _1__nOE,
  input  _20__Vcc,
  input  _2__D1,
  input  _3__D2,
  input  _4__D3,
  input  _5__D4,
  input  _6__D5,
  input  _7__D6,
  input  _8__D7,
  input  _9__D8,
  input  _10__GND,
  input  _11__CP,
  output _19__Q0,
  output _18__Q1,
  output _17__Q2,
  output _16__Q3,
  output _15__Q4,
  output _14__Q5,
  output _13__Q6,
  output _12__Q7
);

  wire d_ff_1_q, d_ff_2_q, d_ff_3_q, d_ff_4_q, d_ff_5_q, d_ff_6_q, d_ff_7_q, d_ff_8_q, not_1_out;

  not not_1 (not_1_out, _1__nOE);
  D_Flip_Flop #(.trigger("high")) d_ff_1 (.clk(_11__CP), .D(_2__D1), .Q(d_ff_1_q));  // open: Qn, preset, en, reset
  D_Flip_Flop #(.trigger("high")) d_ff_2 (.clk(_11__CP), .D(_3__D2), .Q(d_ff_2_q));  // open: Qn, preset, en, reset
  D_Flip_Flop #(.trigger("high")) d_ff_3 (.clk(_11__CP), .D(_4__D3), .Q(d_ff_3_q));  // open: Qn, preset, en, reset
  D_Flip_Flop #(.trigger("high")) d_ff_4 (.clk(_11__CP), .D(_5__D4), .Q(d_ff_4_q));  // open: Qn, preset, en, reset
  D_Flip_Flop #(.trigger("high")) d_ff_5 (.clk(_11__CP), .D(_6__D5), .Q(d_ff_5_q));  // open: Qn, preset, en, reset
  D_Flip_Flop #(.trigger("high")) d_ff_6 (.clk(_11__CP), .D(_7__D6), .Q(d_ff_6_q));  // open: Qn, preset, en, reset
  D_Flip_Flop #(.trigger("high")) d_ff_7 (.clk(_11__CP), .D(_8__D7), .Q(d_ff_7_q));  // open: Qn, preset, en, reset
  D_Flip_Flop #(.trigger("high")) d_ff_8 (.clk(_11__CP), .D(_9__D8), .Q(d_ff_8_q));  // open: Qn, preset, en, reset
  assign _19__Q0 = not_1_out ? d_ff_1_q : 1'bz;  // Controlled_Buffer controlled_buffer_1
  assign _18__Q1 = not_1_out ? d_ff_2_q : 1'bz;  // Controlled_Buffer controlled_buffer_2
  assign _17__Q2 = not_1_out ? d_ff_3_q : 1'bz;  // Controlled_Buffer controlled_buffer_3
  assign _16__Q3 = not_1_out ? d_ff_4_q : 1'bz;  // Controlled_Buffer controlled_buffer_4
  assign _15__Q4 = not_1_out ? d_ff_5_q : 1'bz;  // Controlled_Buffer controlled_buffer_5
  assign _14__Q5 = not_1_out ? d_ff_6_q : 1'bz;  // Controlled_Buffer controlled_buffer_6
  assign _13__Q6 = not_1_out ? d_ff_7_q : 1'bz;  // Controlled_Buffer controlled_buffer_7
  assign _12__Q7 = not_1_out ? d_ff_8_q : 1'bz;  // Controlled_Buffer controlled_buffer_8

  // Notes on the sheet:
  //   74574: Octal D-type flip-flop; positive edge-trigger; 3-state
endmodule

module _74595 (
  input  _16__Vcc,
  input  _14__SER,
  input  _13__nOE,
  input  _12__RCLK,
  input  _11__SRCLK,
  input  _10__nSRCLR,
  input  _8__GND,
  output _1__QB,
  output _2__QC,
  output _15__QA,
  output _3__QD,
  output _4__QE,
  output _5__QF,
  output _6__QG,
  output _7__QH,
  output _9__QH_prime
);

  wire d_ff_1_q, d_ff_2_q, d_ff_3_q, d_ff_4_q, d_ff_5_q, d_ff_6_q, d_ff_7_q, d_ff_9_q, d_ff_10_q, d_ff_11_q,
       d_ff_12_q, d_ff_13_q, d_ff_14_q, d_ff_15_q, d_ff_16_q, not_1_out, not_2_out;

  not not_1 (not_1_out, _10__nSRCLR);
  D_Flip_Flop d_ff_1 (.clk(_11__SRCLK), .D(_14__SER), .Q(d_ff_1_q), .reset(not_1_out));  // open: Qn, preset, en
  D_Flip_Flop d_ff_2 (.clk(_11__SRCLK), .D(d_ff_1_q), .Q(d_ff_2_q), .reset(not_1_out));  // open: Qn, preset, en
  D_Flip_Flop d_ff_3 (.clk(_11__SRCLK), .D(d_ff_2_q), .Q(d_ff_3_q), .reset(not_1_out));  // open: Qn, preset, en
  D_Flip_Flop d_ff_4 (.clk(_11__SRCLK), .D(d_ff_3_q), .Q(d_ff_4_q), .reset(not_1_out));  // open: Qn, preset, en
  D_Flip_Flop d_ff_5 (.clk(_11__SRCLK), .D(d_ff_4_q), .Q(d_ff_5_q), .reset(not_1_out));  // open: Qn, preset, en
  D_Flip_Flop d_ff_6 (.clk(_11__SRCLK), .D(d_ff_5_q), .Q(d_ff_6_q), .reset(not_1_out));  // open: Qn, preset, en
  D_Flip_Flop d_ff_7 (.clk(_11__SRCLK), .D(d_ff_6_q), .Q(d_ff_7_q), .reset(not_1_out));  // open: Qn, preset, en
  D_Flip_Flop d_ff_8 (.clk(_11__SRCLK), .D(d_ff_7_q), .Q(_9__QH_prime), .reset(not_1_out));  // open: Qn, preset, en
  not not_2 (not_2_out, _13__nOE);
  D_Flip_Flop d_ff_9 (.clk(_12__RCLK), .D(d_ff_1_q), .Q(d_ff_9_q));  // open: Qn, preset, en, reset
  D_Flip_Flop d_ff_10 (.clk(_12__RCLK), .D(d_ff_2_q), .Q(d_ff_10_q));  // open: Qn, preset, en, reset
  D_Flip_Flop d_ff_11 (.clk(_12__RCLK), .D(d_ff_3_q), .Q(d_ff_11_q));  // open: Qn, preset, en, reset
  D_Flip_Flop d_ff_12 (.clk(_12__RCLK), .D(d_ff_4_q), .Q(d_ff_12_q));  // open: Qn, preset, en, reset
  D_Flip_Flop d_ff_13 (.clk(_12__RCLK), .D(d_ff_5_q), .Q(d_ff_13_q));  // open: Qn, preset, en, reset
  D_Flip_Flop d_ff_14 (.clk(_12__RCLK), .D(d_ff_6_q), .Q(d_ff_14_q));  // open: Qn, preset, en, reset
  D_Flip_Flop d_ff_15 (.clk(_12__RCLK), .D(d_ff_7_q), .Q(d_ff_15_q));  // open: Qn, preset, en, reset
  D_Flip_Flop d_ff_16 (.clk(_12__RCLK), .D(_9__QH_prime), .Q(d_ff_16_q));  // open: Qn, preset, en, reset
  assign _15__QA = not_2_out ? d_ff_9_q : 1'bz;  // Controlled_Buffer controlled_buffer_1
  assign _1__QB = not_2_out ? d_ff_10_q : 1'bz;  // Controlled_Buffer controlled_buffer_2
  assign _2__QC = not_2_out ? d_ff_11_q : 1'bz;  // Controlled_Buffer controlled_buffer_3
  assign _3__QD = not_2_out ? d_ff_12_q : 1'bz;  // Controlled_Buffer controlled_buffer_4
  assign _4__QE = not_2_out ? d_ff_13_q : 1'bz;  // Controlled_Buffer controlled_buffer_5
  assign _5__QF = not_2_out ? d_ff_14_q : 1'bz;  // Controlled_Buffer controlled_buffer_6
  assign _6__QG = not_2_out ? d_ff_15_q : 1'bz;  // Controlled_Buffer controlled_buffer_7
  assign _7__QH = not_2_out ? d_ff_16_q : 1'bz;  // Controlled_Buffer controlled_buffer_8

  // Other names for the same wires on the sheet: nOE = _13__nOE; nSRCLR = _10__nSRCLR; QA = _15__QA; QB = _1__QB;
  //   QC = _2__QC; QD = _3__QD; QE = _4__QE; QF = _5__QF; QG = _6__QG; QH = _7__QH; QH_prime = _9__QH_prime;
  //   RCLK = _12__RCLK; SER = _14__SER; SRCLK = _11__SRCLK

  // Notes on the sheet:
  //   74595: 8-Bit Shifter Serial-in/Parallel-out
endmodule

module _74682 (
  input  _20__Vcc,
  input  _2__A0,
  input  _3__B0,
  input  _18__B7,
  input  _4__A1,
  input  _17__A7,
  input  _5__B1,
  input  _16__B6,
  input  _6__A2,
  input  _15__A6,
  input  _7__B2,
  input  _14__B5,
  input  _8__A3,
  input  _13__A5,
  input  _9__B3,
  input  _12__B4,
  input  _10__GND,
  input  _11__A4,
  output _1__A___B,
  output _19__A___B
);

  wire and_1_out, and_2_out, and_3_out, and_4_out, and_5_out, and_6_out, and_7_out, and_8_out, not_1_out,
       not_2_out, not_3_out, not_4_out, not_5_out, not_6_out, not_7_out, not_8_out, not_9_out, not_10_out,
       not_11_out, not_12_out, not_13_out, not_14_out, not_15_out, not_16_out, not_17_out, not_18_out,
       not_19_out, not_20_out, not_21_out, not_22_out, not_23_out, not_24_out, xnor_1_out, xnor_3_out,
       xnor_4_out, xnor_5_out, xnor_6_out, xnor_8_out;

  not not_1 (not_1_out, _2__A0);
  not not_2 (not_2_out, _3__B0);
  not not_3 (not_3_out, _4__A1);
  not not_4 (not_4_out, _5__B1);
  not not_5 (not_5_out, _6__A2);
  not not_6 (not_6_out, _7__B2);
  not not_7 (not_7_out, _8__A3);
  not not_8 (not_8_out, _9__B3);
  not not_9 (not_9_out, _11__A4);
  not not_10 (not_10_out, _12__B4);
  not not_11 (not_11_out, _13__A5);
  not not_12 (not_12_out, _14__B5);
  not not_13 (not_13_out, _15__A6);
  not not_14 (not_14_out, _16__B6);
  not not_15 (not_15_out, _17__A7);
  not not_16 (not_16_out, _18__B7);
  xnor xnor_1 (xnor_1_out, not_1_out, not_2_out);
  xnor xnor_2 (not_16_out, not_3_out, not_4_out);
  xnor xnor_3 (xnor_3_out, not_5_out, not_6_out);
  xnor xnor_4 (xnor_4_out, not_7_out, not_8_out);
  xnor xnor_5 (xnor_5_out, not_9_out, not_10_out);
  xnor xnor_6 (xnor_6_out, not_11_out, not_12_out);
  xnor xnor_7 (xnor_4_out, not_13_out, not_14_out);
  xnor xnor_8 (xnor_8_out, not_15_out, not_16_out);
  not not_17 (not_17_out, not_15_out);
  not not_18 (not_18_out, not_13_out);
  not not_19 (not_19_out, not_11_out);
  not not_20 (not_20_out, not_9_out);
  not not_21 (not_21_out, not_7_out);
  not not_22 (not_22_out, not_5_out);
  not not_23 (not_23_out, not_3_out);
  not not_24 (not_24_out, not_1_out);
  and and_1 (and_1_out, xnor_1_out, not_16_out, xnor_3_out, xnor_4_out, xnor_5_out, xnor_6_out, xnor_4_out, not_16_out, not_17_out);
  and and_2 (and_2_out, xnor_1_out, not_16_out, xnor_3_out, xnor_4_out, xnor_5_out, xnor_6_out, not_14_out, not_18_out);
  and and_3 (and_3_out, xnor_1_out, not_16_out, xnor_3_out, xnor_4_out, xnor_5_out, not_12_out, not_19_out);
  and and_4 (and_4_out, xnor_1_out, not_16_out, xnor_3_out, xnor_4_out, not_10_out, not_20_out);
  and and_5 (and_5_out, xnor_1_out, not_16_out, xnor_3_out, not_8_out, not_21_out);
  and and_6 (and_6_out, xnor_1_out, not_16_out, not_6_out, not_22_out);
  and and_7 (and_7_out, xnor_1_out, not_4_out, not_23_out);
  and and_8 (and_8_out, not_2_out, not_24_out);
  nand nand_1 (_19__A___B, xnor_1_out, not_16_out, xnor_3_out, xnor_4_out, xnor_5_out, xnor_6_out, xnor_4_out, xnor_8_out);
  nor nor_1 (_1__A___B, and_1_out, and_2_out, and_3_out, and_4_out, and_5_out, and_6_out, and_7_out, and_8_out);

  // Notes on the sheet:
  //   74682: 8-bit magnitude comparator 
endmodule

module _744075 (
  input  _1__1A,
  input  _14__Vcc,
  input  _2__1B,
  input  _13__1C,
  input  _3__2A,
  input  _4__2B,
  input  _11__3C,
  input  _5__2C,
  input  _10__3B,
  input  _9__3A,
  input  _7__GND,
  output _12__1Y,
  output _6__2Y,
  output _8__3Y
);

  or or_1 (_6__2Y, _5__2C, _4__2B, _3__2A);
  or or_2 (_12__1Y, _2__1B, _1__1A, _13__1C);
  or or_3 (_8__3Y, _11__3C, _10__3B, _9__3A);

  // Notes on the sheet:
  //   744075: triple 3-input OR 
endmodule

// 27C512
module _27C512_1 (
  input  _1__A15,
  input  _28__Vcc,
  input  _2__A12,
  input  _27__A14,
  input  _3__A7,
  input  _26__A13,
  input  _4__A6,
  input  _25__A8,
  input  _5__A5,
  input  _24__A9,
  input  _6__A4,
  input  _23__A11,
  input  _7__A3,
  input  _22__nOE_Vpp,
  input  _8__A2,
  input  _21__A10,
  input  _9__A1,
  input  _20__nCE,
  input  _10__A0,
  input  _14__GND,
  output _19__O7,
  output _11__O0,
  output _18__O6,
  output _12__O1,
  output _17__O5,
  output _13__O2,
  output _16__O4,
  output _15__O3
);

  wire not_1_out;
  wire [7:0] rom_1_data;

  not not_1 (not_1_out, _22__nOE_Vpp);
  ROM #(.addrWidth(16)) rom_1 (
    .addr({_1__A15, _27__A14, _26__A13, _2__A12, _23__A11, _21__A10, _24__A9, _25__A8, _3__A7, _4__A6, _5__A5, _6__A4, _7__A3, _8__A2, _9__A1, _10__A0}),
    .data(rom_1_data));  // open: sel
  assign {_19__O7, _18__O6, _17__O5, _16__O4, _15__O3, _13__O2, _12__O1, _11__O0} = not_1_out ? rom_1_data : 8'bz;  // Controlled_Buffer controlled_buffer_1

  // Notes on the sheet:
  //   27C512: 64K x 8-bit EPROM 
endmodule

// 27C512
module _27C512_2 (
  input  _1__A15,
  input  _28__Vcc,
  input  _2__A12,
  input  _27__A14,
  input  _3__A7,
  input  _26__A13,
  input  _4__A6,
  input  _25__A8,
  input  _5__A5,
  input  _24__A9,
  input  _6__A4,
  input  _23__A11,
  input  _7__A3,
  input  _22__nOE_Vpp,
  input  _8__A2,
  input  _21__A10,
  input  _9__A1,
  input  _20__nCE,
  input  _10__A0,
  input  _14__GND,
  output _19__O7,
  output _11__O0,
  output _18__O6,
  output _12__O1,
  output _17__O5,
  output _13__O2,
  output _16__O4,
  output _15__O3
);

  wire not_1_out;
  wire [7:0] rom_1_data;

  not not_1 (not_1_out, _22__nOE_Vpp);
  ROM #(.addrWidth(16)) rom_1 (
    .addr({_1__A15, _27__A14, _26__A13, _2__A12, _23__A11, _21__A10, _24__A9, _25__A8, _3__A7, _4__A6, _5__A5, _6__A4, _7__A3, _8__A2, _9__A1, _10__A0}),
    .data(rom_1_data));  // open: sel
  assign {_19__O7, _18__O6, _17__O5, _16__O4, _15__O3, _13__O2, _12__O1, _11__O0} = not_1_out ? rom_1_data : 8'bz;  // Controlled_Buffer controlled_buffer_1

  // Notes on the sheet:
  //   27C512: 64K x 8-bit EPROM 
endmodule

// 27C512
module _27C512_3 (
  input  _1__A15,
  input  _28__Vcc,
  input  _2__A12,
  input  _27__A14,
  input  _3__A7,
  input  _26__A13,
  input  _4__A6,
  input  _25__A8,
  input  _5__A5,
  input  _24__A9,
  input  _6__A4,
  input  _23__A11,
  input  _7__A3,
  input  _22__nOE_Vpp,
  input  _8__A2,
  input  _21__A10,
  input  _9__A1,
  input  _20__nCE,
  input  _10__A0,
  input  _14__GND,
  output _19__O7,
  output _11__O0,
  output _18__O6,
  output _12__O1,
  output _17__O5,
  output _13__O2,
  output _16__O4,
  output _15__O3
);

  wire not_1_out;
  wire [7:0] rom_1_data;

  not not_1 (not_1_out, _22__nOE_Vpp);
  ROM #(.addrWidth(16)) rom_1 (
    .addr({_1__A15, _27__A14, _26__A13, _2__A12, _23__A11, _21__A10, _24__A9, _25__A8, _3__A7, _4__A6, _5__A5, _6__A4, _7__A3, _8__A2, _9__A1, _10__A0}),
    .data(rom_1_data));  // open: sel
  assign {_19__O7, _18__O6, _17__O5, _16__O4, _15__O3, _13__O2, _12__O1, _11__O0} = not_1_out ? rom_1_data : 8'bz;  // Controlled_Buffer controlled_buffer_1

  // Notes on the sheet:
  //   27C512: 64K x 8-bit EPROM 
endmodule
