// Logisim project Gigatron TTL.circ as structural Verilog: 18 circuits, main circuit Gigatron TTL
module Gigatron_TTL (
  input  auto_clock_switch_manual,
  input  manual_clock,
  input  SER_DATA,
  output SER_LATCH,
  output SER_PULSE,
  output [7:0] To_DAC_VGA,
  output [3:0] To_DAC_Sound
);

  wire AC7, AL, AR0, AR1, AR2, AR3, CLK1, CLK2, CO, EH, EL, IX, nAE, nDE, nIE, nLD, nOE, nOL, nPH, nPL, nRST,
       nWE, nXL, nYL, Reset_Button_out, System_clock_out;
  wire [2:0] ac_accumulator_register_1_q;
  wire [3:0] ac_accumulator_register_1_q_2, alu_1_alu, alu_1_alu_2, bus_ac_tristate_buffer_1_q,
       bus_ac_tristate_buffer_1_q_2, d_data_register_1_q, d_data_register_1_q_2,
       mau_memory_address_unit_1_to_ram_2, mau_memory_address_unit_1_to_ram_3, pc_program_counter_1_to_rom,
       pc_program_counter_1_to_rom_2, pc_program_counter_1_to_rom_3, pc_program_counter_1_to_rom_4,
       x_x_register_1_x_output, x_x_register_1_x_output_2, xout_extented_output_1_q, y_y_register_1_q;
  wire [7:0] ir_instruction_register_1_q, rom_1_to_d, rom_1_to_ir;
  wire [7:4] y_y_register_1_q_2;
  wire [14:8] mau_memory_address_unit_1_to_ram;

  LED led_1 (.in(y_y_register_1_q_2[7]));
  LED led_2 (.in(y_y_register_1_q_2[6]));
  LED led_3 (.in(alu_1_alu[2]));
  LED led_4 (.in(alu_1_alu[3]));
  Hex_Digit_Display hex_digit_display_1 (.value(y_y_register_1_q_2));  // open: dp
  Hex_Digit_Display hex_digit_display_2 (.value(y_y_register_1_q));  // open: dp
  LED led_5 (.in(y_y_register_1_q[3]));
  LED led_6 (.in(y_y_register_1_q_2[5]));
  LED led_7 (.in(y_y_register_1_q[2]));
  LED led_8 (.in(y_y_register_1_q_2[4]));
  Hex_Digit_Display hex_digit_display_3 (.value(alu_1_alu_2));  // open: dp
  Hex_Digit_Display hex_digit_display_4 (.value(alu_1_alu));  // open: dp
  LED led_9 (.in(alu_1_alu[1]));
  LED led_10 (.in(alu_1_alu[0]));
  LED led_11 (.in(alu_1_alu_2[2]));
  LED led_12 (.in(alu_1_alu_2[3]));
  OUT__Output_register out_output_register_1 (
    .D({alu_1_alu, alu_1_alu_2}), .Q({SER_LATCH, SER_PULSE, To_DAC_VGA[5:0]}), .CP(CLK2), .nE(nOL));
  LED led_13 (.in(SER_LATCH));
  LED led_14 (.in(SER_PULSE));
  LED led_15 (.in(y_y_register_1_q[0]));
  LED led_16 (.in(y_y_register_1_q[1]));
  LED led_17 (.in(alu_1_alu_2[1]));
  LED led_18 (.in(alu_1_alu_2[0]));
  Hex_Digit_Display hex_digit_display_5 (.value(To_DAC_VGA[3:0]));  // open: dp
  Hex_Digit_Display hex_digit_display_6 (.value({SER_LATCH, SER_PULSE, To_DAC_VGA[5:4]}));  // open: dp
  LED led_19 (.in(To_DAC_VGA[5]));
  LED led_20 (.in(To_DAC_VGA[3]));
  LED led_21 (.in(To_DAC_VGA[2]));
  LED led_22 (.in(To_DAC_VGA[4]));
  Hex_Digit_Display hex_digit_display_7 (.value(pc_program_counter_1_to_rom_3));  // open: dp
  LED led_23 (.in(To_DAC_VGA[1]));
  LED led_24 (.in(To_DAC_VGA[0]));
  Hex_Digit_Display hex_digit_display_8 (.value(pc_program_counter_1_to_rom));  // open: dp
  PC__Program_Counter pc_program_counter_1 (
    .From_Bus({bus_ac_tristate_buffer_1_q, bus_ac_tristate_buffer_1_q_2}),
    .From_Y({y_y_register_1_q_2, y_y_register_1_q}),
    .To_ROM({pc_program_counter_1_to_rom_3, pc_program_counter_1_to_rom, pc_program_counter_1_to_rom_2, pc_program_counter_1_to_rom_4}),
    .clk(CLK1), .nreset(nRST), .nPL(nPL), .nPH(nPH));
  Hex_Digit_Display hex_digit_display_9 (.value(pc_program_counter_1_to_rom_4));  // open: dp
  Hex_Digit_Display hex_digit_display_10 (.value(pc_program_counter_1_to_rom_2));  // open: dp
  Y__Y_register y_y_register_1 (
    .D({alu_1_alu, alu_1_alu_2}), .Q({y_y_register_1_q_2, y_y_register_1_q}), .CP(CLK2), .nE(nYL));
  X__X_register x_x_register_1 (
    .From_ALU({alu_1_alu, alu_1_alu_2}), .X_output({x_x_register_1_x_output, x_x_register_1_x_output_2}),
    .CP(CLK2), .IX(IX), .nXL(nXL));
  ALU alu_1 (
    .AC({AC7, ac_accumulator_register_1_q, ac_accumulator_register_1_q_2}),
    .Bus({bus_ac_tristate_buffer_1_q, bus_ac_tristate_buffer_1_q_2}), .ALU({alu_1_alu, alu_1_alu_2}),
    .CO(CO), .AL(AL), .AR({AR3, AR2, AR1, AR0}));
  ROM rom_1 (
    .From_PC({pc_program_counter_1_to_rom_3, pc_program_counter_1_to_rom, pc_program_counter_1_to_rom_2, pc_program_counter_1_to_rom_4}),
    .To_IR(rom_1_to_ir), .To_D(rom_1_to_d));
  Hex_Digit_Display hex_digit_display_11 (.value(x_x_register_1_x_output));  // open: dp
  LED led_25 (.in(x_x_register_1_x_output[1]));
  LED led_26 (.in(x_x_register_1_x_output[2]));
  LED led_27 (.in(x_x_register_1_x_output[3]));
  Clock_part System_clock (.out(System_clock_out));
  Button Reset_Button (.out(Reset_Button_out));
  Pull_Resistor #(.pull(1)) pull_resistor_1 (.node(nRST));
  not not_1 (nRST, Reset_Button_out);
  Hex_Digit_Display hex_digit_display_12 (.value(d_data_register_1_q_2));  // open: dp
  Hex_Digit_Display hex_digit_display_13 (.value(x_x_register_1_x_output_2));  // open: dp
  LED led_28 (.in(x_x_register_1_x_output_2[1]));
  LED led_29 (.in(x_x_register_1_x_output_2[3]));
  LED led_30 (.in(x_x_register_1_x_output[0]));
  LED led_31 (.in(x_x_register_1_x_output_2[2]));
  Hex_Digit_Display hex_digit_display_14 (.value(d_data_register_1_q));  // open: dp
  LED led_32 (.in(x_x_register_1_x_output_2[0]));
  AC__Accumulator_register ac_accumulator_register_1 (
    .D({alu_1_alu, alu_1_alu_2}), .Q({AC7, ac_accumulator_register_1_q, ac_accumulator_register_1_q_2}),
    .CP(CLK2), .nE(nLD));
  XOUT__Extented_Output xout_extented_output_1 (
    .CP(SER_LATCH), .D({AC7, ac_accumulator_register_1_q, ac_accumulator_register_1_q_2}),
    .Q({To_DAC_Sound, xout_extented_output_1_q}));
  Clock clock_1 (
    .clk(System_clock_out), .switch(auto_clock_switch_manual), .manual(manual_clock), .clock_output(CLK1),
    .clock__output(CLK2));  // open: halt
  IR__Instruction_register ir_instruction_register_1 (.D(rom_1_to_ir), .Q(ir_instruction_register_1_q), .CP(CLK1));
  D__Data_register d_data_register_1 (.D(rom_1_to_d), .Q({d_data_register_1_q_2, d_data_register_1_q}), .CP(CLK1));
  MAU__Memory_Address_Unit mau_memory_address_unit_1 (
    .Fropm_X({x_x_register_1_x_output, x_x_register_1_x_output_2}),
    .From_D({d_data_register_1_q_2, d_data_register_1_q}), .From_Y({y_y_register_1_q_2, y_y_register_1_q}),
    .To_RAM({mau_memory_address_unit_1_to_ram, mau_memory_address_unit_1_to_ram_2, mau_memory_address_unit_1_to_ram_3}),
    .EL(EL), .EH(EH));
  LED led_33 (.in(xout_extented_output_1_q[2]));
  LED led_34 (.in(xout_extented_output_1_q[3]));
  Hex_Digit_Display hex_digit_display_15 (.value(ir_instruction_register_1_q[7:4]));  // open: dp
  LED led_35 (.in(xout_extented_output_1_q[1]));
  LED led_36 (.in(xout_extented_output_1_q[0]));
  Hex_Digit_Display hex_digit_display_16 (.value(ir_instruction_register_1_q[3:0]));  // open: dp
  Hex_Digit_Display hex_digit_display_17 (.value({1'b0, mau_memory_address_unit_1_to_ram[14:12]}));  // open: dp
  Hex_Digit_Display hex_digit_display_18 (.value(mau_memory_address_unit_1_to_ram[11:8]));  // open: dp
  Hex_Digit_Display hex_digit_display_19 (.value(mau_memory_address_unit_1_to_ram_2));  // open: dp
  Hex_Digit_Display hex_digit_display_20 (.value(mau_memory_address_unit_1_to_ram_3));  // open: dp
  Hex_Digit_Display hex_digit_display_21 (.value({AC7, ac_accumulator_register_1_q}));  // open: dp
  LED led_37 (.in(ac_accumulator_register_1_q[1]));
  LED led_38 (.in(ac_accumulator_register_1_q[2]));
  LED led_39 (.in(AC7));
  BUS_AC__Tristate_Buffer bus_ac_tristate_buffer_1 (
    .D({AC7, ac_accumulator_register_1_q, ac_accumulator_register_1_q_2}),
    .Q({bus_ac_tristate_buffer_1_q, bus_ac_tristate_buffer_1_q_2}), ._1G(nAE), ._2G(nAE));
  CU__Control_Unit cu_control_unit_1 (
    .From_IR(ir_instruction_register_1_q), .nIE(nIE), .nAE(nAE), .nOE(nOE), .nDE(nDE), .nXL(nXL), .nYL(nYL),
    .IX(IX), .nWE(nWE), .EH(EH), .EL(EL), .nOL(nOL), .nLD(nLD), .nPH(nPH), .nPL(nPL), .AL(AL), .AR0(AR0),
    .AR1(AR1), .AR2(AR2), .AR3(AR3), .CO(CO), .AC7(AC7), .CLK1(CLK1));
  BUS_D__Tristate_Buffer bus_d_tristate_buffer_1 (
    .D({d_data_register_1_q_2, d_data_register_1_q}),
    .Q({bus_ac_tristate_buffer_1_q, bus_ac_tristate_buffer_1_q_2}), ._1G(nDE), ._2G(nDE));
  RAM ram_1 (
    .Address({mau_memory_address_unit_1_to_ram, mau_memory_address_unit_1_to_ram_2, mau_memory_address_unit_1_to_ram_3}),
    .Output({bus_ac_tristate_buffer_1_q, bus_ac_tristate_buffer_1_q_2}),
    .Input({bus_ac_tristate_buffer_1_q, bus_ac_tristate_buffer_1_q_2}), .nWE(nWE), .nOE(nOE));
  Hex_Digit_Display hex_digit_display_22 (.value(ac_accumulator_register_1_q_2));  // open: dp
  LED led_40 (.in(ac_accumulator_register_1_q_2[2]));
  LED led_41 (.in(ac_accumulator_register_1_q[0]));
  LED led_42 (.in(ac_accumulator_register_1_q_2[3]));
  LED led_43 (.in(ac_accumulator_register_1_q_2[1]));
  LED led_44 (.in(ac_accumulator_register_1_q_2[0]));
  LED led_45 (.in(bus_ac_tristate_buffer_1_q[3]));
  Hex_Digit_Display hex_digit_display_23 (.value(bus_ac_tristate_buffer_1_q));  // open: dp
  Hex_Digit_Display hex_digit_display_24 (.value(bus_ac_tristate_buffer_1_q_2));  // open: dp
  LED led_46 (.in(bus_ac_tristate_buffer_1_q_2[3]));
  LED led_47 (.in(bus_ac_tristate_buffer_1_q[1]));
  LED led_48 (.in(bus_ac_tristate_buffer_1_q[2]));
  LED led_49 (.in(bus_ac_tristate_buffer_1_q[0]));
  LED led_50 (.in(bus_ac_tristate_buffer_1_q_2[1]));
  LED led_51 (.in(bus_ac_tristate_buffer_1_q_2[2]));
  LED led_52 (.in(bus_ac_tristate_buffer_1_q_2[0]));
  BUS_IN__Shifter_8_bits bus_in_shifter_8_bits_1 (
    .out_5({bus_ac_tristate_buffer_1_q, bus_ac_tristate_buffer_1_q_2}), .SER_IN(SER_DATA), .PCLK(SER_PULSE),
    .CLK(SER_PULSE), .nOE(nIE));
  Pull_Resistor #(.pull(1)) pull_resistor_2 (.node(SER_DATA));

  assign To_DAC_VGA[7:6] = {SER_LATCH, SER_PULSE};

  // Other names for the same wires on the sheet: HSync = SER_PULSE; VSync = SER_LATCH

  // Notes on the sheet:
  //   Control Panel
  //   Controller Port
endmodule

module Clock (
  input  clk,
  input  switch,
  input  manual,
  input  halt,
  output clock_output,
  output clock__output
);

  wire and_1_out, and_2_out, not_1_out, not_2_out, or_1_out;

  not not_1 (not_1_out, switch);
  not not_2 (not_2_out, halt);
  and and_1 (and_1_out, clk, switch);
  and and_2 (and_2_out, not_1_out, manual);
  or or_1 (or_1_out, and_1_out, and_2_out);
  and and_3 (clock_output, or_1_out, not_2_out);
  not not_3 (clock__output, clock_output);

  // Notes on the sheet:
  //   manual: pull=down
  //   halt: pull=down
endmodule

// CU
module CU__Control_Unit (
  input  CO,
  input  AC7,
  input  CLK1,
  input  [7:0] From_IR,
  output nIE,
  output nAE,
  output nOE,
  output nDE,
  output nXL,
  output nYL,
  output IX,
  output nWE,
  output EH,
  output EL,
  output nOL,
  output nLD,
  output nPH,
  output nPL,
  output AL,
  output AR0,
  output AR1,
  output AR2,
  output AR3
);

  wire and_1_out, and_2_out, and_3_out, and_4_out, and_7_out, and_8_out, and_9_out, n74138_1__7__y7,
       n74138_1__9__y6, n74138_1__12__y3, n74138_1__13__y2, n74138_1__14__y1, n74138_1__15__y0,
       n74138_2__7__y7, n74138_2__9__y6, n74138_2__10__y5, n74138_2__11__y4, n74138_2__12__y3,
       n74138_2__13__y2, n74138_2__14__y1, n74138_2__15__y0, n74139_1__12__2y0, n74153_1__7__y1,
       n74153_1__9__y2, n74240_1__16__1y2, n74240_1__18__1y1;

  _74139 u_74139_1 (
    ._1__1G(1'b0), ._2__1A(From_IR[0]), ._3__1B(From_IR[1]), ._4__1Y0(nDE), ._5__1Y1(nOE), ._6__1Y2(nAE),
    ._7__1Y3(nIE), ._15__2G(From_IR[4]), ._14__2A(From_IR[3]), ._13__2B(From_IR[2]),
    ._12__2Y0(n74139_1__12__2y0));  // open: _8__GND, _16__Vcc, _11__2Y1, _10__2Y2, _9__2Y3
  _74138 u_74138_1 (
    ._1__A(From_IR[2]), ._2__B(From_IR[3]), ._3__C(From_IR[4]), ._4__G2A(1'b0), ._5__G2B(1'b0),
    ._6__G1(n74138_2__7__y7), ._7__Y7(n74138_1__7__y7), ._15__Y0(n74138_1__15__y0),
    ._14__Y1(n74138_1__14__y1), ._13__Y2(n74138_1__13__y2), ._12__Y3(n74138_1__12__y3), ._11__Y4(nXL),
    ._10__Y5(nYL), ._9__Y6(n74138_1__9__y6));  // open: _8__GND, _16__Vcc
  _74138 u_74138_2 (
    ._1__A(From_IR[5]), ._2__B(From_IR[6]), ._3__C(From_IR[7]), ._4__G2A(1'b0), ._5__G2B(1'b0),
    ._6__G1(1'b1), ._7__Y7(n74138_2__7__y7), ._15__Y0(n74138_2__15__y0), ._14__Y1(n74138_2__14__y1),
    ._13__Y2(n74138_2__13__y2), ._12__Y3(n74138_2__12__y3), ._11__Y4(n74138_2__11__y4),
    ._10__Y5(n74138_2__10__y5), ._9__Y6(n74138_2__9__y6));  // open: _8__GND, _16__Vcc
  _74153 u_74153_1 (
    ._1__nG1(n74138_2__7__y7), ._2__B(CO), ._3__1C3(1'b0), ._4__1C2(From_IR[4]), ._5__1C1(From_IR[3]),
    ._6__1C0(From_IR[2]), ._7__Y1(n74153_1__7__y1), ._15__nG2(1'b0), ._14__A(AC7), ._13__2C3(1'b0),
    ._12__2C2(1'b0), ._11__2C1(1'b0), ._10__2C0(1'b0), ._9__Y2(n74153_1__9__y2));  // open: _8__GND, _16__Vcc
  and and_1 (and_1_out, n74138_1__12__y3, n74138_1__13__y2, n74138_1__14__y1, n74138_1__15__y0);
  and and_2 (and_2_out, n74138_1__7__y7, n74138_1__9__y6);
  and and_3 (and_3_out, From_IR[7], n74138_2__7__y7);
  and and_4 (and_4_out, n74138_2__7__y7, n74138_2__10__y5);
  and and_5 (EL, n74138_1__7__y7, n74138_1__12__y3, n74138_1__14__y1);
  and and_6 (EH, n74138_1__12__y3, n74138_1__13__y2, n74138_1__7__y7);
  and and_7 (and_7_out, n74138_2__7__y7, n74138_2__11__y4, n74138_2__12__y3, n74138_2__13__y2, n74138_2__15__y0);
  and and_8 (and_8_out, n74138_2__10__y5, n74138_2__12__y3, n74138_2__13__y2);
  and and_9 (and_9_out, n74138_2__11__y4, n74138_2__13__y2, n74138_2__14__y1, n74138_2__15__y0);
  _7432 u_7432_1 (
    ._1__1A(CLK1), ._2__1B(n74138_2__9__y6), ._3__1Y(nWE), ._4__2A(and_2_out), ._5__2B(n74240_1__16__1y2),
    ._6__2Y(nOL), ._13__4B(n74138_2__7__y7), ._12__4A(n74139_1__12__2y0), ._11__4Y(nPH),
    ._10__3B(n74240_1__16__1y2), ._9__3A(and_1_out), ._8__3Y(nLD));  // open: _7__GND, _14__Vcc
  _74240 u_74240_1 (
    ._1___1G(1'b0), ._2__1A1(n74153_1__7__y1), ._3__2Y4(AR3), ._4__1A2(n74138_2__9__y6), ._5__2Y3(IX),
    ._6__1A3(and_7_out), ._7__2Y2(AR1), ._8__1A4(and_4_out), ._9__2Y1(AL), ._19___2G(1'b0),
    ._18__1Y1(n74240_1__18__1y1), ._17__2A4(and_9_out), ._16__1Y2(n74240_1__16__1y2),
    ._15__2A3(n74138_1__7__y7), ._14__1Y3(AR2), ._13__2A2(and_8_out), ._12__1Y4(AR0), ._11__2A1(and_3_out));  // open: _10__GND, _20__Vcc
  and and_10 (nPL, nPH, n74240_1__18__1y1);

  // Notes on the sheet:
  //    greater
  //    less
  //    equal
  //   Bus access decoder
  //   Mode decoder
  //   [D],AC
  //   [X],AC
  //   [Y,D],AC
  //   [Y,X],AC
  //   [D],X
  //   [D],Y
  //   [D],OUT
  //   LD
  //   AND
  //   OR
  //   XOR
  //   ADD
  //   SUB
  //   ST
  //   Bcc
  //   [Y,X++],OUT
  //   Diodes matrix equivalent
  //   Diodes matrix equivalent
  //   To BUS
  //   To PC
  //   To ALU
  //   To user registers
  //   To memory address unit
  //   To user registers
endmodule

module ALU (
  input  AL,
  input  [3:0] AR,
  input  [7:0] AC,
  input  [7:0] Bus,
  output [7:0] ALU,
  output CO
);

  wire n74153_1__7__y1, n74153_1__9__y2, n74153_2__7__y1, n74153_2__9__y2, n74153_3__7__y1, n74153_3__9__y2,
       n74153_4__7__y1, n74153_4__9__y2, n74153_5__7__y1, n74153_5__9__y2, n74153_6__7__y1, n74153_6__9__y2,
       n74153_7__7__y1, n74153_7__9__y2, n74153_8__7__y1, n74153_8__9__y2, n74283_1__9__c4;

  _74153 u_74153_1 (
    ._1__nG1(1'b0), ._2__B(Bus[0]), ._3__1C3(AR[3]), ._4__1C2(AR[2]), ._5__1C1(AR[1]), ._6__1C0(AR[0]),
    ._7__Y1(n74153_1__7__y1), ._15__nG2(AL), ._14__A(AC[0]), ._13__2C3(1'b1), ._12__2C2(1'b0),
    ._11__2C1(1'b1), ._10__2C0(1'b0), ._9__Y2(n74153_1__9__y2));  // open: _8__GND, _16__Vcc
  _74153 u_74153_2 (
    ._1__nG1(AL), ._2__B(AC[4]), ._3__1C3(1'b1), ._4__1C2(1'b1), ._5__1C1(1'b0), ._6__1C0(1'b0),
    ._7__Y1(n74153_2__7__y1), ._15__nG2(1'b0), ._14__A(Bus[4]), ._13__2C3(AR[3]), ._12__2C2(AR[1]),
    ._11__2C1(AR[2]), ._10__2C0(AR[0]), ._9__Y2(n74153_2__9__y2));  // open: _8__GND, _16__Vcc
  _74153 u_74153_3 (
    ._1__nG1(1'b0), ._2__B(Bus[1]), ._3__1C3(AR[3]), ._4__1C2(AR[2]), ._5__1C1(AR[1]), ._6__1C0(AR[0]),
    ._7__Y1(n74153_3__7__y1), ._15__nG2(AL), ._14__A(AC[1]), ._13__2C3(1'b1), ._12__2C2(1'b0),
    ._11__2C1(1'b1), ._10__2C0(1'b0), ._9__Y2(n74153_3__9__y2));  // open: _8__GND, _16__Vcc
  _74153 u_74153_4 (
    ._1__nG1(AL), ._2__B(AC[5]), ._3__1C3(1'b1), ._4__1C2(1'b1), ._5__1C1(1'b0), ._6__1C0(1'b0),
    ._7__Y1(n74153_4__7__y1), ._15__nG2(1'b0), ._14__A(Bus[5]), ._13__2C3(AR[3]), ._12__2C2(AR[1]),
    ._11__2C1(AR[2]), ._10__2C0(AR[0]), ._9__Y2(n74153_4__9__y2));  // open: _8__GND, _16__Vcc
  _74153 u_74153_5 (
    ._1__nG1(1'b0), ._2__B(Bus[2]), ._3__1C3(AR[3]), ._4__1C2(AR[2]), ._5__1C1(AR[1]), ._6__1C0(AR[0]),
    ._7__Y1(n74153_5__7__y1), ._15__nG2(AL), ._14__A(AC[2]), ._13__2C3(1'b1), ._12__2C2(1'b0),
    ._11__2C1(1'b1), ._10__2C0(1'b0), ._9__Y2(n74153_5__9__y2));  // open: _8__GND, _16__Vcc
  _74153 u_74153_6 (
    ._1__nG1(AL), ._2__B(AC[6]), ._3__1C3(1'b1), ._4__1C2(1'b1), ._5__1C1(1'b0), ._6__1C0(1'b0),
    ._7__Y1(n74153_6__7__y1), ._15__nG2(1'b0), ._14__A(Bus[6]), ._13__2C3(AR[3]), ._12__2C2(AR[1]),
    ._11__2C1(AR[2]), ._10__2C0(AR[0]), ._9__Y2(n74153_6__9__y2));  // open: _8__GND, _16__Vcc
  _74153 u_74153_7 (
    ._1__nG1(1'b0), ._2__B(Bus[3]), ._3__1C3(AR[3]), ._4__1C2(AR[2]), ._5__1C1(AR[1]), ._6__1C0(AR[0]),
    ._7__Y1(n74153_7__7__y1), ._15__nG2(AL), ._14__A(AC[3]), ._13__2C3(1'b1), ._12__2C2(1'b0),
    ._11__2C1(1'b1), ._10__2C0(1'b0), ._9__Y2(n74153_7__9__y2));  // open: _8__GND, _16__Vcc
  _74153 u_74153_8 (
    ._1__nG1(AL), ._2__B(AC[7]), ._3__1C3(1'b1), ._4__1C2(1'b1), ._5__1C1(1'b0), ._6__1C0(1'b0),
    ._7__Y1(n74153_8__7__y1), ._15__nG2(1'b0), ._14__A(Bus[7]), ._13__2C3(AR[3]), ._12__2C2(AR[1]),
    ._11__2C1(AR[2]), ._10__2C0(AR[0]), ._9__Y2(n74153_8__9__y2));  // open: _8__GND, _16__Vcc
  _74283 u_74283_1 (
    ._1__S2(ALU[1]), ._2__B2(n74153_3__9__y2), ._3__A2(n74153_3__7__y1), ._4__S1(ALU[0]),
    ._5__A1(n74153_1__7__y1), ._6__B1(n74153_1__9__y2), ._7__C0(AR[0]), ._15__B3(n74153_5__9__y2),
    ._14__A3(n74153_5__7__y1), ._13__S3(ALU[2]), ._12__A4(n74153_7__7__y1), ._11__B4(n74153_7__9__y2),
    ._10__S4(ALU[3]), ._9__C4(n74283_1__9__c4));  // open: _8__GND, _16__Vcc
  _74283 u_74283_2 (
    ._1__S2(ALU[5]), ._2__B2(n74153_4__7__y1), ._3__A2(n74153_4__9__y2), ._4__S1(ALU[4]),
    ._5__A1(n74153_2__7__y1), ._6__B1(n74153_2__9__y2), ._7__C0(n74283_1__9__c4), ._15__B3(n74153_6__7__y1),
    ._14__A3(n74153_6__9__y2), ._13__S3(ALU[6]), ._12__A4(n74153_8__7__y1), ._11__B4(n74153_8__9__y2),
    ._10__S4(ALU[7]), ._9__C4(CO));  // open: _8__GND, _16__Vcc

  // Notes on the sheet:
  //   bit0
  //   bit4
  //   bit1
  //   bit5
  //   bit2
  //   bit6
  //   bit3
  //   bit7
endmodule

module ROM (
  input  [15:0] From_PC,
  output [7:0] To_IR,
  output [7:0] To_D
);

  ROM_part #(.addrWidth(16), .dataWidth(16)) rom_1 (.addr(From_PC), .data({To_D, To_IR}));  // open: sel

  // Notes on the sheet:
  //   contents of rom_1 (hex, n*v repeats v):
  //   0 fc2 10 1c4 1d 1c4 3 fa1 14f8 2 f11 5 7e 85 1e c6 f01 180 fc2 6fc 2
endmodule

module RAM (
  input  nWE,
  input  nOE,
  input  [14:0] Address,
  input  [7:0] Input,
  output [7:0] Output
);

  wire and_1_out, not_1_out;
  wire [7:0] ram_1_data;

  RAM_part #(.addrWidth(15), .bus("asynch")) ram_1 (.addr(Address), .data(ram_1_data), .ld(nWE));  // open: sel, clr
  assign ram_1_data = not_1_out ? Input : 8'bz;  // Controlled_Buffer controlled_buffer_1
  not not_1 (not_1_out, nWE);
  and and_1 (and_1_out, nWE, ~nOE);  // AND_Gate
  assign Output = and_1_out ? ram_1_data : 8'bz;  // Controlled_Buffer controlled_buffer_2
endmodule

// MAU
module MAU__Memory_Address_Unit (
  input  EL,
  input  EH,
  input  [7:0] Fropm_X,
  input  [7:0] From_D,
  input  [7:0] From_Y,
  output [14:0] To_RAM
);

  wire n74157_4__12__y4;

  _74157 u_74157_1 (
    ._1__S(EL), ._2__A1(Fropm_X[0]), ._3__B1(From_D[0]), ._4__Y1(To_RAM[0]), ._5__A2(Fropm_X[1]),
    ._6__B2(From_D[1]), ._7__Y2(To_RAM[1]), ._15__G(1'b0), ._14__A4(Fropm_X[3]), ._13__B4(From_D[3]),
    ._12__Y4(To_RAM[3]), ._11__A3(Fropm_X[2]), ._10__B3(From_D[2]), ._9__Y3(To_RAM[2]));  // open: _8__GND, _16__Vcc
  _74157 u_74157_2 (
    ._1__S(EL), ._2__A1(Fropm_X[4]), ._3__B1(From_D[4]), ._4__Y1(To_RAM[4]), ._5__A2(Fropm_X[5]),
    ._6__B2(From_D[5]), ._7__Y2(To_RAM[5]), ._15__G(1'b0), ._14__A4(Fropm_X[7]), ._13__B4(From_D[7]),
    ._12__Y4(To_RAM[7]), ._11__A3(Fropm_X[6]), ._10__B3(From_D[6]), ._9__Y3(To_RAM[6]));  // open: _8__GND, _16__Vcc
  _74157 u_74157_3 (
    ._1__S(1'b0), ._2__A1(From_Y[0]), ._3__B1(1'b1), ._4__Y1(To_RAM[8]), ._5__A2(From_Y[1]), ._6__B2(1'b1),
    ._7__Y2(To_RAM[9]), ._15__G(EH), ._14__A4(From_Y[3]), ._13__B4(1'b1), ._12__Y4(To_RAM[11]),
    ._11__A3(From_Y[2]), ._10__B3(1'b1), ._9__Y3(To_RAM[10]));  // open: _8__GND, _16__Vcc
  _74157 u_74157_4 (
    ._1__S(1'b0), ._2__A1(From_Y[4]), ._3__B1(1'b1), ._4__Y1(To_RAM[12]), ._5__A2(From_Y[5]), ._6__B2(1'b1),
    ._7__Y2(To_RAM[13]), ._15__G(EH), ._14__A4(From_Y[7]), ._13__B4(1'b1), ._12__Y4(n74157_4__12__y4),
    ._11__A3(From_Y[6]), ._10__B3(1'b1), ._9__Y3(To_RAM[14]));  // open: _8__GND, _16__Vcc
endmodule

// PC
module PC__Program_Counter (
  input  clk,
  input  nreset,
  input  nPL,
  input  nPH,
  input  [7:0] From_Bus,
  input  [7:0] From_Y,
  output [15:0] To_ROM
);

  wire n74161_1__15__tc, n74161_2__15__tc, n74161_3__15__tc;

  _74161 u_74161_1 (
    ._1__nMR(nreset), ._2__CP(clk), ._3__D0(From_Bus[0]), ._4__D1(From_Bus[1]), ._5__D2(From_Bus[2]),
    ._6__D3(From_Bus[3]), ._7__CEP(1'b1), ._15__TC(n74161_1__15__tc), ._14__Q0(To_ROM[0]),
    ._13__Q1(To_ROM[1]), ._12__Q2(To_ROM[2]), ._11__O3(To_ROM[3]), ._10__CET(1'b1), ._9__nPE(nPL));  // open: _8__GND, _16__Vcc
  _74161 u_74161_2 (
    ._1__nMR(nreset), ._2__CP(clk), ._3__D0(From_Bus[4]), ._4__D1(From_Bus[5]), ._5__D2(From_Bus[6]),
    ._6__D3(From_Bus[7]), ._7__CEP(1'b1), ._15__TC(n74161_2__15__tc), ._14__Q0(To_ROM[4]),
    ._13__Q1(To_ROM[5]), ._12__Q2(To_ROM[6]), ._11__O3(To_ROM[7]), ._10__CET(n74161_1__15__tc), ._9__nPE(nPL));  // open: _8__GND, _16__Vcc
  _74161 u_74161_3 (
    ._1__nMR(nreset), ._2__CP(clk), ._3__D0(From_Y[0]), ._4__D1(From_Y[1]), ._5__D2(From_Y[2]),
    ._6__D3(From_Y[3]), ._7__CEP(nPL), ._15__TC(n74161_3__15__tc), ._14__Q0(To_ROM[8]), ._13__Q1(To_ROM[9]),
    ._12__Q2(To_ROM[10]), ._11__O3(To_ROM[11]), ._10__CET(n74161_2__15__tc), ._9__nPE(nPH));  // open: _8__GND, _16__Vcc
  _74161 u_74161_4 (
    ._1__nMR(nreset), ._2__CP(clk), ._3__D0(From_Y[4]), ._4__D1(From_Y[5]), ._5__D2(From_Y[6]),
    ._6__D3(From_Y[7]), ._7__CEP(nPL), ._14__Q0(To_ROM[12]), ._13__Q1(To_ROM[13]), ._12__Q2(To_ROM[14]),
    ._11__O3(To_ROM[15]), ._10__CET(n74161_3__15__tc), ._9__nPE(nPH));  // open: _8__GND, _16__Vcc, _15__TC
endmodule

// IR
module IR__Instruction_register (
  input  CP,
  input  [7:0] D,
  output [7:0] Q
);

  _74273 u_74273_1 (
    ._1__nCLR(1'b1), ._2__Q0(Q[0]), ._3__D0(D[0]), ._4__D1(D[1]), ._5__Q1(Q[1]), ._6__Q2(Q[2]),
    ._7__D2(D[2]), ._8__D3(D[3]), ._9__Q3(Q[3]), ._19__Q7(Q[7]), ._18__D7(D[7]), ._17__D6(D[6]),
    ._16__Q6(Q[6]), ._15__Q5(Q[5]), ._14__D5(D[5]), ._13__D4(D[4]), ._12__Q4(Q[4]), ._11__CP(CP));  // open: _10__GND, _20__Vcc
endmodule

// D
module D__Data_register (
  input  CP,
  input  [7:0] D,
  output [7:0] Q
);

  _74273 u_74273_1 (
    ._1__nCLR(1'b1), ._2__Q0(Q[0]), ._3__D0(D[0]), ._4__D1(D[1]), ._5__Q1(Q[1]), ._6__Q2(Q[2]),
    ._7__D2(D[2]), ._8__D3(D[3]), ._9__Q3(Q[3]), ._19__Q7(Q[7]), ._18__D7(D[7]), ._17__D6(D[6]),
    ._16__Q6(Q[6]), ._15__Q5(Q[5]), ._14__D5(D[5]), ._13__D4(D[4]), ._12__Q4(Q[4]), ._11__CP(CP));  // open: _10__GND, _20__Vcc
endmodule

// AC register
module AC__Accumulator_register (
  input  CP,
  input  nE,
  input  [7:0] D,
  output [7:0] Q
);

  _74377 u_74377_1 (
    ._1__nE(nE), ._2__Q0(Q[0]), ._3__D0(D[0]), ._4__D1(D[1]), ._5__Q1(Q[1]), ._6__Q2(Q[2]), ._7__D2(D[2]),
    ._8__D3(D[3]), ._9__Q3(Q[3]), ._19__Q7(Q[7]), ._18__D7(D[7]), ._17__D6(D[6]), ._16__Q6(Q[6]),
    ._15__Q5(Q[5]), ._14__D5(D[5]), ._13__D4(D[4]), ._12__Q4(Q[4]), ._11__CP(CP));  // open: _10__GND, _20__Vcc
endmodule

// X
module X__X_register (
  input  CP,
  input  IX,
  input  nXL,
  input  [7:0] From_ALU,
  output [7:0] X_output
);

  wire n74161_1__15__tc;

  _74161 u_74161_1 (
    ._1__nMR(1'b1), ._2__CP(CP), ._3__D0(From_ALU[0]), ._4__D1(From_ALU[1]), ._5__D2(From_ALU[2]),
    ._6__D3(From_ALU[3]), ._7__CEP(IX), ._15__TC(n74161_1__15__tc), ._14__Q0(X_output[0]),
    ._13__Q1(X_output[1]), ._12__Q2(X_output[2]), ._11__O3(X_output[3]), ._10__CET(1'b1), ._9__nPE(nXL));  // open: _8__GND, _16__Vcc
  _74161 u_74161_2 (
    ._1__nMR(1'b1), ._2__CP(CP), ._3__D0(From_ALU[4]), ._4__D1(From_ALU[5]), ._5__D2(From_ALU[6]),
    ._6__D3(From_ALU[7]), ._7__CEP(IX), ._14__Q0(X_output[4]), ._13__Q1(X_output[5]), ._12__Q2(X_output[6]),
    ._11__O3(X_output[7]), ._10__CET(n74161_1__15__tc), ._9__nPE(nXL));  // open: _8__GND, _16__Vcc, _15__TC
endmodule

// Y
module Y__Y_register (
  input  CP,
  input  nE,
  input  [7:0] D,
  output [7:0] Q
);

  _74377 u_74377_1 (
    ._1__nE(nE), ._2__Q0(Q[0]), ._3__D0(D[0]), ._4__D1(D[1]), ._5__Q1(Q[1]), ._6__Q2(Q[2]), ._7__D2(D[2]),
    ._8__D3(D[3]), ._9__Q3(Q[3]), ._19__Q7(Q[7]), ._18__D7(D[7]), ._17__D6(D[6]), ._16__Q6(Q[6]),
    ._15__Q5(Q[5]), ._14__D5(D[5]), ._13__D4(D[4]), ._12__Q4(Q[4]), ._11__CP(CP));  // open: _10__GND, _20__Vcc
endmodule

// OUT
module OUT__Output_register (
  input  CP,
  input  nE,
  input  [7:0] D,
  output [7:0] Q
);

  _74377 u_74377_1 (
    ._1__nE(nE), ._2__Q0(Q[0]), ._3__D0(D[0]), ._4__D1(D[1]), ._5__Q1(Q[1]), ._6__Q2(Q[2]), ._7__D2(D[2]),
    ._8__D3(D[3]), ._9__Q3(Q[3]), ._19__Q7(Q[7]), ._18__D7(D[7]), ._17__D6(D[6]), ._16__Q6(Q[6]),
    ._15__Q5(Q[5]), ._14__D5(D[5]), ._13__D4(D[4]), ._12__Q4(Q[4]), ._11__CP(CP));  // open: _10__GND, _20__Vcc
endmodule

// XOUT
module XOUT__Extented_Output (
  input  CP,
  input  [7:0] D,
  output [7:0] Q
);

  _74273 u_74273_1 (
    ._1__nCLR(1'b1), ._2__Q0(Q[0]), ._3__D0(D[0]), ._4__D1(D[1]), ._5__Q1(Q[1]), ._6__Q2(Q[2]),
    ._7__D2(D[2]), ._8__D3(D[3]), ._9__Q3(Q[3]), ._19__Q7(Q[7]), ._18__D7(D[7]), ._17__D6(D[6]),
    ._16__Q6(Q[6]), ._15__Q5(Q[5]), ._14__D5(D[5]), ._13__D4(D[4]), ._12__Q4(Q[4]), ._11__CP(CP));  // open: _10__GND, _20__Vcc
endmodule

// BUS-D
module BUS_D__Tristate_Buffer (
  input  _1G,
  input  _2G,
  input  [7:0] D,
  output [7:0] Q
);

  _74244 u_74244_1 (
    ._1___1G(_1G), ._2__1A1(D[0]), ._3__2Y4(Q[7]), ._4__1A2(D[1]), ._5__2Y3(Q[6]), ._6__1A3(D[2]),
    ._7__2Y2(Q[5]), ._8__1A4(D[3]), ._9__2Y1(Q[4]), ._19___2G(_2G), ._18__1Y1(Q[0]), ._17__2A4(D[7]),
    ._16__1Y2(Q[1]), ._15__2A3(D[6]), ._14__1Y3(Q[2]), ._13__2A2(D[5]), ._12__1Y4(Q[3]), ._11__2A1(D[4]));  // open: _10__GND, _20__Vcc
endmodule

// BUS-AC
module BUS_AC__Tristate_Buffer (
  input  _1G,
  input  _2G,
  input  [7:0] D,
  output [7:0] Q
);

  _74244 u_74244_1 (
    ._1___1G(_1G), ._2__1A1(D[0]), ._3__2Y4(Q[7]), ._4__1A2(D[1]), ._5__2Y3(Q[6]), ._6__1A3(D[2]),
    ._7__2Y2(Q[5]), ._8__1A4(D[3]), ._9__2Y1(Q[4]), ._19___2G(_2G), ._18__1Y1(Q[0]), ._17__2A4(D[7]),
    ._16__1Y2(Q[1]), ._15__2A3(D[6]), ._14__1Y3(Q[2]), ._13__2A2(D[5]), ._12__1Y4(Q[3]), ._11__2A1(D[4]));  // open: _10__GND, _20__Vcc
endmodule

// BUS-IN
module BUS_IN__Shifter_8_bits (
  input  PCLK,
  input  CLK,
  input  nOE,
  input  SER_IN,
  output [7:0] out_5
);

  _74595 u_74595_1 (
    ._1__QB(out_5[1]), ._2__QC(out_5[2]), ._3__QD(out_5[3]), ._4__QE(out_5[4]), ._5__QF(out_5[5]),
    ._6__QG(out_5[6]), ._7__QH(out_5[7]), ._15__QA(out_5[0]), ._14__SER(SER_IN), ._13__nOE(nOE),
    ._12__RCLK(PCLK), ._11__SRCLK(CLK), ._10__nSRCLR(1'b1));  // open: _8__GND, _16__Vcc, _9__QH_prime
endmodule
