// Logisim project Gigatron.circ as structural Verilog: 21 circuits, main circuit Gigatron
module Gigatron (
  input  auto_clock_switch_manual,
  input  manual_clock,
  input  [14:0] memory_address,
  input  run__debug_mode_switch,
  input  [7:0] memory_data_inputs,
  input  Serial_Data,
  output Serial_Pulse,
  output Serial_Latch,
  output [7:0] to_DAC_VGA,
  output [3:0] To_Sound_R2R
);

  wire AC7, AE, AL, AR0, AR1, AR2, AR3, CLK1, CLK2, CO, DE, EH, EL, IE, IX, LD, OE, OL, PH, PL, RST,
       System_clock_out, WE, XL, YL;
  wire [3:0] controlled_buffer_1_out, controlled_buffer_1_out_2, register_8_bits_1_output,
       register_8_bits_1_output_2, register_x_1_output, XOUT_output;
  wire [6:0] register_8_bits_en_2_output;
  wire [7:0] alu_1_output, register_8_bits_2_output, register_8_bits_en_1_output;
  wire [7:4] register_x_1_output_2;
  wire [14:0] mau_memory_address_unit_1_composed_memory_address;
  wire [15:0] pc_program_counter_1_output, rom_1_data;

  Register_8_bits__en OUT (
    .\input (alu_1_output), .\output ({Serial_Latch, Serial_Pulse, to_DAC_VGA[5:0]}), .clk(CLK2), .Enable(OL));
  LED led_1 (.in(Serial_Latch));
  Hex_Digit_Display hex_digit_display_1 (.value(to_DAC_VGA[3:0]));  // open: dp
  Hex_Digit_Display hex_digit_display_2 (.value({Serial_Latch, Serial_Pulse, to_DAC_VGA[5:4]}));  // open: dp
  LED led_2 (.in(Serial_Pulse));
  LED led_3 (.in(to_DAC_VGA[5]));
  LED led_4 (.in(to_DAC_VGA[4]));
  LED led_5 (.in(to_DAC_VGA[3]));
  Hex_Digit_Display hex_digit_display_3 (.value(alu_1_output[7:4]));  // open: dp
  LED led_6 (.in(alu_1_output[7]));
  LED led_7 (.in(alu_1_output[6]));
  LED led_8 (.in(alu_1_output[5]));
  LED led_9 (.in(alu_1_output[4]));
  LED led_10 (.in(to_DAC_VGA[1]));
  LED led_11 (.in(to_DAC_VGA[2]));
  LED led_12 (.in(to_DAC_VGA[0]));
  PC__Program_Counter pc_program_counter_1 (
    .from_Y(register_8_bits_en_1_output), .\output (pc_program_counter_1_output), .PH(PH), .PL(PL),
    .from_Bus({controlled_buffer_1_out_2, controlled_buffer_1_out}), .CLK(CLK1), .reset(RST));
  Register_8_bits__en register_8_bits_en_1 (
    .\input (alu_1_output), .\output (register_8_bits_en_1_output), .clk(CLK2), .Enable(YL));
  Hex_Digit_Display hex_digit_display_4 (.value(alu_1_output[3:0]));  // open: dp
  LED led_13 (.in(alu_1_output[2]));
  LED led_14 (.in(alu_1_output[1]));
  LED led_15 (.in(alu_1_output[3]));
  LED led_16 (.in(alu_1_output[0]));
  Hex_Digit_Display hex_digit_display_5 (.value(pc_program_counter_1_output[11:8]));  // open: dp
  Hex_Digit_Display hex_digit_display_6 (.value(pc_program_counter_1_output[15:12]));  // open: dp
  LED led_17 (.in(pc_program_counter_1_output[15]));
  Hex_Digit_Display hex_digit_display_7 (.value(register_8_bits_en_1_output[7:4]));  // open: dp
  LED led_18 (.in(register_8_bits_en_1_output[6]));
  LED led_19 (.in(register_8_bits_en_1_output[7]));
  LED led_20 (.in(register_8_bits_en_1_output[5]));
  ALU alu_1 (
    .A({AC7, register_8_bits_en_2_output}), .B({controlled_buffer_1_out_2, controlled_buffer_1_out}),
    .Output(alu_1_output), .AR({AR3, AR2, AR1, AR0}), .CO(CO), .AL(AL));
  Hex_Digit_Display hex_digit_display_8 (.value(pc_program_counter_1_output[3:0]));  // open: dp
  Hex_Digit_Display hex_digit_display_9 (.value(pc_program_counter_1_output[7:4]));  // open: dp
  LED led_21 (.in(pc_program_counter_1_output[12]));
  LED led_22 (.in(pc_program_counter_1_output[14]));
  LED led_23 (.in(pc_program_counter_1_output[11]));
  LED led_24 (.in(pc_program_counter_1_output[13]));
  Hex_Digit_Display hex_digit_display_10 (.value(register_8_bits_en_1_output[3:0]));  // open: dp
  LED led_25 (.in(register_8_bits_en_1_output[2]));
  LED led_26 (.in(register_8_bits_en_1_output[3]));
  LED led_27 (.in(register_8_bits_en_1_output[1]));
  LED led_28 (.in(register_8_bits_en_1_output[4]));
  LED led_29 (.in(pc_program_counter_1_output[9]));
  LED led_30 (.in(pc_program_counter_1_output[8]));
  LED led_31 (.in(pc_program_counter_1_output[10]));
  LED led_32 (.in(register_8_bits_en_1_output[0]));
  Register_8_bits__en register_8_bits_en_2 (
    .\input (alu_1_output), .\output ({AC7, register_8_bits_en_2_output}), .clk(CLK2), .Enable(LD));
  LED led_33 (.in(pc_program_counter_1_output[6]));
  LED led_34 (.in(pc_program_counter_1_output[4]));
  LED led_35 (.in(pc_program_counter_1_output[5]));
  LED led_36 (.in(pc_program_counter_1_output[7]));
  Register_X register_x_1 (
    .Load_value(alu_1_output), .Output({register_x_1_output_2, register_x_1_output}), .Count_Enable(IX),
    .Load(XL), .CLK(CLK2));
  ROM #(.addrWidth(16), .dataWidth(16)) rom_1 (.addr(pc_program_counter_1_output), .data(rom_1_data));  // open: sel
  LED led_37 (.in(pc_program_counter_1_output[2]));
  LED led_38 (.in(pc_program_counter_1_output[0]));
  LED led_39 (.in(pc_program_counter_1_output[1]));
  LED led_40 (.in(pc_program_counter_1_output[3]));
  Hex_Digit_Display hex_digit_display_11 (.value({AC7, register_8_bits_en_2_output[6:4]}));  // open: dp
  LED led_41 (.in(register_8_bits_en_2_output[4]));
  LED led_42 (.in(register_8_bits_en_2_output[6]));
  LED led_43 (.in(AC7));
  LED led_44 (.in(register_8_bits_en_2_output[5]));
  LED led_45 (.in(register_x_1_output_2[6]));
  LED led_46 (.in(register_x_1_output_2[7]));
  Hex_Digit_Display hex_digit_display_12 (.value(register_8_bits_en_2_output[3:0]));  // open: dp
  LED led_47 (.in(register_8_bits_en_2_output[2]));
  LED led_48 (.in(register_8_bits_en_2_output[3]));
  LED led_49 (.in(register_8_bits_en_2_output[1]));
  LED led_50 (.in(register_8_bits_en_2_output[0]));
  Hex_Digit_Display hex_digit_display_13 (.value(register_x_1_output));  // open: dp
  Hex_Digit_Display hex_digit_display_14 (.value(register_x_1_output_2));  // open: dp
  LED led_51 (.in(register_x_1_output_2[5]));
  LED led_52 (.in(register_x_1_output[2]));
  LED led_53 (.in(register_x_1_output[3]));
  LED led_54 (.in(register_x_1_output_2[4]));
  Register_8_bits register_8_bits_1 (
    .Input(rom_1_data[7:0]), .Output({register_8_bits_1_output, register_8_bits_1_output_2}), .clk(CLK1));
  Register_8_bits register_8_bits_2 (.Input(rom_1_data[15:8]), .Output(register_8_bits_2_output), .clk(CLK1));
  LED led_55 (.in(register_x_1_output[1]));
  LED led_56 (.in(register_x_1_output[0]));
  Register_8_bits XOUT (
    .Input({AC7, register_8_bits_en_2_output}), .Output({To_Sound_R2R, XOUT_output}), .clk(Serial_Pulse));
  LED led_57 (.in(mau_memory_address_unit_1_composed_memory_address[14]));
  Hex_Digit_Display hex_digit_display_15 (.value(register_8_bits_1_output));  // open: dp
  LED led_58 (.in(register_8_bits_1_output[3]));
  LED led_59 (.in(register_8_bits_1_output[2]));
  LED led_60 (.in(register_8_bits_1_output[1]));
  LED led_61 (.in(register_8_bits_1_output[0]));
  Hex_Digit_Display hex_digit_display_16 (.value(register_8_bits_2_output[7:4]));  // open: dp
  LED led_62 (.in(register_8_bits_2_output[6]));
  LED led_63 (.in(register_8_bits_2_output[5]));
  LED led_64 (.in(register_8_bits_2_output[7]));
  LED led_65 (.in(register_8_bits_2_output[4]));
  MAU__Memory_Address_Unit mau_memory_address_unit_1 (
    .Composed_Memory_Address(mau_memory_address_unit_1_composed_memory_address), .High_Address(EH),
    .Low_Address(EL), .from_Y(register_8_bits_en_1_output),
    .from_X({register_x_1_output_2, register_x_1_output}), .from_D(register_8_bits_2_output));
  LED led_66 (.in(mau_memory_address_unit_1_composed_memory_address[13]));
  LED led_67 (.in(mau_memory_address_unit_1_composed_memory_address[12]));
  LED led_68 (.in(mau_memory_address_unit_1_composed_memory_address[10]));
  LED led_69 (.in(mau_memory_address_unit_1_composed_memory_address[11]));
  assign {controlled_buffer_1_out_2, controlled_buffer_1_out} = AE ? {AC7, register_8_bits_en_2_output} : 8'bz;  // Controlled_Buffer controlled_buffer_1
  Hex_Digit_Display hex_digit_display_17 (.value(register_8_bits_1_output_2));  // open: dp
  LED led_70 (.in(register_8_bits_1_output_2[0]));
  LED led_71 (.in(register_8_bits_1_output_2[2]));
  LED led_72 (.in(register_8_bits_1_output_2[3]));
  LED led_73 (.in(register_8_bits_1_output_2[1]));
  Hex_Digit_Display hex_digit_display_18 (.value(register_8_bits_2_output[3:0]));  // open: dp
  LED led_74 (.in(register_8_bits_2_output[0]));
  LED led_75 (.in(register_8_bits_2_output[1]));
  LED led_76 (.in(register_8_bits_2_output[2]));
  LED led_77 (.in(register_8_bits_2_output[3]));
  LED led_78 (.in(mau_memory_address_unit_1_composed_memory_address[7]));
  LED led_79 (.in(mau_memory_address_unit_1_composed_memory_address[8]));
  LED led_80 (.in(mau_memory_address_unit_1_composed_memory_address[9]));
  Hex_Digit_Display hex_digit_display_19 (.value({1'b0, mau_memory_address_unit_1_composed_memory_address[14:12]}));  // open: dp
  LED led_81 (.in(mau_memory_address_unit_1_composed_memory_address[6]));
  LED led_82 (.in(mau_memory_address_unit_1_composed_memory_address[5]));
  LED led_83 (.in(mau_memory_address_unit_1_composed_memory_address[3]));
  LED led_84 (.in(mau_memory_address_unit_1_composed_memory_address[4]));
  Hex_Digit_Display hex_digit_display_20 (.value(controlled_buffer_1_out_2));  // open: dp
  LED led_85 (.in(controlled_buffer_1_out_2[3]));
  LED led_86 (.in(controlled_buffer_1_out_2[2]));
  LED led_87 (.in(controlled_buffer_1_out_2[1]));
  LED led_88 (.in(XOUT_output[2]));
  LED led_89 (.in(XOUT_output[3]));
  Hex_Digit_Display hex_digit_display_21 (.value(mau_memory_address_unit_1_composed_memory_address[7:4]));  // open: dp
  Hex_Digit_Display hex_digit_display_22 (.value(mau_memory_address_unit_1_composed_memory_address[11:8]));  // open: dp
  LED led_90 (.in(mau_memory_address_unit_1_composed_memory_address[1]));
  LED led_91 (.in(mau_memory_address_unit_1_composed_memory_address[0]));
  LED led_92 (.in(mau_memory_address_unit_1_composed_memory_address[2]));
  Hex_Digit_Display hex_digit_display_23 (.value(controlled_buffer_1_out));  // open: dp
  LED led_93 (.in(controlled_buffer_1_out[1]));
  LED led_94 (.in(controlled_buffer_1_out[3]));
  LED led_95 (.in(controlled_buffer_1_out_2[0]));
  LED led_96 (.in(controlled_buffer_1_out[2]));
  LED led_97 (.in(XOUT_output[0]));
  LED led_98 (.in(XOUT_output[1]));
  assign {controlled_buffer_1_out_2, controlled_buffer_1_out} = DE ? register_8_bits_2_output : 8'bz;  // Controlled_Buffer controlled_buffer_2
  Hex_Digit_Display hex_digit_display_24 (.value(mau_memory_address_unit_1_composed_memory_address[3:0]));  // open: dp
  LED led_99 (.in(controlled_buffer_1_out[0]));
  CU__Control_Unit cu_control_unit_1 (
    .IR({register_8_bits_1_output, register_8_bits_1_output_2}), .DE(DE), .OE(OE), .AE(AE), .IE(IE), .XL(XL),
    .YL(YL), .IX(IX), .EH(EH), .EL(EL), .AL(AL), .AR0(AR0), .AR1(AR1), .AR2(AR2), .AR3(AR3), .OL(OL),
    .LD(LD), .PH(PH), .PL(PL), .AC7(AC7), .CO(CO), .clk(CLK1), .WE(WE));
  Memory memory_1 (
    .Memory_Address(mau_memory_address_unit_1_composed_memory_address),
    .Memory_Data_Input({controlled_buffer_1_out_2, controlled_buffer_1_out}),
    .Memory_Data_Output({controlled_buffer_1_out_2, controlled_buffer_1_out}), .Write_enable(WE),
    .Output_enable(OE), .programmable_address(memory_address), .progrmmable_data_inputs(memory_data_inputs),
    .run__debug_mode_switch(run__debug_mode_switch));
  LED u_OE (.in(OE));
  LED u_DE (.in(DE));
  LED u_AE (.in(AE));
  LED u_XL (.in(XL));
  LED u_IE (.in(IE));
  LED u_YL (.in(YL));
  Pull_Resistor #(.pull(1)) pull_resistor_1 (.node(Serial_Data));
  LED u_EH (.in(EH));
  LED u_IX (.in(IX));
  LED u_EL (.in(EL));
  Button Reset_Button (.out(RST));
  LED u_LD (.in(LD));
  LED u_OL (.in(OL));
  LED u_PL (.in(PL));
  Clock_part System_clock (.out(System_clock_out));
  Shifter_8_bits shifter_8_bits_1 (
    .Serial_input(Serial_Data), .Parallel_output({controlled_buffer_1_out_2, controlled_buffer_1_out}),
    .CLK(Serial_Pulse), .Output_enable(IE));  // open: Serial_output
  LED u_PH (.in(PH));
  LED u_AR0 (.in(AR0));
  LED u_AR1 (.in(AR1));
  LED u_AR3 (.in(AR3));
  LED u_AL (.in(AL));
  LED u_AR2 (.in(AR2));
  Clock clock_1 (
    .clk(System_clock_out), .switch(auto_clock_switch_manual), .manual(manual_clock), .clock_output(CLK1),
    .clock__output(CLK2));  // open: halt
  LED u_WE (.in(WE));

  assign to_DAC_VGA[7:6] = {Serial_Latch, Serial_Pulse};

  // Other names for the same wires on the sheet: HSync = Serial_Pulse; VSync = Serial_Latch

  // Notes on the sheet:
  //   Serial_Latch: pull=up
  //   Y
  //   ROM
  //   AC
  //   contents of rom_1 (hex, n*v repeats v):
  //   0 2c2 3 3c2 4c2 401 1a0 4c2 301 c2 401 1c2 0 2c2 101 19f0 2 1 281 2c2 101 1a0 1c2 efc 2 201 3c2 401
  //   1a0 5e4 2 301 1a 2
  //   X
  //   IR
  //   D
  //   Memory debugging
  //   allows direct memory changes
  //   BUS
  //   BUS
  //   BUS
  //   Control Panel
  //   Controller Port
endmodule

module Clock (
  input  clk,
  input  switch,
  input  manual,
  input  halt,
  output clock_output,
  output clock__output
);

  wire and_1_out, and_2_out, not_1_out, not_2_out, or_1_out;

  not not_1 (not_1_out, switch);
  not not_2 (not_2_out, halt);
  and and_1 (and_1_out, clk, switch);
  and and_2 (and_2_out, not_1_out, manual);
  or or_1 (or_1_out, and_1_out, and_2_out);
  and and_3 (clock_output, or_1_out, not_2_out);
  not not_3 (clock__output, clock_output);

  // Notes on the sheet:
  //   manual: pull=down
  //   halt: pull=down
endmodule

// CU
module CU__Control_Unit (
  input  clk,
  input  CO,
  input  AC7,
  input  [7:0] IR,
  output DE,
  output OE,
  output AE,
  output IE,
  output XL,
  output YL,
  output IX,
  output EH,
  output EL,
  output OL,
  output LD,
  output PL,
  output PH,
  output AR0,
  output AR1,
  output AR2,
  output AR3,
  output AL,
  output WE
);

  wire decoder_2_4_2_output_0, decoder_3_8_1_output_0, decoder_3_8_1_output_1, decoder_3_8_1_output_2,
       decoder_3_8_1_output_3, decoder_3_8_1_output_4, decoder_3_8_1_output_5, decoder_3_8_1_output_6,
       decoder_3_8_1_output_7, decoder_3_8_2_output_0, decoder_3_8_2_output_1, decoder_3_8_2_output_2,
       decoder_3_8_2_output_3, decoder_3_8_2_output_6, mux_4_1_1_output, not_1_out, not_2_out, or_5_out,
       or_6_out;

  Decoder_3_8 decoder_3_8_1 (
    .Input_2(IR[7]), .Input_1(IR[6]), .Input_0(IR[5]), .Output_0(decoder_3_8_1_output_0),
    .Output_1(decoder_3_8_1_output_1), .Output_2(decoder_3_8_1_output_2), .Output_3(decoder_3_8_1_output_3),
    .Output_4(decoder_3_8_1_output_4), .Output_5(decoder_3_8_1_output_5), .Output_6(decoder_3_8_1_output_6),
    .Output_7(decoder_3_8_1_output_7));  // open: Enable
  nor nor_1 (AL, decoder_3_8_1_output_0, decoder_3_8_1_output_1, decoder_3_8_1_output_2, decoder_3_8_1_output_3, decoder_3_8_1_output_7);
  Decoder_2_4 decoder_2_4_1 (
    .Input_1(IR[1]), .Input_0(IR[0]), .Output_0(DE), .Output_1(OE), .Output_2(AE), .Output_3(IE));  // open: Enable
  not not_1 (not_1_out, decoder_3_8_1_output_7);
  Decoder_3_8 decoder_3_8_2 (
    .Input_2(IR[4]), .Input_1(IR[3]), .Input_0(IR[2]), .Output_0(decoder_3_8_2_output_0),
    .Output_1(decoder_3_8_2_output_1), .Output_2(decoder_3_8_2_output_2), .Output_3(decoder_3_8_2_output_3),
    .Output_4(XL), .Output_5(YL), .Output_6(decoder_3_8_2_output_6), .Output_7(IX), .Enable(not_1_out));
  not not_2 (not_2_out, IR[4]);
  Decoder_2_4 decoder_2_4_2 (
    .Input_1(IR[3]), .Input_0(IR[2]), .Output_0(decoder_2_4_2_output_0), .Enable(not_2_out));  // open: Output_1, Output_2, Output_3
  or or_1 (AR0, decoder_3_8_1_output_5, decoder_3_8_1_output_7);
  or or_2 (AR1, decoder_3_8_1_output_2, decoder_3_8_1_output_3, decoder_3_8_1_output_5);
  or or_3 (AR2, decoder_3_8_1_output_0, decoder_3_8_1_output_2, decoder_3_8_1_output_3, decoder_3_8_1_output_4, decoder_3_8_1_output_7);
  Mux_4_1 mux_4_1_1 (
    .Input0(IR[2]), .Input1(IR[3]), .Input2(IR[4]), .Input3(1'b0), .Output(mux_4_1_1_output), .Select_1(CO),
    .Select_0(AC7), .Enable(decoder_3_8_1_output_7));
  or or_4 (AR3, decoder_3_8_1_output_0, decoder_3_8_1_output_1, decoder_3_8_1_output_2, decoder_3_8_1_output_4);
  or or_5 (or_5_out, decoder_3_8_2_output_0, decoder_3_8_2_output_1, decoder_3_8_2_output_2, decoder_3_8_2_output_3);
  or or_6 (or_6_out, decoder_3_8_2_output_6, IX);
  or or_7 (EL, decoder_3_8_2_output_1, decoder_3_8_2_output_3, IX);
  and and_1 (OL, or_6_out, ~decoder_3_8_1_output_6);  // AND_Gate
  and and_2 (LD, or_5_out, ~decoder_3_8_1_output_6);  // AND_Gate
  or or_8 (PL, mux_4_1_1_output, PH);
  and and_3 (PH, decoder_2_4_2_output_0, decoder_3_8_1_output_7);
  and and_4 (WE, decoder_3_8_1_output_6, ~clk);  // AND_Gate
  or or_9 (EH, decoder_3_8_2_output_2, decoder_3_8_2_output_3, IX);

  // Notes on the sheet:
  //   Instruction decoder
  //   LD
  //   AND
  //   OR
  //   XOR
  //   ADD
  //   SUB
  //   ST
  //   Bcc
  //   Bus access decoder
  //    greater
  //    less
  //    equal
  //   Mode decoder
  //   16 bits jump (JMP) decoder
  //   Condition detector
  //   [D],AC
  //   [X],AC
  //   [Y,D],AC
  //   [Y,X],AC
  //   [D],X
  //   [D],Y
  //   [D],OUT
  //   [Y,X++],OUT
  //   000=1
endmodule

module ALU (
  input  [3:0] AR,
  input  AL,
  input  [7:0] A,
  input  [7:0] B,
  output [7:0] Output,
  output CO
);

  wire adder_4_bits_1_cout;
  wire [3:0] mux_4_1_1_output, mux_4_1_2_output, mux_4_1_3_output, mux_4_1_4_output;

  Mux_4_1 mux_4_1_1 (
    .Input0(1'b0), .Input1(1'b1), .Input2(1'b0), .Input3(1'b1), .Output(mux_4_1_1_output[0]),
    .Select_1(B[0]), .Select_0(A[0]), .Enable(AL));
  Mux_4_1 mux_4_1_2 (
    .Input0(AR[0]), .Input1(AR[1]), .Input2(AR[2]), .Input3(AR[3]), .Output(mux_4_1_2_output[0]),
    .Select_1(B[0]), .Select_0(A[0]), .Enable(1'b1));
  Mux_4_1 mux_4_1_3 (
    .Input0(1'b0), .Input1(1'b1), .Input2(1'b0), .Input3(1'b1), .Output(mux_4_1_3_output[0]),
    .Select_1(B[4]), .Select_0(A[4]), .Enable(AL));
  Mux_4_1 mux_4_1_4 (
    .Input0(AR[0]), .Input1(AR[1]), .Input2(AR[2]), .Input3(AR[3]), .Output(mux_4_1_4_output[0]),
    .Select_1(B[4]), .Select_0(A[4]), .Enable(1'b1));
  Mux_4_1 mux_4_1_5 (
    .Input0(1'b0), .Input1(1'b1), .Input2(1'b0), .Input3(1'b1), .Output(mux_4_1_1_output[1]),
    .Select_1(B[1]), .Select_0(A[1]), .Enable(AL));
  Mux_4_1 mux_4_1_6 (
    .Input0(AR[0]), .Input1(AR[1]), .Input2(AR[2]), .Input3(AR[3]), .Output(mux_4_1_2_output[1]),
    .Select_1(B[1]), .Select_0(A[1]), .Enable(1'b1));
  Mux_4_1 mux_4_1_7 (
    .Input0(1'b0), .Input1(1'b1), .Input2(1'b0), .Input3(1'b1), .Output(mux_4_1_3_output[1]),
    .Select_1(B[5]), .Select_0(A[5]), .Enable(AL));
  Mux_4_1 mux_4_1_8 (
    .Input0(AR[0]), .Input1(AR[1]), .Input2(AR[2]), .Input3(AR[3]), .Output(mux_4_1_4_output[1]),
    .Select_1(B[5]), .Select_0(A[5]), .Enable(1'b1));
  Mux_4_1 mux_4_1_9 (
    .Input0(1'b0), .Input1(1'b1), .Input2(1'b0), .Input3(1'b1), .Output(mux_4_1_1_output[2]),
    .Select_1(B[2]), .Select_0(A[2]), .Enable(AL));
  Mux_4_1 mux_4_1_10 (
    .Input0(AR[0]), .Input1(AR[1]), .Input2(AR[2]), .Input3(AR[3]), .Output(mux_4_1_2_output[2]),
    .Select_1(B[2]), .Select_0(A[2]), .Enable(1'b1));
  Mux_4_1 mux_4_1_11 (
    .Input0(1'b0), .Input1(1'b1), .Input2(1'b0), .Input3(1'b1), .Output(mux_4_1_3_output[2]),
    .Select_1(B[6]), .Select_0(A[6]), .Enable(AL));
  Mux_4_1 mux_4_1_12 (
    .Input0(AR[0]), .Input1(AR[1]), .Input2(AR[2]), .Input3(AR[3]), .Output(mux_4_1_4_output[2]),
    .Select_1(B[6]), .Select_0(A[6]), .Enable(1'b1));
  Mux_4_1 mux_4_1_13 (
    .Input0(1'b0), .Input1(1'b1), .Input2(1'b0), .Input3(1'b1), .Output(mux_4_1_1_output[3]),
    .Select_1(B[3]), .Select_0(A[3]), .Enable(AL));
  Mux_4_1 mux_4_1_14 (
    .Input0(AR[0]), .Input1(AR[1]), .Input2(AR[2]), .Input3(AR[3]), .Output(mux_4_1_2_output[3]),
    .Select_1(B[3]), .Select_0(A[3]), .Enable(1'b1));
  Mux_4_1 mux_4_1_15 (
    .Input0(1'b0), .Input1(1'b1), .Input2(1'b0), .Input3(1'b1), .Output(mux_4_1_3_output[3]),
    .Select_1(B[7]), .Select_0(A[7]), .Enable(AL));
  Mux_4_1 mux_4_1_16 (
    .Input0(AR[0]), .Input1(AR[1]), .Input2(AR[2]), .Input3(AR[3]), .Output(mux_4_1_4_output[3]),
    .Select_1(B[7]), .Select_0(A[7]), .Enable(1'b1));
  Adder_4_bits adder_4_bits_1 (
    .A(mux_4_1_1_output), .B(mux_4_1_2_output), .Sum(Output[3:0]), .Cin(AR[0]), .Cout(adder_4_bits_1_cout));
  Adder_4_bits adder_4_bits_2 (
    .A(mux_4_1_3_output), .B(mux_4_1_4_output), .Sum(Output[7:4]), .Cin(adder_4_bits_1_cout), .Cout(CO));
endmodule

// PC
module PC__Program_Counter (
  input  PH,
  input  PL,
  input  CLK,
  input  reset,
  input  [7:0] from_Bus,
  input  [7:0] from_Y,
  output [15:0] \output 
);

  wire counter_8_bits_1_cout;

  Counter_8_bits counter_8_bits_1 (
    .Inputs(from_Bus), .Outputs(\output [7:0]), .Load(PL), .CLK(CLK), .Cout(counter_8_bits_1_cout),
    .reset(reset));  // open: Enable
  Counter_8_bits counter_8_bits_2 (
    .Inputs(from_Y), .Outputs(\output [15:8]), .Enable(counter_8_bits_1_cout), .Load(PH), .CLK(CLK),
    .reset(reset));  // open: Cout
endmodule

// MEMORY
module Memory (
  input  Write_enable,
  input  Output_enable,
  input  [14:0] Memory_Address,
  input  [7:0] Memory_Data_Input,
  input  [14:0] programmable_address,
  input  [7:0] progrmmable_data_inputs,
  input  run__debug_mode_switch,
  output [7:0] Memory_Data_Output
);

  wire not_1_out, or_1_out;
  wire [7:0] mux_2_1_x8_1_output, ram_1_uncontrolled_output_value;
  wire [14:0] mux_2_1_x15_1_output;

  LED led_1 (.in(Memory_Address[14]));
  LED led_2 (.in(Memory_Address[13]));
  LED led_3 (.in(Memory_Address[11]));
  LED led_4 (.in(Memory_Address[12]));
  LED led_5 (.in(Memory_Address[10]));
  Hex_Digit_Display hex_digit_display_1 (.value(Memory_Data_Input[7:4]));  // open: dp
  LED led_6 (.in(Memory_Address[6]));
  LED led_7 (.in(Memory_Address[9]));
  LED led_8 (.in(Memory_Address[8]));
  LED led_9 (.in(Memory_Address[7]));
  LED led_10 (.in(Memory_Data_Input[7]));
  Hex_Digit_Display hex_digit_display_2 (.value(Memory_Data_Input[3:0]));  // open: dp
  LED led_11 (.in(Memory_Address[4]));
  LED led_12 (.in(Memory_Address[3]));
  LED led_13 (.in(Memory_Address[5]));
  LED led_14 (.in(Memory_Address[2]));
  LED led_15 (.in(Memory_Data_Input[3]));
  LED led_16 (.in(Memory_Data_Input[4]));
  LED led_17 (.in(Memory_Data_Input[6]));
  LED led_18 (.in(Memory_Data_Input[5]));
  LED led_19 (.in(Memory_Address[0]));
  LED led_20 (.in(Memory_Address[1]));
  Hex_Digit_Display hex_digit_display_3 (.value({1'b0, Memory_Address[14:12]}));  // open: dp
  LED led_21 (.in(Memory_Data_Input[2]));
  LED led_22 (.in(Memory_Data_Input[0]));
  LED led_23 (.in(Memory_Data_Input[1]));
  Hex_Digit_Display hex_digit_display_4 (.value(Memory_Address[11:8]));  // open: dp
  Hex_Digit_Display hex_digit_display_5 (.value(Memory_Address[3:0]));  // open: dp
  Hex_Digit_Display hex_digit_display_6 (.value(Memory_Address[7:4]));  // open: dp
  Mux_2_1__x15 mux_2_1_x15_1 (
    .Input_0(Memory_Address), .Input_1(programmable_address), .Output(mux_2_1_x15_1_output),
    .Select(run__debug_mode_switch));
  Mux_2_1__x8 mux_2_1_x8_1 (
    .Input_0(Memory_Data_Input), .Input_1(progrmmable_data_inputs), .Output(mux_2_1_x8_1_output),
    .Select(run__debug_mode_switch));
  not not_1 (not_1_out, run__debug_mode_switch);
  LED run_mode_on (.in(not_1_out));
  LED programming_mode_on (.in(run__debug_mode_switch));
  or or_1 (or_1_out, run__debug_mode_switch, Write_enable);
  RAM ram_1 (
    .Addresse(mux_2_1_x15_1_output), .Input_Value(mux_2_1_x8_1_output),
    .Controlled_Output_Value(Memory_Data_Output),
    .Uncontrolled_Output_Value(ram_1_uncontrolled_output_value), .Write_Enable(or_1_out),
    .Output_Enable(Output_enable));
  Hex_Digit_Display hex_digit_display_7 (.value(ram_1_uncontrolled_output_value[3:0]));  // open: dp
  Hex_Digit_Display hex_digit_display_8 (.value(ram_1_uncontrolled_output_value[7:4]));  // open: dp
  LED led_24 (.in(ram_1_uncontrolled_output_value[6]));
  LED led_25 (.in(ram_1_uncontrolled_output_value[4]));
  LED led_26 (.in(ram_1_uncontrolled_output_value[5]));
  LED led_27 (.in(ram_1_uncontrolled_output_value[7]));
  LED led_28 (.in(ram_1_uncontrolled_output_value[3]));
  LED led_29 (.in(ram_1_uncontrolled_output_value[1]));
  LED led_30 (.in(ram_1_uncontrolled_output_value[0]));
  LED led_31 (.in(ram_1_uncontrolled_output_value[2]));

  // Notes on the sheet:
  //   run__debug_mode_switch: pull=down
  //   programmable_address: pull=down
  //   Memory_Data_Input: pull=down
  //   progrmmable_data_inputs: pull=down
  //   Notes :
  //   - The debug must be used while the execution is stopped
  //   - All the circuitry here are additionnal, used for debuging purposes
  //   - The debug mode allows to modify directly and easelly the RAM
endmodule

// MAU
module MAU__Memory_Address_Unit (
  input  High_Address,
  input  Low_Address,
  input  [7:0] from_D,
  input  [7:0] from_X,
  input  [7:0] from_Y,
  output [14:0] Composed_Memory_Address
);

  wire [7:7] mux_2_1_x8_2_output;

  Mux_2_1__x8 mux_2_1_x8_1 (
    .Input_0(from_D), .Input_1(from_X), .Output(Composed_Memory_Address[7:0]), .Select(Low_Address));
  Mux_2_1__x8 mux_2_1_x8_2 (
    .Input_0({8{1'b0}}), .Input_1(from_Y), .Output({mux_2_1_x8_2_output[7], Composed_Memory_Address[14:8]}),
    .Select(High_Address));
endmodule

module RAM (
  input  Write_Enable,
  input  Output_Enable,
  input  [14:0] Addresse,
  input  [7:0] Input_Value,
  output [7:0] Controlled_Output_Value,
  output [7:0] Uncontrolled_Output_Value
);

  wire and_1_out, not_1_out;

  assign Uncontrolled_Output_Value = Write_Enable ? Input_Value : 8'bz;  // Controlled_Buffer controlled_buffer_1
  RAM_part #(.addrWidth(15), .bus("asynch")) ram_1 (
    .addr(Addresse), .data(Uncontrolled_Output_Value), .sel(1'b1), .ld(not_1_out), .clr(1'b0));
  not not_1 (not_1_out, Write_Enable);
  and and_1 (and_1_out, not_1_out, Output_Enable);
  assign Controlled_Output_Value = and_1_out ? Uncontrolled_Output_Value : 8'bz;  // Controlled_Buffer controlled_buffer_2

  // Notes on the sheet:
  //   Notes :
  //   RAM
  //   - This memory mimic the HM62256 memory
  //   - The uncontrolled output port is fectif, used for debuging
  //   - We can't have on Logisim the same input/output port simultaneously, thus we separate them
endmodule

// Register
module Register_8_bits (
  input  clk,
  input  [7:0] Input,
  output [7:0] Output
);

  D_Flip_Flop d_ff_1 (.clk(clk), .D(Input[0]), .Q(Output[0]), .en(1'b1));  // open: Qn, preset, reset
  D_Flip_Flop d_ff_2 (.clk(clk), .D(Input[1]), .Q(Output[1]), .en(1'b1));  // open: Qn, preset, reset
  D_Flip_Flop d_ff_3 (.clk(clk), .D(Input[2]), .Q(Output[2]), .en(1'b1));  // open: Qn, preset, reset
  D_Flip_Flop d_ff_4 (.clk(clk), .D(Input[3]), .Q(Output[3]), .en(1'b1));  // open: Qn, preset, reset
  D_Flip_Flop d_ff_5 (.clk(clk), .D(Input[4]), .Q(Output[4]), .en(1'b1));  // open: Qn, preset, reset
  D_Flip_Flop d_ff_6 (.clk(clk), .D(Input[5]), .Q(Output[5]), .en(1'b1));  // open: Qn, preset, reset
  D_Flip_Flop d_ff_7 (.clk(clk), .D(Input[6]), .Q(Output[6]), .en(1'b1));  // open: Qn, preset, reset
  D_Flip_Flop d_ff_8 (.clk(clk), .D(Input[7]), .Q(Output[7]), .en(1'b1));  // open: Qn, preset, reset
endmodule

// Register
module Register_8_bits__en (
  input  clk,
  input  Enable,
  input  [7:0] \input ,
  output [7:0] \output 
);

  D_Flip_Flop d_ff_1 (.clk(clk), .D(\input [0]), .Q(\output [0]), .en(Enable));  // open: Qn, preset, reset
  D_Flip_Flop d_ff_2 (.clk(clk), .D(\input [1]), .Q(\output [1]), .en(Enable));  // open: Qn, preset, reset
  D_Flip_Flop d_ff_3 (.clk(clk), .D(\input [2]), .Q(\output [2]), .en(Enable));  // open: Qn, preset, reset
  D_Flip_Flop d_ff_4 (.clk(clk), .D(\input [3]), .Q(\output [3]), .en(Enable));  // open: Qn, preset, reset
  D_Flip_Flop d_ff_5 (.clk(clk), .D(\input [4]), .Q(\output [4]), .en(Enable));  // open: Qn, preset, reset
  D_Flip_Flop d_ff_6 (.clk(clk), .D(\input [5]), .Q(\output [5]), .en(Enable));  // open: Qn, preset, reset
  D_Flip_Flop d_ff_7 (.clk(clk), .D(\input [6]), .Q(\output [6]), .en(Enable));  // open: Qn, preset, reset
  D_Flip_Flop d_ff_8 (.clk(clk), .D(\input [7]), .Q(\output [7]), .en(Enable));  // open: Qn, preset, reset
endmodule

// Register
module Register_X (
  input  Count_Enable,
  input  Load,
  input  CLK,
  input  [7:0] Load_value,
  output [7:0] Output
);

  Counter_8_bits counter_8_bits_1 (
    .Inputs(Load_value), .Outputs(Output), .Enable(Count_Enable), .Load(Load), .CLK(CLK));  // open: Cout, reset
endmodule

module Counter_8_bits (
  input  Enable,
  input  Load,
  input  CLK,
  input  reset,
  input  [7:0] Inputs,
  output [7:0] Outputs,
  output Cout
);

  wire and_1_out, and_2_out, and_3_out, and_4_out, and_5_out, and_6_out, and_7_out, mux_2_1_1_output,
       mux_2_1_2_output, mux_2_1_3_output, mux_2_1_4_output, mux_2_1_5_output, mux_2_1_6_output,
       mux_2_1_7_output, mux_2_1_8_output, xor_1_out, xor_2_out, xor_3_out, xor_4_out, xor_5_out, xor_6_out,
       xor_7_out, xor_8_out;

  Mux_2_1 mux_2_1_1 (.Input_0(Enable), .Input_1(Inputs[0]), .Output(mux_2_1_1_output), .Select(Load));
  Mux_2_1 mux_2_1_2 (.Input_0(and_1_out), .Input_1(Inputs[1]), .Output(mux_2_1_2_output), .Select(Load));
  Mux_2_1 mux_2_1_3 (.Input_0(and_2_out), .Input_1(Inputs[2]), .Output(mux_2_1_3_output), .Select(Load));
  Mux_2_1 mux_2_1_4 (.Input_0(and_3_out), .Input_1(Inputs[3]), .Output(mux_2_1_4_output), .Select(Load));
  Mux_2_1 mux_2_1_5 (.Input_0(and_4_out), .Input_1(Inputs[4]), .Output(mux_2_1_5_output), .Select(Load));
  Mux_2_1 mux_2_1_6 (.Input_0(and_5_out), .Input_1(Inputs[5]), .Output(mux_2_1_6_output), .Select(Load));
  Mux_2_1 mux_2_1_7 (.Input_0(and_6_out), .Input_1(Inputs[6]), .Output(mux_2_1_7_output), .Select(Load));
  Mux_2_1 mux_2_1_8 (.Input_0(and_7_out), .Input_1(Inputs[7]), .Output(mux_2_1_8_output), .Select(Load));
  xor xor_1 (xor_1_out, Load, mux_2_1_1_output);
  xor xor_2 (xor_2_out, Load, mux_2_1_2_output);
  xor xor_3 (xor_3_out, Load, mux_2_1_3_output);
  xor xor_4 (xor_4_out, Load, mux_2_1_4_output);
  xor xor_5 (xor_5_out, Load, mux_2_1_5_output);
  xor xor_6 (xor_6_out, Load, mux_2_1_6_output);
  xor xor_7 (xor_7_out, Load, mux_2_1_7_output);
  xor xor_8 (xor_8_out, Load, mux_2_1_8_output);
  J_K_Flip_Flop j_k_ff_1 (
    .J(mux_2_1_1_output), .clk(CLK), .K(xor_1_out), .Q(Outputs[0]), .reset(reset));  // open: Qn, preset, en
  and and_1 (and_1_out, Outputs[0], Enable);
  J_K_Flip_Flop j_k_ff_2 (
    .J(mux_2_1_2_output), .clk(CLK), .K(xor_2_out), .Q(Outputs[1]), .reset(reset));  // open: Qn, preset, en
  and and_2 (and_2_out, Outputs[1], and_1_out);
  J_K_Flip_Flop j_k_ff_3 (
    .J(mux_2_1_3_output), .clk(CLK), .K(xor_3_out), .Q(Outputs[2]), .reset(reset));  // open: Qn, preset, en
  and and_3 (and_3_out, Outputs[2], and_2_out);
  J_K_Flip_Flop j_k_ff_4 (
    .J(mux_2_1_4_output), .clk(CLK), .K(xor_4_out), .Q(Outputs[3]), .reset(reset));  // open: Qn, preset, en
  and and_4 (and_4_out, Outputs[3], and_3_out);
  J_K_Flip_Flop j_k_ff_5 (
    .J(mux_2_1_5_output), .clk(CLK), .K(xor_5_out), .Q(Outputs[4]), .reset(reset));  // open: Qn, preset, en
  and and_5 (and_5_out, Outputs[4], and_4_out);
  J_K_Flip_Flop j_k_ff_6 (
    .J(mux_2_1_6_output), .clk(CLK), .K(xor_6_out), .Q(Outputs[5]), .reset(reset));  // open: Qn, preset, en
  and and_6 (and_6_out, Outputs[5], and_5_out);
  J_K_Flip_Flop j_k_ff_7 (
    .J(mux_2_1_7_output), .clk(CLK), .K(xor_7_out), .Q(Outputs[6]), .reset(reset));  // open: Qn, preset, en
  and and_7 (and_7_out, Outputs[6], and_6_out);
  J_K_Flip_Flop j_k_ff_8 (
    .J(mux_2_1_8_output), .clk(CLK), .K(xor_8_out), .Q(Outputs[7]), .reset(reset));  // open: Qn, preset, en
  and and_8 (Cout, Outputs[7], and_7_out);

  // Notes on the sheet:
  //   Enable: pull=up
endmodule

module Shifter_8_bits (
  input  CLK,
  input  Output_enable,
  input  Serial_input,
  output Serial_output,
  output [7:0] Parallel_output
);

  wire [6:0] d_ff_1_q;

  D_Flip_Flop d_ff_1 (.clk(CLK), .D(Serial_input), .Q(d_ff_1_q[0]));  // open: Qn, preset, en, reset
  D_Flip_Flop d_ff_2 (.clk(CLK), .D(d_ff_1_q[0]), .Q(d_ff_1_q[1]));  // open: Qn, preset, en, reset
  D_Flip_Flop d_ff_3 (.clk(CLK), .D(d_ff_1_q[1]), .Q(d_ff_1_q[2]));  // open: Qn, preset, en, reset
  D_Flip_Flop d_ff_4 (.clk(CLK), .D(d_ff_1_q[2]), .Q(d_ff_1_q[3]));  // open: Qn, preset, en, reset
  D_Flip_Flop d_ff_5 (.clk(CLK), .D(d_ff_1_q[3]), .Q(d_ff_1_q[4]));  // open: Qn, preset, en, reset
  D_Flip_Flop d_ff_6 (.clk(CLK), .D(d_ff_1_q[4]), .Q(d_ff_1_q[5]));  // open: Qn, preset, en, reset
  D_Flip_Flop d_ff_7 (.clk(CLK), .D(d_ff_1_q[5]), .Q(d_ff_1_q[6]));  // open: Qn, preset, en, reset
  D_Flip_Flop d_ff_8 (.clk(CLK), .D(d_ff_1_q[6]), .Q(Serial_output));  // open: Qn, preset, en, reset
  assign Parallel_output = Output_enable ? {Serial_output, d_ff_1_q} : 8'bz;  // Controlled_Buffer controlled_buffer_1
endmodule

module Adder_4_bits (
  input  Cin,
  input  [3:0] A,
  input  [3:0] B,
  output [3:0] Sum,
  output Cout
);

  wire fulladder_1_cout, fulladder_2_cout, fulladder_3_cout;

  FullAdder fulladder_1 (.A(A[0]), .B(B[0]), .S(Sum[0]), .Cin(Cin), .Cout(fulladder_1_cout));
  FullAdder fulladder_2 (.A(A[1]), .B(B[1]), .S(Sum[1]), .Cin(fulladder_1_cout), .Cout(fulladder_2_cout));
  FullAdder fulladder_3 (.A(A[2]), .B(B[2]), .S(Sum[2]), .Cin(fulladder_2_cout), .Cout(fulladder_3_cout));
  FullAdder fulladder_4 (.A(A[3]), .B(B[3]), .S(Sum[3]), .Cin(fulladder_3_cout), .Cout(Cout));
endmodule

// Full Adder
module FullAdder (
  input  Cin,
  input  A,
  input  B,
  output S,
  output Cout
);

  wire and_1_out, and_2_out, and_3_out;

  xor xor_1 (S, A, B, Cin);
  and and_1 (and_1_out, A, B);
  and and_2 (and_2_out, A, Cin);
  and and_3 (and_3_out, B, Cin);
  or or_1 (Cout, and_1_out, and_2_out, and_3_out);
endmodule

module Mux_4_1 (
  input  Select_1,
  input  Select_0,
  input  Input0,
  input  Input1,
  input  Input2,
  input  Input3,
  input  Enable,
  output Output
);

  wire and_1_out, and_2_out, and_3_out, and_4_out, not_1_out, not_2_out, or_1_out;

  not not_1 (not_1_out, Select_1);
  not not_2 (not_2_out, Select_0);
  and and_1 (and_1_out, not_2_out, not_1_out, Input0);
  and and_2 (and_2_out, not_1_out, Select_0, Input1);
  and and_3 (and_3_out, not_2_out, Select_1, Input2);
  and and_4 (and_4_out, Select_0, Select_1, Input3);
  or or_1 (or_1_out, and_1_out, and_2_out, and_3_out, and_4_out);
  and and_5 (Output, or_1_out, Enable);

  // Notes on the sheet:
  //   Enable: pull=up
endmodule

// Mux 2-1
module Mux_2_1__x15 (
  input  Select,
  input  [14:0] Input_0,
  input  [14:0] Input_1,
  output [14:0] Output
);

  wire [14:0] and_1_out, and_2_out;
  wire [14:14] not_1_out;

  not not_1 (not_1_out[14], Select);
  assign and_1_out = {15{Select}} & Input_1;  // AND_Gate and_1, 15 bits wide
  assign and_2_out = {15{not_1_out[14]}} & Input_0;  // AND_Gate and_2, 15 bits wide
  assign Output = and_2_out | and_1_out;  // OR_Gate or_1, 15 bits wide
endmodule

// Mux 2-1
module Mux_2_1__x8 (
  input  Select,
  input  [7:0] Input_0,
  input  [7:0] Input_1,
  output [7:0] Output
);

  wire [7:0] and_1_out, and_2_out;
  wire [7:7] not_1_out;

  not not_1 (not_1_out[7], Select);
  assign and_1_out = {8{not_1_out[7]}} & Input_0;  // AND_Gate and_1, 8 bits wide
  assign and_2_out = {8{Select}} & Input_1;  // AND_Gate and_2, 8 bits wide
  assign Output = and_1_out | and_2_out;  // OR_Gate or_1, 8 bits wide
endmodule

module Mux_2_1 (
  input  Select,
  input  Input_0,
  input  Input_1,
  output Output
);

  wire and_1_out, and_2_out, not_1_out;

  not not_1 (not_1_out, Select);
  and and_1 (and_1_out, not_1_out, Input_0);
  and and_2 (and_2_out, Select, Input_1);
  or or_1 (Output, and_1_out, and_2_out);
endmodule

module Decoder_3_8 (
  input  Enable,
  input  Input_2,
  input  Input_1,
  input  Input_0,
  output Output_0,
  output Output_1,
  output Output_2,
  output Output_3,
  output Output_4,
  output Output_5,
  output Output_6,
  output Output_7
);

  and and_1 (Output_0, ~Input_2, ~Input_1, ~Input_0, Enable);  // AND_Gate
  and and_2 (Output_1, ~Input_2, ~Input_1, Input_0, Enable);  // AND_Gate
  and and_3 (Output_2, ~Input_2, Input_1, ~Input_0, Enable);  // AND_Gate
  and and_4 (Output_3, ~Input_2, Input_1, Input_0, Enable);  // AND_Gate
  and and_5 (Output_4, Input_2, ~Input_1, ~Input_0, Enable);  // AND_Gate
  and and_6 (Output_5, Input_2, ~Input_1, Input_0, Enable);  // AND_Gate
  and and_7 (Output_6, Input_2, Input_1, ~Input_0, Enable);  // AND_Gate
  and and_8 (Output_7, Input_2, Input_1, Input_0, Enable);

  // Notes on the sheet:
  //   Enable: pull=up
endmodule

module Decoder_2_4 (
  input  Enable,
  input  Input_1,
  input  Input_0,
  output Output_0,
  output Output_1,
  output Output_2,
  output Output_3
);

  and and_1 (Output_0, ~Input_1, Enable, ~Input_0);  // AND_Gate
  and and_2 (Output_1, ~Input_1, Enable, Input_0);  // AND_Gate
  and and_3 (Output_2, Input_1, Enable, ~Input_0);  // AND_Gate
  and and_4 (Output_3, Input_1, Enable, Input_0);

  // Notes on the sheet:
  //   Enable: pull=up
endmodule
