// Logisim project Keyboard.circ as structural Verilog: 1 circuit, main circuit Keyboard
module Keyboard (
  input  in_1,
  input  in_2,
  input  in_3,
  input  Strobe,
  input  nOutput_Enable,
  output Int,
  output [7:0] \output 
);

  wire button_1_out, button_2_out, button_3_out, button_4_out, button_5_out, button_6_out, button_7_out,
       button_8_out, button_9_out, button_10_out, button_11_out, button_12_out, button_13_out, button_14_out,
       button_15_out, button_16_out, button_17_out, button_18_out, button_19_out, button_20_out,
       button_21_out, button_22_out, button_23_out, button_24_out, button_25_out, button_26_out,
       button_27_out, button_28_out, button_29_out, button_30_out, button_31_out, button_32_out,
       button_33_out, button_34_out, button_35_out, button_36_out, button_37_out, button_38_out,
       button_39_out, button_40_out, button_41_out, button_42_out, button_43_out, button_44_out,
       button_45_out, button_46_out, button_47_out, button_48_out, button_49_out, button_50_out,
       button_51_out, button_52_out, button_53_out, n74138_1__7__y7, n74138_1__9__y6, n74138_1__10__y5,
       n74138_1__11__y4, n74138_1__12__y3, n74138_1__13__y2, n74138_1__14__y1, n74138_1__15__y0,
       n74161_1__12__q2, n74161_1__13__q1, n74161_1__14__q0, n74273_1__2__q0, n74273_1__5__q1,
       n74273_1__6__q2, n74273_1__9__q3, n74273_1__12__q4, n74273_1__15__q5, n74273_1__16__q6,
       n74273_1__19__q7;

  _74161 u_74161_1 (
    ._1__nMR(1'b1), ._2__CP(Strobe), ._7__CEP(1'b1), ._14__Q0(n74161_1__14__q0), ._13__Q1(n74161_1__13__q1),
    ._12__Q2(n74161_1__12__q2), ._10__CET(1'b1), ._9__nPE(1'b1));  // open: _3__D0, _4__D1, _5__D2, _6__D3, _8__GND, _16__Vcc, _15__TC, _11__O3
  _74138 u_74138_1 (
    ._1__A(n74161_1__14__q0), ._2__B(n74161_1__13__q1), ._3__C(n74161_1__12__q2), ._4__G2A(1'b0),
    ._5__G2B(1'b0), ._6__G1(1'b1), ._7__Y7(n74138_1__7__y7), ._15__Y0(n74138_1__15__y0),
    ._14__Y1(n74138_1__14__y1), ._13__Y2(n74138_1__13__y2), ._12__Y3(n74138_1__12__y3),
    ._11__Y4(n74138_1__11__y4), ._10__Y5(n74138_1__10__y5), ._9__Y6(n74138_1__9__y6));  // open: _8__GND, _16__Vcc
  Pull_Resistor #(.pull(1)) pull_resistor_1 (.node(n74138_1__7__y7));
  Button button_1 (.out(button_1_out));
  Transistor #(.\type ("n")) transistor_1 (.in(n74138_1__15__y0), .out(n74138_1__7__y7), .gate(button_1_out));
  Button button_2 (.out(button_2_out));
  Transistor #(.\type ("n")) transistor_2 (.in(n74138_1__14__y1), .out(n74138_1__7__y7), .gate(button_2_out));
  Button button_3 (.out(button_3_out));
  Transistor #(.\type ("n")) transistor_3 (.in(n74138_1__13__y2), .out(n74138_1__7__y7), .gate(button_3_out));
  Button button_4 (.out(button_4_out));
  Transistor #(.\type ("n")) transistor_4 (.in(n74138_1__12__y3), .out(n74138_1__7__y7), .gate(button_4_out));
  Button button_5 (.out(button_5_out));
  Transistor #(.\type ("n")) transistor_5 (.in(n74138_1__11__y4), .out(n74138_1__7__y7), .gate(button_5_out));
  Button button_6 (.out(button_6_out));
  Transistor #(.\type ("n")) transistor_6 (.in(n74138_1__10__y5), .out(n74138_1__7__y7), .gate(button_6_out));
  Button button_7 (.out(button_7_out));
  Transistor #(.\type ("n")) transistor_7 (.in(n74138_1__9__y6), .out(n74138_1__7__y7), .gate(button_7_out));
  Pull_Resistor #(.pull(1)) pull_resistor_2 (.node(n74138_1__7__y7));
  Button button_8 (.out(button_8_out));
  Transistor #(.\type ("n")) transistor_8 (.in(n74138_1__15__y0), .out(n74138_1__7__y7), .gate(in_1));
  Button button_9 (.out(button_9_out));
  Transistor #(.\type ("n")) transistor_9 (.in(n74138_1__14__y1), .out(n74138_1__7__y7), .gate(in_2));
  Button button_10 (.out(button_10_out));
  Button button_11 (.out(button_11_out));
  Transistor #(.\type ("n")) transistor_10 (.in(n74138_1__13__y2), .out(n74138_1__7__y7), .gate(button_11_out));
  Button button_12 (.out(button_12_out));
  Button button_13 (.out(button_13_out));
  Transistor #(.\type ("n")) transistor_11 (.in(n74138_1__12__y3), .out(n74138_1__7__y7), .gate(button_12_out));
  Button button_14 (.out(button_14_out));
  Button button_15 (.out(button_15_out));
  Transistor #(.\type ("n")) transistor_12 (.in(n74138_1__11__y4), .out(n74138_1__7__y7), .gate(button_14_out));
  Button button_16 (.out(button_16_out));
  Button button_17 (.out(button_17_out));
  Transistor #(.\type ("n")) transistor_13 (.in(n74138_1__10__y5), .out(n74138_1__7__y7), .gate(button_17_out));
  Button button_18 (.out(button_18_out));
  Button button_19 (.out(button_19_out));
  Transistor #(.\type ("n")) transistor_14 (.in(n74138_1__9__y6), .out(n74138_1__7__y7), .gate(button_19_out));
  Pull_Resistor #(.pull(1)) pull_resistor_3 (.node(n74138_1__7__y7));
  Button button_20 (.out(button_20_out));
  Transistor #(.\type ("n")) transistor_15 (.in(n74138_1__15__y0), .out(n74138_1__7__y7), .gate(button_20_out));
  Transistor #(.\type ("n")) transistor_16 (.in(n74138_1__15__y0), .out(n74138_1__7__y7), .gate(button_8_out));
  Button button_21 (.out(button_21_out));
  Transistor #(.\type ("n")) transistor_17 (.in(n74138_1__14__y1), .out(n74138_1__7__y7), .gate(button_21_out));
  Transistor #(.\type ("n")) transistor_18 (.in(n74138_1__14__y1), .out(n74138_1__7__y7), .gate(button_9_out));
  Button button_22 (.out(button_22_out));
  Transistor #(.\type ("n")) transistor_19 (.in(n74138_1__13__y2), .out(n74138_1__7__y7), .gate(button_22_out));
  Transistor #(.\type ("n")) transistor_20 (.in(n74138_1__13__y2), .out(n74138_1__7__y7), .gate(button_10_out));
  Button button_23 (.out(button_23_out));
  Transistor #(.\type ("n")) transistor_21 (.in(n74138_1__12__y3), .out(n74138_1__7__y7), .gate(button_23_out));
  Transistor #(.\type ("n")) transistor_22 (.in(n74138_1__12__y3), .out(n74138_1__7__y7), .gate(button_13_out));
  Button button_24 (.out(button_24_out));
  Transistor #(.\type ("n")) transistor_23 (.in(n74138_1__11__y4), .out(n74138_1__7__y7), .gate(button_15_out));
  Transistor #(.\type ("n")) transistor_24 (.in(n74138_1__11__y4), .out(n74138_1__7__y7), .gate(button_24_out));
  Button button_25 (.out(button_25_out));
  Transistor #(.\type ("n")) transistor_25 (.in(n74138_1__10__y5), .out(n74138_1__7__y7), .gate(button_25_out));
  Transistor #(.\type ("n")) transistor_26 (.in(n74138_1__10__y5), .out(n74138_1__7__y7), .gate(button_16_out));
  Button button_26 (.out(button_26_out));
  Transistor #(.\type ("n")) transistor_27 (.in(n74138_1__9__y6), .out(n74138_1__7__y7), .gate(button_18_out));
  Transistor #(.\type ("n")) transistor_28 (.in(n74138_1__9__y6), .out(n74138_1__7__y7), .gate(button_26_out));
  _7430 u_7430_1 (
    ._1__1A(n74138_1__7__y7), ._2__1B(n74138_1__7__y7), ._3__1C(n74138_1__7__y7), ._4__1D(n74138_1__7__y7),
    ._5__1E(n74138_1__7__y7), ._6__1F(n74138_1__7__y7), ._12__1H(n74138_1__7__y7), ._11__1G(n74138_1__7__y7),
    ._8__3Y(Int));  // open: _7__GND, _14__Vcc, _13__NC, _10__NC, _9__NC
  Pull_Resistor #(.pull(1)) pull_resistor_4 (.node(n74138_1__7__y7));
  Pull_Resistor #(.pull(1)) pull_resistor_5 (.node(n74138_1__7__y7));
  Button button_27 (.out(button_27_out));
  Transistor #(.\type ("n")) transistor_29 (.in(n74138_1__15__y0), .out(n74138_1__7__y7), .gate(button_27_out));
  Transistor #(.\type ("n")) transistor_30 (.in(n74138_1__14__y1), .out(n74138_1__7__y7), .gate(in_3));
  Button button_28 (.out(button_28_out));
  Transistor #(.\type ("n")) transistor_31 (.in(n74138_1__13__y2), .out(n74138_1__7__y7), .gate(button_28_out));
  Button button_29 (.out(button_29_out));
  Transistor #(.\type ("n")) transistor_32 (.in(n74138_1__12__y3), .out(n74138_1__7__y7), .gate(button_29_out));
  Button button_30 (.out(button_30_out));
  Transistor #(.\type ("n")) transistor_33 (.in(n74138_1__11__y4), .out(n74138_1__7__y7), .gate(button_30_out));
  Button button_31 (.out(button_31_out));
  Transistor #(.\type ("n")) transistor_34 (.in(n74138_1__10__y5), .out(n74138_1__7__y7), .gate(button_31_out));
  Button button_32 (.out(button_32_out));
  Transistor #(.\type ("n")) transistor_35 (.in(n74138_1__9__y6), .out(n74138_1__7__y7), .gate(button_32_out));
  _74273 u_74273_1 (
    ._2__Q0(n74273_1__2__q0), ._3__D0(n74138_1__7__y7), ._4__D1(n74138_1__7__y7), ._5__Q1(n74273_1__5__q1),
    ._6__Q2(n74273_1__6__q2), ._7__D2(n74138_1__7__y7), ._8__D3(n74138_1__7__y7), ._9__Q3(n74273_1__9__q3),
    ._19__Q7(n74273_1__19__q7), ._18__D7(n74138_1__7__y7), ._17__D6(n74138_1__7__y7),
    ._16__Q6(n74273_1__16__q6), ._15__Q5(n74273_1__15__q5), ._14__D5(n74138_1__7__y7),
    ._13__D4(n74138_1__7__y7), ._12__Q4(n74273_1__12__q4), ._11__CP(Strobe));  // open: _1__nCLR, _10__GND, _20__Vcc
  _74240 u_74240_1 (
    ._1___1G(nOutput_Enable), ._2__1A1(n74273_1__2__q0), ._3__2Y4(\output [7]), ._4__1A2(n74273_1__5__q1),
    ._5__2Y3(\output [6]), ._6__1A3(n74273_1__6__q2), ._7__2Y2(\output [5]), ._8__1A4(n74273_1__9__q3),
    ._9__2Y1(\output [4]), ._19___2G(nOutput_Enable), ._18__1Y1(\output [0]), ._17__2A4(n74273_1__19__q7),
    ._16__1Y2(\output [1]), ._15__2A3(n74273_1__16__q6), ._14__1Y3(\output [2]), ._13__2A2(n74273_1__15__q5),
    ._12__1Y4(\output [3]), ._11__2A1(n74273_1__12__q4));  // open: _10__GND, _20__Vcc
  Pull_Resistor #(.pull(1)) pull_resistor_6 (.node(n74138_1__7__y7));
  Button button_33 (.out(button_33_out));
  Button button_34 (.out(button_34_out));
  Transistor #(.\type ("n")) transistor_36 (.in(n74138_1__15__y0), .out(n74138_1__7__y7), .gate(button_33_out));
  Button button_35 (.out(button_35_out));
  Button button_36 (.out(button_36_out));
  Transistor #(.\type ("n")) transistor_37 (.in(n74138_1__14__y1), .out(n74138_1__7__y7), .gate(button_36_out));
  Button button_37 (.out(button_37_out));
  Button button_38 (.out(button_38_out));
  Transistor #(.\type ("n")) transistor_38 (.in(n74138_1__13__y2), .out(n74138_1__7__y7), .gate(button_38_out));
  Button button_39 (.out(button_39_out));
  Button button_40 (.out(button_40_out));
  Transistor #(.\type ("n")) transistor_39 (.in(n74138_1__12__y3), .out(n74138_1__7__y7), .gate(button_39_out));
  Button button_41 (.out(button_41_out));
  Button button_42 (.out(button_42_out));
  Transistor #(.\type ("n")) transistor_40 (.in(n74138_1__11__y4), .out(n74138_1__7__y7), .gate(button_42_out));
  Button button_43 (.out(button_43_out));
  Button button_44 (.out(button_44_out));
  Transistor #(.\type ("n")) transistor_41 (.in(n74138_1__10__y5), .out(n74138_1__7__y7), .gate(button_43_out));
  Button button_45 (.out(button_45_out));
  Button button_46 (.out(button_46_out));
  Transistor #(.\type ("n")) transistor_42 (.in(n74138_1__9__y6), .out(n74138_1__7__y7), .gate(button_45_out));
  Pull_Resistor #(.pull(1)) pull_resistor_7 (.node(n74138_1__7__y7));
  Button button_47 (.out(button_47_out));
  Transistor #(.\type ("n")) transistor_43 (.in(n74138_1__15__y0), .out(n74138_1__7__y7), .gate(button_47_out));
  Transistor #(.\type ("n")) transistor_44 (.in(n74138_1__15__y0), .out(n74138_1__7__y7), .gate(button_34_out));
  Button button_48 (.out(button_48_out));
  Transistor #(.\type ("n")) transistor_45 (.in(n74138_1__14__y1), .out(n74138_1__7__y7), .gate(button_48_out));
  Transistor #(.\type ("n")) transistor_46 (.in(n74138_1__14__y1), .out(n74138_1__7__y7), .gate(button_35_out));
  Button button_49 (.out(button_49_out));
  Transistor #(.\type ("n")) transistor_47 (.in(n74138_1__13__y2), .out(n74138_1__7__y7), .gate(button_49_out));
  Transistor #(.\type ("n")) transistor_48 (.in(n74138_1__13__y2), .out(n74138_1__7__y7), .gate(button_37_out));
  Button button_50 (.out(button_50_out));
  Transistor #(.\type ("n")) transistor_49 (.in(n74138_1__12__y3), .out(n74138_1__7__y7), .gate(button_40_out));
  Transistor #(.\type ("n")) transistor_50 (.in(n74138_1__12__y3), .out(n74138_1__7__y7), .gate(button_50_out));
  Button button_51 (.out(button_51_out));
  Transistor #(.\type ("n")) transistor_51 (.in(n74138_1__11__y4), .out(n74138_1__7__y7), .gate(button_41_out));
  Transistor #(.\type ("n")) transistor_52 (.in(n74138_1__11__y4), .out(n74138_1__7__y7), .gate(button_51_out));
  Button button_52 (.out(button_52_out));
  Transistor #(.\type ("n")) transistor_53 (.in(n74138_1__10__y5), .out(n74138_1__7__y7), .gate(button_52_out));
  Transistor #(.\type ("n")) transistor_54 (.in(n74138_1__10__y5), .out(n74138_1__7__y7), .gate(button_44_out));
  Button button_53 (.out(button_53_out));
  Transistor #(.\type ("n")) transistor_55 (.in(n74138_1__9__y6), .out(n74138_1__7__y7), .gate(button_46_out));
  Transistor #(.\type ("n")) transistor_56 (.in(n74138_1__9__y6), .out(n74138_1__7__y7), .gate(button_53_out));
  Pull_Resistor #(.pull(1)) pull_resistor_8 (.node(n74138_1__7__y7));
endmodule
