// Logisim project Megatron TTL.circ as structural Verilog: 25 circuits, main circuit Megatron TTL
module Megatron_TTL (
  input  auto_clock_switch_manual,
  input  manual_clock
);

  wire A_B, AC7, CLK1, CLK2, Cn, EH, EL, IX, M, nAE, nCE, nDE, nIE, nIE1, nIE2, nIE3, nIE4, nIO, nLD, nOE,
       nOL, nOW1, nOW2, nOW3, nOW4, nPC1, nPC2, nPC3, nPC4, nPC5, nPC6, nPC7, nPC8, nPH, nPL, nRST, nWE, nXL,
       nYL, Reset_Button_out, S0, S1, S2, S3, System_clock_out;
  wire [2:0] ac_accumulator_register_1_q, mau_memory_address_unit_1_to_ram_2;
  wire [3:0] ac_accumulator_register_1_q_2, ioc_input_output_control_register_1_peripherals,
       ioc_input_output_control_register_1_peripherals_2, mau_memory_address_unit_1_to_ram,
       pc_program_counter_1_to_rom, x_x_register_1_x_output, x_x_register_1_x_output_2;
  wire [7:0] alu_1_alu, bus_ac_tristate_buffer_1_q, mau_memory_address_unit_1_to_ram_3,
       out_output_register_1_q, rom_1_to_d, rom_1_to_ir, y_y_register_1_q;
  wire [11:0] pc_program_counter_1_to_rom_2;

  Hex_Digit_Display hex_digit_display_1 (.value(y_y_register_1_q[7:4]));  // open: dp
  LED led_1 (.in(y_y_register_1_q[5]));
  LED led_2 (.in(y_y_register_1_q[7]));
  LED led_3 (.in(y_y_register_1_q[6]));
  Hex_Digit_Display hex_digit_display_2 (.value(alu_1_alu[7:4]));  // open: dp
  LED led_4 (.in(alu_1_alu[7]));
  LED led_5 (.in(alu_1_alu[6]));
  LED led_6 (.in(alu_1_alu[5]));
  OUT__Output_register out_output_register_1 (.D(alu_1_alu), .Q(out_output_register_1_q), .CP(CLK2), .nE(nOW1));
  Hex_Digit_Display hex_digit_display_3 (.value(y_y_register_1_q[3:0]));  // open: dp
  LED led_7 (.in(y_y_register_1_q[2]));
  LED led_8 (.in(y_y_register_1_q[4]));
  LED led_9 (.in(y_y_register_1_q[1]));
  LED led_10 (.in(y_y_register_1_q[3]));
  Hex_Digit_Display hex_digit_display_4 (.value(alu_1_alu[3:0]));  // open: dp
  LED led_11 (.in(alu_1_alu[3]));
  LED led_12 (.in(alu_1_alu[2]));
  LED led_13 (.in(alu_1_alu[4]));
  LED led_14 (.in(alu_1_alu[1]));
  Hex_Digit_Display hex_digit_display_5 (.value(out_output_register_1_q[7:4]));  // open: dp
  LED led_15 (.in(out_output_register_1_q[4]));
  LED led_16 (.in(out_output_register_1_q[6]));
  LED led_17 (.in(out_output_register_1_q[7]));
  LED led_18 (.in(out_output_register_1_q[5]));
  LED led_19 (.in(y_y_register_1_q[0]));
  LED led_20 (.in(alu_1_alu[0]));
  Hex_Digit_Display hex_digit_display_6 (.value(out_output_register_1_q[3:0]));  // open: dp
  LED led_21 (.in(out_output_register_1_q[0]));
  LED led_22 (.in(out_output_register_1_q[2]));
  LED led_23 (.in(out_output_register_1_q[1]));
  LED led_24 (.in(out_output_register_1_q[3]));
  Hex_Digit_Display hex_digit_display_7 (.value(pc_program_counter_1_to_rom));  // open: dp
  Hex_Digit_Display hex_digit_display_8 (.value(pc_program_counter_1_to_rom_2[7:4]));  // open: dp
  Hex_Digit_Display hex_digit_display_9 (.value(pc_program_counter_1_to_rom_2[11:8]));  // open: dp
  PC__Program_Counter pc_program_counter_1 (
    .From_Bus(bus_ac_tristate_buffer_1_q), .From_Y(y_y_register_1_q),
    .To_ROM({pc_program_counter_1_to_rom, pc_program_counter_1_to_rom_2}), .clk(CLK1), .nreset(nRST),
    .nPL(nPL), .nPH(nPH));
  Hex_Digit_Display hex_digit_display_10 (.value(pc_program_counter_1_to_rom_2[3:0]));  // open: dp
  Y__Y_register y_y_register_1 (.D(alu_1_alu), .Q(y_y_register_1_q), .CP(CLK2), .nE(nYL));
  X__X_register x_x_register_1 (
    .From_ALU(alu_1_alu), .X_output({x_x_register_1_x_output, x_x_register_1_x_output_2}), .CP(CLK2),
    .IX(IX), .nXL(nXL));
  ALU alu_1 (
    .AC({AC7, ac_accumulator_register_1_q, ac_accumulator_register_1_q_2}), .Bus(bus_ac_tristate_buffer_1_q),
    .ALU(alu_1_alu), .Cn(Cn), .S({S3, S2, S1, S0}), .M(M), .A_B(A_B));
  IOC__Input_Output_Control_register ioc_input_output_control_register_1 (
    .ALU(alu_1_alu),
    .peripherals({ioc_input_output_control_register_1_peripherals, ioc_input_output_control_register_1_peripherals_2}),
    .CP(CLK2), .nE(nIO));
  ROM rom_1 (
    .From_PC({pc_program_counter_1_to_rom, pc_program_counter_1_to_rom_2}), .To_IR(rom_1_to_ir),
    .To_D(rom_1_to_d));
  Hex_Digit_Display hex_digit_display_11 (.value(x_x_register_1_x_output));  // open: dp
  LED led_25 (.in(x_x_register_1_x_output[1]));
  LED led_26 (.in(x_x_register_1_x_output[2]));
  LED led_27 (.in(x_x_register_1_x_output[3]));
  Clock_part System_clock (.out(System_clock_out));
  Pull_Resistor #(.pull(1)) pull_resistor_1 (.node(nRST));
  Button Reset_Button (.out(Reset_Button_out));
  not not_1 (nRST, Reset_Button_out);
  Hex_Digit_Display hex_digit_display_12 (.value(rom_1_to_d[7:4]));  // open: dp
  Hex_Digit_Display hex_digit_display_13 (.value(x_x_register_1_x_output_2));  // open: dp
  LED led_28 (.in(x_x_register_1_x_output_2[2]));
  LED led_29 (.in(x_x_register_1_x_output[0]));
  LED led_30 (.in(x_x_register_1_x_output_2[1]));
  LED led_31 (.in(x_x_register_1_x_output_2[3]));
  LED led_32 (.in(ioc_input_output_control_register_1_peripherals[3]));
  LED led_33 (.in(ioc_input_output_control_register_1_peripherals[2]));
  Clock clock_1 (
    .clk(System_clock_out), .switch(auto_clock_switch_manual), .manual(manual_clock), .clock_output(CLK1),
    .clock__output(CLK2));  // open: halt
  Hex_Digit_Display hex_digit_display_14 (.value(rom_1_to_d[3:0]));  // open: dp
  LED led_34 (.in(x_x_register_1_x_output_2[0]));
  AC__Accumulator_register ac_accumulator_register_1 (
    .D(alu_1_alu), .Q({AC7, ac_accumulator_register_1_q, ac_accumulator_register_1_q_2}), .CP(CLK2), .nE(nLD));
  Hex_Digit_Display hex_digit_display_15 (.value(ioc_input_output_control_register_1_peripherals));  // open: dp
  Hex_Digit_Display hex_digit_display_16 (.value(ioc_input_output_control_register_1_peripherals_2));  // open: dp
  LED led_35 (.in(ioc_input_output_control_register_1_peripherals_2[2]));
  LED led_36 (.in(ioc_input_output_control_register_1_peripherals[0]));
  LED led_37 (.in(ioc_input_output_control_register_1_peripherals_2[3]));
  LED led_38 (.in(ioc_input_output_control_register_1_peripherals[1]));
  Hex_Digit_Display hex_digit_display_17 (.value(rom_1_to_ir[7:4]));  // open: dp
  MAU__Memory_Address_Unit mau_memory_address_unit_1 (
    .Fropm_X({x_x_register_1_x_output, x_x_register_1_x_output_2}), .From_D(rom_1_to_d),
    .From_Y(y_y_register_1_q),
    .To_RAM({mau_memory_address_unit_1_to_ram_2, mau_memory_address_unit_1_to_ram, mau_memory_address_unit_1_to_ram_3}),
    .EL(EL), .EH(EH));
  LED led_39 (.in(ioc_input_output_control_register_1_peripherals_2[1]));
  LED led_40 (.in(ioc_input_output_control_register_1_peripherals_2[0]));
  Hex_Digit_Display hex_digit_display_18 (.value(rom_1_to_ir[3:0]));  // open: dp
  Hex_Digit_Display hex_digit_display_19 (.value({1'b0, mau_memory_address_unit_1_to_ram_2}));  // open: dp
  Hex_Digit_Display hex_digit_display_20 (.value(mau_memory_address_unit_1_to_ram));  // open: dp
  Hex_Digit_Display hex_digit_display_21 (.value(mau_memory_address_unit_1_to_ram_3[7:4]));  // open: dp
  Hex_Digit_Display hex_digit_display_22 (.value(mau_memory_address_unit_1_to_ram_3[3:0]));  // open: dp
  Hex_Digit_Display hex_digit_display_23 (.value({AC7, ac_accumulator_register_1_q}));  // open: dp
  LED led_41 (.in(ac_accumulator_register_1_q[2]));
  LED led_42 (.in(AC7));
  LED led_43 (.in(ac_accumulator_register_1_q[1]));
  BUS_AC__Tristate_Buffer bus_ac_tristate_buffer_1 (
    .D({AC7, ac_accumulator_register_1_q, ac_accumulator_register_1_q_2}), .Q(bus_ac_tristate_buffer_1_q),
    ._1G(nAE), ._2G(nAE));
  IOU__Input_Ouput_Unit iou_input_ouput_unit_1 (
    .from_input_output_control_register({ioc_input_output_control_register_1_peripherals, ioc_input_output_control_register_1_peripherals_2}),
    .nIE1__input_enable_1(nIE1), .nIE2__input_enable_2(nIE2), .nIE3__input_enable_3(nIE3),
    .nIE4__input_enable_4(nIE4), .nOW1__output_write_1(nOW1), .nOW2__output_write_2(nOW2),
    .nOW3__output_write_3(nOW3), .nOW4__output_write_4(nOW4), .nPC1__peripheral_control_1(nPC1),
    .nPC2__peripheral_control_2(nPC2), .nPC3__peripheral_control_3(nPC3), .nPC4__peripheral_control_4(nPC4),
    .nPC5__peripheral_control_5(nPC5), .nPC6__peripheral_control_6(nPC6), .nPC7__peripheral_control_7(nPC7),
    .nPC8__peripheral_control_8(nPC8), .nIE(nIE), .nOL(nOL), .nCSE(nCE));
  CU__Control_Unit cu_control_unit_1 (
    .From_IR(rom_1_to_ir), .nIE(nIE), .nAE(nAE), .nOE(nOE), .nDE(nDE), .nXL(nXL), .nYL(nYL), .IX(IX),
    .nWE(nWE), .nCE(nCE), .nIO(nIO), .nOL(nOL), .nLD(nLD), .nPH(nPH), .A_B(A_B), .AC7(AC7), .CLK1(CLK1),
    .nPL(nPL), .EL(EL), .S3(S3), .S2(S2), .S1(S1), .S0(S0), .M(M), .Cn(Cn), .EH(EH));
  BUS_D__Tristate_Buffer bus_d_tristate_buffer_1 (.D(rom_1_to_d), .Q(bus_ac_tristate_buffer_1_q), ._1G(nDE), ._2G(nDE));
  RAM ram_1 (
    .Address({mau_memory_address_unit_1_to_ram_2, mau_memory_address_unit_1_to_ram, mau_memory_address_unit_1_to_ram_3}),
    .Output(bus_ac_tristate_buffer_1_q), .Input(bus_ac_tristate_buffer_1_q), .nWE(nWE), .nOE(nOE));
  Hex_Digit_Display hex_digit_display_24 (.value(ac_accumulator_register_1_q_2));  // open: dp
  LED led_44 (.in(ac_accumulator_register_1_q_2[1]));
  LED led_45 (.in(ac_accumulator_register_1_q_2[3]));
  LED led_46 (.in(ac_accumulator_register_1_q[0]));
  LED led_47 (.in(ac_accumulator_register_1_q_2[2]));
  LED led_48 (.in(ac_accumulator_register_1_q_2[0]));
  LED led_49 (.in(bus_ac_tristate_buffer_1_q[6]));
  LED led_50 (.in(bus_ac_tristate_buffer_1_q[7]));
  Hex_Digit_Display hex_digit_display_25 (.value(bus_ac_tristate_buffer_1_q[3:0]));  // open: dp
  Hex_Digit_Display hex_digit_display_26 (.value(bus_ac_tristate_buffer_1_q[7:4]));  // open: dp
  LED led_51 (.in(bus_ac_tristate_buffer_1_q[4]));
  LED led_52 (.in(bus_ac_tristate_buffer_1_q[3]));
  LED led_53 (.in(bus_ac_tristate_buffer_1_q[2]));
  LED led_54 (.in(bus_ac_tristate_buffer_1_q[5]));
  LED led_55 (.in(bus_ac_tristate_buffer_1_q[0]));
  LED led_56 (.in(bus_ac_tristate_buffer_1_q[1]));
  KEYBOARD_IN__Shifter_8_bits keyboard_in_shifter_8_bits_1 (
    .out_5(bus_ac_tristate_buffer_1_q), .PCLK(nPC1), .CLK(CLK2), .nOE(nIE1));  // open: SER_IN
  GAMEPAD_IN__Shifter_8_bits gamepad_in_shifter_8_bits_1 (
    .out_5(bus_ac_tristate_buffer_1_q), .PCLK(nPC2), .CLK(CLK2), .nOE(nIE2));  // open: SER_IN

  // Notes on the sheet:
  //   Control Panel
  //   Control Enable
endmodule

module Clock (
  input  clk,
  input  switch,
  input  manual,
  input  halt,
  output clock_output,
  output clock__output
);

  wire and_1_out, and_2_out, not_1_out, not_2_out, or_1_out;

  not not_1 (not_1_out, switch);
  not not_2 (not_2_out, halt);
  and and_1 (and_1_out, clk, switch);
  and and_2 (and_2_out, not_1_out, manual);
  or or_1 (or_1_out, and_1_out, and_2_out);
  and and_3 (clock_output, or_1_out, not_2_out);
  not not_3 (clock__output, clock_output);

  // Notes on the sheet:
  //   halt: pull=down
  //   manual: pull=down
endmodule

// CU
module CU__Control_Unit (
  input  CLK1,
  input  A_B,
  input  AC7,
  input  [7:0] From_IR,
  output nIE,
  output nAE,
  output nOE,
  output nDE,
  output EH,
  output EL,
  output nWE,
  output nCE,
  output nXL,
  output nYL,
  output IX,
  output nIO,
  output nOL,
  output nLD,
  output nPH,
  output nPL,
  output S3,
  output S2,
  output S1,
  output S0,
  output M,
  output Cn
);

  wire cu_datapath_rom_1__12__o1;

  CU_DataPath_ROM cu_datapath_rom_1 (
    ._1__A15(1'b0), ._2__A12(1'b0), ._3__A7(From_IR[7]), ._4__A6(From_IR[6]), ._5__A5(From_IR[5]),
    ._6__A4(From_IR[4]), ._7__A3(From_IR[3]), ._8__A2(From_IR[2]), ._9__A1(From_IR[1]), ._10__A0(From_IR[0]),
    ._11__O0(nCE), ._12__O1(cu_datapath_rom_1__12__o1), ._13__O2(EL), ._27__A14(1'b0), ._26__A13(1'b0),
    ._25__A8(AC7), ._24__A9(A_B), ._23__A11(1'b0), ._22__nOE_Vpp(1'b0), ._21__A10(1'b0), ._20__nCE(1'b0),
    ._19__O7(nIE), ._18__O6(nAE), ._17__O5(nOE), ._16__O4(nDE), ._15__O3(EH));  // open: _14__GND, _28__Vcc
  CU_Registers_ROM cu_registers_rom_1 (
    ._1__A15(1'b0), ._2__A12(1'b0), ._3__A7(From_IR[7]), ._4__A6(From_IR[6]), ._5__A5(From_IR[5]),
    ._6__A4(From_IR[4]), ._7__A3(From_IR[3]), ._8__A2(From_IR[2]), ._9__A1(From_IR[1]), ._10__A0(From_IR[0]),
    ._11__O0(nPL), ._12__O1(nPH), ._13__O2(nLD), ._27__A14(1'b0), ._26__A13(1'b0), ._25__A8(AC7),
    ._24__A9(A_B), ._23__A11(1'b0), ._22__nOE_Vpp(1'b0), ._21__A10(1'b0), ._20__nCE(1'b0), ._19__O7(nXL),
    ._18__O6(nYL), ._17__O5(IX), ._16__O4(nIO), ._15__O3(nOL));  // open: _14__GND, _28__Vcc
  CU_ALU_ROM cu_alu_rom_1 (
    ._1__A15(1'b0), ._2__A12(1'b0), ._3__A7(From_IR[7]), ._4__A6(From_IR[6]), ._5__A5(From_IR[5]),
    ._6__A4(From_IR[4]), ._7__A3(From_IR[3]), ._8__A2(From_IR[2]), ._9__A1(From_IR[1]), ._10__A0(From_IR[0]),
    ._13__O2(Cn), ._27__A14(1'b0), ._26__A13(1'b0), ._25__A8(AC7), ._24__A9(A_B), ._23__A11(1'b0),
    ._22__nOE_Vpp(1'b0), ._21__A10(1'b0), ._20__nCE(1'b0), ._19__O7(S3), ._18__O6(S2), ._17__O5(S1),
    ._16__O4(S0), ._15__O3(M));  // open: _11__O0, _12__O1, _14__GND, _28__Vcc
  or or_1 (nWE, cu_datapath_rom_1__12__o1, CLK1);

  // Notes on the sheet:
  //   A_B: pull=down
  //   To BUS
  //   To memory
  //   To IOC register
  //   To PC
  //   To ALU
  //   To memory address unit
  //   To input outputl unit
  //   To user registers
  //   To user registers
endmodule

// 27C512
module CU_DataPath_ROM (
  input  _1__A15,
  input  _28__Vcc,
  input  _2__A12,
  input  _27__A14,
  input  _3__A7,
  input  _26__A13,
  input  _4__A6,
  input  _25__A8,
  input  _5__A5,
  input  _24__A9,
  input  _6__A4,
  input  _23__A11,
  input  _7__A3,
  input  _22__nOE_Vpp,
  input  _8__A2,
  input  _21__A10,
  input  _9__A1,
  input  _20__nCE,
  input  _10__A0,
  input  _14__GND,
  output _19__O7,
  output _11__O0,
  output _18__O6,
  output _12__O1,
  output _17__O5,
  output _13__O2,
  output _16__O4,
  output _15__O3
);

  wire not_1_out;
  wire [7:0] rom_1_data;

  not not_1 (not_1_out, _22__nOE_Vpp);
  ROM_part #(.addrWidth(16)) rom_1 (
    .addr({_1__A15, _27__A14, _26__A13, _2__A12, _23__A11, _21__A10, _24__A9, _25__A8, _3__A7, _4__A6, _5__A5, _6__A4, _7__A3, _8__A2, _9__A1, _10__A0}),
    .data(rom_1_data));  // open: sel
  assign {_19__O7, _18__O6, _17__O5, _16__O4, _15__O3, _13__O2, _12__O1, _11__O0} = not_1_out ? rom_1_data : 8'bz;  // Controlled_Buffer controlled_buffer_1

  // Notes on the sheet:
  //   27C512: 64K x 8-bit EPROM 
  //   contents of rom_1 (hex, n*v repeats v):
  //   ef df bf 7f eb db bb 7b e7 d7 b7 77 e3 d3 b3 73 ef df bf 7f ef df bf 7f ef df bf 7f e3 d3 b3 73 ef
  //   df bf 7f eb db bb 7b e7 d7 b7 77 e3 d3 b3 73 ef df bf 7f ef df bf 7f ef df bf 7f e3 d3 b3 73 ef df
  //   bf 7f eb db bb 7b e7 d7 b7 77 e3 d3 b3 73 ef df bf 7f ef df bf 7f ef df bf 7f e3 d3 b3 73 ef df bf
  //   7f eb db bb 7b e7 d7 b7 77 e3 d3 b3 73 ef df bf 7f ef df bf 7f ef df bf 7f e3 d3 b3 73 ef df bf 7f
  //   eb db bb 7b e7 d7 b7 77 e3 d3 b3 73 ef df bf 7f ef df bf 7f ef df bf 7f e3 d3 b3 73 ef df bf 7f eb
  //   db bb 7b e7 d7 b7 77 e3 d3 b3 73 ef df bf 7f ef df bf 7f ef df bf 7f e3 d3 b3 73 ed df bd 7d e9 db
  //   b9 79 e5 d7 b5 75 e1 d3 b1 71 ef df bf 7f ef df bf 7f ef df bf 7f ef df bf 7f ef df bf 7f ef df bf
  //   7f ef df bf 7f ef df bf 7f ef df bf 7f ef df bf 7f ef df bf 7f ef df bf 7f ef df bf 7f eb db bb 7b
  //   e7 d7 b7 77 e3 d3 b3 73 ef df bf 7f ef df bf 7f ef df bf 7f e3 d3 b3 73 ef df bf 7f eb db bb 7b e7
  //   d7 b7 77 e3 d3 b3 73 ef df bf 7f ef df bf 7f ef df bf 7f e3 d3 b3 73 ef df bf 7f eb db bb 7b e7 d7
  //   b7 77 e3 d3 b3 73 ef df bf 7f ef df bf 7f ef df bf 7f e3 d3 b3 73 ef df bf 7f eb db bb 7b e7 d7 b7
  //   77 e3 d3 b3 73 ef df bf 7f ef df bf 7f ef df bf 7f e3 d3 b3 73 ef df bf 7f eb db bb 7b e7 d7 b7 77
  //   e3 d3 b3 73 ef df bf 7f ef df bf 7f ef df bf 7f e3 d3 b3 73 ef df bf 7f eb db bb 7b e7 d7 b7 77 e3
  //   d3 b3 73 ef df bf 7f ef df bf 7f ef df bf 7f e3 d3 b3 73 ed df bd 7d e9 db b9 79 e5 d7 b5 75 e1 d3
  //   b1 71 ed ef bd 7d ed ee bd 7d ed bf bd 7d e1 7f b1 71 ef df bf 7f ef df bf 7f ef df bf 7f ef df bf
  //   7f ef df bf 7f ef df bf 7f ef df bf 7f ef df bf 7f ef df bf 7f eb db bb 7b e7 d7 b7 77 e3 d3 b3 73
  //   ef df bf 7f ef df bf 7f ef df bf 7f e3 d3 b3 73 ef df bf 7f eb db bb 7b e7 d7 b7 77 e3 d3 b3 73 ef
  //   df bf 7f ef df bf 7f ef df bf 7f e3 d3 b3 73 ef df bf 7f eb db bb 7b e7 d7 b7 77 e3 d3 b3 73 ef df
  //   bf 7f ef df bf 7f ef df bf 7f e3 d3 b3 73 ef df bf 7f eb db bb 7b e7 d7 b7 77 e3 d3 b3 73 ef df bf
  //   7f ef df bf 7f ef df bf 7f e3 d3 b3 73 ef df bf 7f eb db bb 7b e7 d7 b7 77 e3 d3 b3 73 ef df bf 7f
  //   ef df bf 7f ef df bf 7f e3 d3 b3 73 ef df bf 7f eb db bb 7b e7 d7 b7 77 e3 d3 b3 73 ef df bf 7f ef
  //   df bf 7f ef df bf 7f e3 d3 b3 73 ed df bd 7d e9 db b9 79 e5 d7 b5 75 e1 d3 b1 71 ed ef bd 7d ed ee
  //   bd 7d ed bf bd 7d e1 7f b1 71 ef df bf 7f ef df bf 7f ef df bf 7f ef df bf 7f ef df bf 7f ef df bf
  //   7f ef df bf 7f ef df bf 7f ef df bf 7f eb db bb 7b e7 d7 b7 77 e3 d3 b3 73 ef df bf 7f ef df bf 7f
  //   ef df bf 7f e3 d3 b3 73 ef df bf 7f eb db bb 7b e7 d7 b7 77 e3 d3 b3 73 ef df bf 7f ef df bf 7f ef
  //   df bf 7f e3 d3 b3 73 ef df bf 7f eb db bb 7b e7 d7 b7 77 e3 d3 b3 73 ef df bf 7f ef df bf 7f ef df
  //   bf 7f e3 d3 b3 73 ef df bf 7f eb db bb 7b e7 d7 b7 77 e3 d3 b3 73 ef df bf 7f ef df bf 7f ef df bf
  //   7f e3 d3 b3 73 ef df bf 7f eb db bb 7b e7 d7 b7 77 e3 d3 b3 73 ef df bf 7f ef df bf 7f ef df bf 7f
  //   e3 d3 b3 73 ef df bf 7f eb db bb 7b e7 d7 b7 77 e3 d3 b3 73 ef df bf 7f ef df bf 7f ef df bf 7f e3
  //   d3 b3 73 ed df bd 7d e9 db b9 79 e5 d7 b5 75 e1 d3 b1 71 ed ef bd 7d ed ee bd 7d ed bf bd 7d e1 7f
  //   b1 71 ef df bf 7f ef df bf 7f ef df bf 7f ef df bf 7f ef df bf 7f ef df bf 7f ef df bf 7f ef df bf
  //   7f
endmodule

// 27C512
module CU_Registers_ROM (
  input  _1__A15,
  input  _28__Vcc,
  input  _2__A12,
  input  _27__A14,
  input  _3__A7,
  input  _26__A13,
  input  _4__A6,
  input  _25__A8,
  input  _5__A5,
  input  _24__A9,
  input  _6__A4,
  input  _23__A11,
  input  _7__A3,
  input  _22__nOE_Vpp,
  input  _8__A2,
  input  _21__A10,
  input  _9__A1,
  input  _20__nCE,
  input  _10__A0,
  input  _14__GND,
  output _19__O7,
  output _11__O0,
  output _18__O6,
  output _12__O1,
  output _17__O5,
  output _13__O2,
  output _16__O4,
  output _15__O3
);

  wire not_1_out;
  wire [7:0] rom_1_data;

  not not_1 (not_1_out, _22__nOE_Vpp);
  ROM_part #(.addrWidth(16)) rom_1 (
    .addr({_1__A15, _27__A14, _26__A13, _2__A12, _23__A11, _21__A10, _24__A9, _25__A8, _3__A7, _4__A6, _5__A5, _6__A4, _7__A3, _8__A2, _9__A1, _10__A0}),
    .data(rom_1_data));  // open: sel
  assign {_19__O7, _18__O6, _17__O5, _16__O4, _15__O3, _13__O2, _12__O1, _11__O0} = not_1_out ? rom_1_data : 8'bz;  // Controlled_Buffer controlled_buffer_1

  // Notes on the sheet:
  //   27C512: 64K x 8-bit EPROM 
  //   contents of rom_1 (hex, n*v repeats v):
  //   16*db 4*5f 4*9f 4*d7 4*f7 16*db 4*5f 4*9f 4*d7 4*f7 16*db 4*5f 4*9f 4*d7 4*f7 16*db 4*5f 4*9f 4*d7
  //   4*f7 16*db 4*5f 4*9f 4*d7 4*f7 16*db 4*5f 4*9f 4*d7 4*f7 df cf df df df cf df df df cf df df df cf
  //   df df 5f cf 5f 5f 9f df 9f 9f df cf df df ff cf ff ff 4*dc 4*de 4*df 4*de 4*df 4*de 4*df 4*de 16*db
  //   4*5f 4*9f 4*d7 4*f7 16*db 4*5f 4*9f 4*d7 4*f7 16*db 4*5f 4*9f 4*d7 4*f7 16*db 4*5f 4*9f 4*d7 4*f7
  //   16*db 4*5f 4*9f 4*d7 4*f7 16*db 4*5f 4*9f 4*d7 4*f7 df cf df df df cf df df df cf df df df cf df df
  //   5f cf 5f 5f 9f df 9f 9f df cf df df ff cf ff ff 4*dc 4*df 8*de 8*df 8*de 16*db 4*5f 4*9f 4*d7 4*f7
  //   16*db 4*5f 4*9f 4*d7 4*f7 16*db 4*5f 4*9f 4*d7 4*f7 16*db 4*5f 4*9f 4*d7 4*f7 16*db 4*5f 4*9f 4*d7
  //   4*f7 16*db 4*5f 4*9f 4*d7 4*f7 df cf df df df cf df df df cf df df df cf df df 5f cf 5f 5f 9f df 9f
  //   9f df cf df df ff cf ff ff 4*dc 12*df 16*de 16*db 4*5f 4*9f 4*d7 4*f7 16*db 4*5f 4*9f 4*d7 4*f7
  //   16*db 4*5f 4*9f 4*d7 4*f7 16*db 4*5f 4*9f 4*d7 4*f7 16*db 4*5f 4*9f 4*d7 4*f7 16*db 4*5f 4*9f 4*d7
  //   4*f7 df cf df df df cf df df df cf df df df cf df df 5f cf 5f 5f 9f df 9f 9f df cf df df ff cf ff ff
  //   4*dc 28*df
endmodule

// 27C512
module CU_ALU_ROM (
  input  _1__A15,
  input  _28__Vcc,
  input  _2__A12,
  input  _27__A14,
  input  _3__A7,
  input  _26__A13,
  input  _4__A6,
  input  _25__A8,
  input  _5__A5,
  input  _24__A9,
  input  _6__A4,
  input  _23__A11,
  input  _7__A3,
  input  _22__nOE_Vpp,
  input  _8__A2,
  input  _21__A10,
  input  _9__A1,
  input  _20__nCE,
  input  _10__A0,
  input  _14__GND,
  output _19__O7,
  output _11__O0,
  output _18__O6,
  output _12__O1,
  output _17__O5,
  output _13__O2,
  output _16__O4,
  output _15__O3
);

  wire not_1_out;
  wire [7:0] rom_1_data;

  not not_1 (not_1_out, _22__nOE_Vpp);
  ROM_part #(.addrWidth(16)) rom_1 (
    .addr({_1__A15, _27__A14, _26__A13, _2__A12, _23__A11, _21__A10, _24__A9, _25__A8, _3__A7, _4__A6, _5__A5, _6__A4, _7__A3, _8__A2, _9__A1, _10__A0}),
    .data(rom_1_data));  // open: sel
  assign {_19__O7, _18__O6, _17__O5, _16__O4, _15__O3, _13__O2, _12__O1, _11__O0} = not_1_out ? rom_1_data : 8'bz;  // Controlled_Buffer controlled_buffer_1

  // Notes on the sheet:
  //   27C512: 64K x 8-bit EPROM 
  //   contents of rom_1 (hex, n*v repeats v):
  //   32*ac 32*bc 32*ec 32*6c 32*94 32*60 fc ac fc fc fc ac fc fc fc ac fc fc fc ac fc fc fc ac fc fc fc
  //   af fc fc fc ac fc fc fc ac fc fc 32*f4 32*ac 32*bc 32*ec 32*6c 32*94 32*60 fc ac fc fc fc ac fc fc
  //   fc ac fc fc fc ac fc fc fc ac fc fc fc af fc fc fc ac fc fc fc ac fc fc 32*f4 32*ac 32*bc 32*ec
  //   32*6c 32*94 32*60 fc ac fc fc fc ac fc fc fc ac fc fc fc ac fc fc fc ac fc fc fc af fc fc fc ac fc
  //   fc fc ac fc fc 32*f4 32*ac 32*bc 32*ec 32*6c 32*94 32*60 fc ac fc fc fc ac fc fc fc ac fc fc fc ac
  //   fc fc fc ac fc fc fc af fc fc fc ac fc fc fc ac fc fc 32*f4
endmodule

module ALU (
  input  M,
  input  Cn,
  input  [3:0] S,
  input  [7:0] AC,
  input  [7:0] Bus,
  output [7:0] ALU,
  output A_B
);

  wire n74181_1__14__a_b, n74181_2__14__a_b, n74181_2__16__cn_4;

  _74181 u_74181_1 (
    ._1__nB0(Bus[4]), ._2__nA0(AC[4]), ._3__S3(S[3]), ._4__S2(S[2]), ._5__S1(S[1]), ._6__S0(S[0]),
    ._7__Cn(n74181_2__16__cn_4), ._8__M(M), ._9__nF0(ALU[4]), ._10__nF1(ALU[5]), ._11__nF2(ALU[6]),
    ._23__nA1(AC[5]), ._22__nB1(Bus[5]), ._21__nA2(AC[6]), ._20__nB2(Bus[6]), ._19__nA3(AC[7]),
    ._18__nB3(Bus[7]), ._14__A_B(n74181_1__14__a_b), ._13__nF3(ALU[7]));  // open: _12__GND, _24__Vcc, _17__nG, _16__Cn_4, _15__nP
  _74181 u_74181_2 (
    ._1__nB0(Bus[0]), ._2__nA0(AC[0]), ._3__S3(S[3]), ._4__S2(S[2]), ._5__S1(S[1]), ._6__S0(S[0]),
    ._7__Cn(Cn), ._8__M(M), ._9__nF0(ALU[0]), ._10__nF1(ALU[1]), ._11__nF2(ALU[2]), ._23__nA1(AC[1]),
    ._22__nB1(Bus[1]), ._21__nA2(AC[2]), ._20__nB2(Bus[2]), ._19__nA3(AC[3]), ._18__nB3(Bus[3]),
    ._16__Cn_4(n74181_2__16__cn_4), ._14__A_B(n74181_2__14__a_b), ._13__nF3(ALU[3]));  // open: _12__GND, _24__Vcc, _17__nG, _15__nP
  and and_1 (A_B, n74181_2__14__a_b, n74181_1__14__a_b);
endmodule

module ROM (
  input  [15:0] From_PC,
  output [7:0] To_IR,
  output [7:0] To_D
);

  ROM_part #(.addrWidth(16), .dataWidth(16)) rom_1 (.addr(From_PC), .data({To_D, To_IR}));  // open: sel

  // Notes on the sheet:
  //   contents of rom_1 (hex, n*v repeats v):
  //   0 2c2 3 3c2 4c2 401 1a0 4c2 301 c2 401 1c2 0 2c2 101 19f0 2 1 281 2c2 101 1a0 1c2 efc 2 201 3c2 401
  //   1a0 5e4 2 301 1a 2
endmodule

module RAM (
  input  nWE,
  input  nOE,
  input  [14:0] Address,
  input  [7:0] Input,
  output [7:0] Output
);

  wire and_1_out, not_1_out;
  wire [7:0] ram_1_data;

  RAM_part #(.addrWidth(15), .bus("asynch")) ram_1 (.addr(Address), .data(ram_1_data), .ld(nWE));  // open: sel, clr
  assign ram_1_data = not_1_out ? Input : 8'bz;  // Controlled_Buffer controlled_buffer_1
  not not_1 (not_1_out, nWE);
  and and_1 (and_1_out, nWE, ~nOE);  // AND_Gate
  assign Output = and_1_out ? ram_1_data : 8'bz;  // Controlled_Buffer controlled_buffer_2
endmodule

// MAU
module MAU__Memory_Address_Unit (
  input  EL,
  input  EH,
  input  [7:0] Fropm_X,
  input  [7:0] From_D,
  input  [7:0] From_Y,
  output [14:0] To_RAM
);

  wire n74157_4__12__y4;

  _74157 u_74157_1 (
    ._1__S(EL), ._2__A1(Fropm_X[0]), ._3__B1(From_D[0]), ._4__Y1(To_RAM[0]), ._5__A2(Fropm_X[1]),
    ._6__B2(From_D[1]), ._7__Y2(To_RAM[1]), ._15__G(1'b0), ._14__A4(Fropm_X[3]), ._13__B4(From_D[3]),
    ._12__Y4(To_RAM[3]), ._11__A3(Fropm_X[2]), ._10__B3(From_D[2]), ._9__Y3(To_RAM[2]));  // open: _8__GND, _16__Vcc
  _74157 u_74157_2 (
    ._1__S(EL), ._2__A1(Fropm_X[4]), ._3__B1(From_D[4]), ._4__Y1(To_RAM[4]), ._5__A2(Fropm_X[5]),
    ._6__B2(From_D[5]), ._7__Y2(To_RAM[5]), ._15__G(1'b0), ._14__A4(Fropm_X[7]), ._13__B4(From_D[7]),
    ._12__Y4(To_RAM[7]), ._11__A3(Fropm_X[6]), ._10__B3(From_D[6]), ._9__Y3(To_RAM[6]));  // open: _8__GND, _16__Vcc
  _74157 u_74157_3 (
    ._1__S(1'b0), ._2__A1(From_Y[0]), ._3__B1(1'b1), ._4__Y1(To_RAM[8]), ._5__A2(From_Y[1]), ._6__B2(1'b1),
    ._7__Y2(To_RAM[9]), ._15__G(EH), ._14__A4(From_Y[3]), ._13__B4(1'b1), ._12__Y4(To_RAM[11]),
    ._11__A3(From_Y[2]), ._10__B3(1'b1), ._9__Y3(To_RAM[10]));  // open: _8__GND, _16__Vcc
  _74157 u_74157_4 (
    ._1__S(1'b0), ._2__A1(From_Y[4]), ._3__B1(1'b1), ._4__Y1(To_RAM[12]), ._5__A2(From_Y[5]), ._6__B2(1'b1),
    ._7__Y2(To_RAM[13]), ._15__G(EH), ._14__A4(From_Y[7]), ._13__B4(1'b1), ._12__Y4(n74157_4__12__y4),
    ._11__A3(From_Y[6]), ._10__B3(1'b1), ._9__Y3(To_RAM[14]));  // open: _8__GND, _16__Vcc
endmodule

// IOU
module IOU__Input_Ouput_Unit (
  input  nIE,
  input  nOL,
  input  nCSE,
  input  [7:0] from_input_output_control_register,
  output nIE1__input_enable_1,
  output nIE2__input_enable_2,
  output nIE3__input_enable_3,
  output nIE4__input_enable_4,
  output nOW1__output_write_1,
  output nOW2__output_write_2,
  output nOW3__output_write_3,
  output nOW4__output_write_4,
  output nPC1__peripheral_control_1,
  output nPC2__peripheral_control_2,
  output nPC3__peripheral_control_3,
  output nPC4__peripheral_control_4,
  output nPC5__peripheral_control_5,
  output nPC6__peripheral_control_6,
  output nPC7__peripheral_control_7,
  output nPC8__peripheral_control_8
);

  Pull_Resistor #(.pull(1)) pull_resistor_1 (.node(nIE4__input_enable_4));
  Pull_Resistor #(.pull(1)) pull_resistor_2 (.node(nIE3__input_enable_3));
  Pull_Resistor #(.pull(1)) pull_resistor_3 (.node(nIE2__input_enable_2));
  Pull_Resistor #(.pull(1)) pull_resistor_4 (.node(nIE1__input_enable_1));
  Pull_Resistor #(.pull(1)) pull_resistor_5 (.node(nPC2__peripheral_control_2));
  Pull_Resistor #(.pull(1)) pull_resistor_6 (.node(nPC4__peripheral_control_4));
  Pull_Resistor #(.pull(1)) pull_resistor_7 (.node(nPC3__peripheral_control_3));
  Pull_Resistor #(.pull(1)) pull_resistor_8 (.node(nPC1__peripheral_control_1));
  _74240 u_74240_1 (
    ._1___1G(nIE), ._2__1A1(from_input_output_control_register[0]), ._3__2Y4(nOW4__output_write_4),
    ._4__1A2(from_input_output_control_register[1]), ._5__2Y3(nOW3__output_write_3),
    ._6__1A3(from_input_output_control_register[2]), ._7__2Y2(nOW2__output_write_2),
    ._8__1A4(from_input_output_control_register[3]), ._9__2Y1(nOW1__output_write_1), ._19___2G(nOL),
    ._18__1Y1(nIE1__input_enable_1), ._17__2A4(from_input_output_control_register[7]),
    ._16__1Y2(nIE2__input_enable_2), ._15__2A3(from_input_output_control_register[6]),
    ._14__1Y3(nIE3__input_enable_3), ._13__2A2(from_input_output_control_register[5]),
    ._12__1Y4(nIE4__input_enable_4), ._11__2A1(from_input_output_control_register[4]));  // open: _10__GND, _20__Vcc
  _74240 u_74240_2 (
    ._1___1G(nCSE), ._2__1A1(from_input_output_control_register[0]), ._3__2Y4(nPC8__peripheral_control_8),
    ._4__1A2(from_input_output_control_register[1]), ._5__2Y3(nPC7__peripheral_control_7),
    ._6__1A3(from_input_output_control_register[2]), ._7__2Y2(nPC6__peripheral_control_6),
    ._8__1A4(from_input_output_control_register[3]), ._9__2Y1(nPC5__peripheral_control_5), ._19___2G(nCSE),
    ._18__1Y1(nPC1__peripheral_control_1), ._17__2A4(from_input_output_control_register[7]),
    ._16__1Y2(nPC2__peripheral_control_2), ._15__2A3(from_input_output_control_register[6]),
    ._14__1Y3(nPC3__peripheral_control_3), ._13__2A2(from_input_output_control_register[5]),
    ._12__1Y4(nPC4__peripheral_control_4), ._11__2A1(from_input_output_control_register[4]));  // open: _10__GND, _20__Vcc
  Pull_Resistor #(.pull(1)) pull_resistor_9 (.node(nOW4__output_write_4));
  Pull_Resistor #(.pull(1)) pull_resistor_10 (.node(nOW3__output_write_3));
  Pull_Resistor #(.pull(1)) pull_resistor_11 (.node(nPC7__peripheral_control_7));
  Pull_Resistor #(.pull(1)) pull_resistor_12 (.node(nPC8__peripheral_control_8));
  Pull_Resistor #(.pull(1)) pull_resistor_13 (.node(nOW2__output_write_2));
  Pull_Resistor #(.pull(1)) pull_resistor_14 (.node(nOW1__output_write_1));
  Pull_Resistor #(.pull(1)) pull_resistor_15 (.node(nPC6__peripheral_control_6));
  Pull_Resistor #(.pull(1)) pull_resistor_16 (.node(nPC5__peripheral_control_5));
endmodule

// PC
module PC__Program_Counter (
  input  clk,
  input  nreset,
  input  nPL,
  input  nPH,
  input  [7:0] From_Bus,
  input  [7:0] From_Y,
  output [15:0] To_ROM
);

  wire n74161_1__15__tc, n74161_2__15__tc, n74161_3__15__tc;

  _74161 u_74161_1 (
    ._1__nMR(nreset), ._2__CP(clk), ._3__D0(From_Bus[0]), ._4__D1(From_Bus[1]), ._5__D2(From_Bus[2]),
    ._6__D3(From_Bus[3]), ._7__CEP(1'b1), ._15__TC(n74161_1__15__tc), ._14__Q0(To_ROM[0]),
    ._13__Q1(To_ROM[1]), ._12__Q2(To_ROM[2]), ._11__O3(To_ROM[3]), ._10__CET(1'b1), ._9__nPE(nPL));  // open: _8__GND, _16__Vcc
  _74161 u_74161_2 (
    ._1__nMR(nreset), ._2__CP(clk), ._3__D0(From_Bus[4]), ._4__D1(From_Bus[5]), ._5__D2(From_Bus[6]),
    ._6__D3(From_Bus[7]), ._7__CEP(1'b1), ._15__TC(n74161_2__15__tc), ._14__Q0(To_ROM[4]),
    ._13__Q1(To_ROM[5]), ._12__Q2(To_ROM[6]), ._11__O3(To_ROM[7]), ._10__CET(n74161_1__15__tc), ._9__nPE(nPL));  // open: _8__GND, _16__Vcc
  _74161 u_74161_3 (
    ._1__nMR(nreset), ._2__CP(clk), ._3__D0(From_Y[0]), ._4__D1(From_Y[1]), ._5__D2(From_Y[2]),
    ._6__D3(From_Y[3]), ._7__CEP(nPL), ._15__TC(n74161_3__15__tc), ._14__Q0(To_ROM[8]), ._13__Q1(To_ROM[9]),
    ._12__Q2(To_ROM[10]), ._11__O3(To_ROM[11]), ._10__CET(n74161_2__15__tc), ._9__nPE(nPH));  // open: _8__GND, _16__Vcc
  _74161 u_74161_4 (
    ._1__nMR(nreset), ._2__CP(clk), ._3__D0(From_Y[4]), ._4__D1(From_Y[5]), ._5__D2(From_Y[6]),
    ._6__D3(From_Y[7]), ._7__CEP(nPL), ._14__Q0(To_ROM[12]), ._13__Q1(To_ROM[13]), ._12__Q2(To_ROM[14]),
    ._11__O3(To_ROM[15]), ._10__CET(n74161_3__15__tc), ._9__nPE(nPH));  // open: _8__GND, _16__Vcc, _15__TC
endmodule

// IR
module IR__Instruction_register (
  input  CP,
  input  [7:0] D,
  output [7:0] Q
);

  _74273 u_74273_1 (
    ._1__nCLR(1'b1), ._2__Q0(Q[0]), ._3__D0(D[0]), ._4__D1(D[1]), ._5__Q1(Q[1]), ._6__Q2(Q[2]),
    ._7__D2(D[2]), ._8__D3(D[3]), ._9__Q3(Q[3]), ._19__Q7(Q[7]), ._18__D7(D[7]), ._17__D6(D[6]),
    ._16__Q6(Q[6]), ._15__Q5(Q[5]), ._14__D5(D[5]), ._13__D4(D[4]), ._12__Q4(Q[4]), ._11__CP(CP));  // open: _10__GND, _20__Vcc
endmodule

// D
module D__Data_register (
  input  CP,
  input  [7:0] D,
  output [7:0] Q
);

  _74273 u_74273_1 (
    ._1__nCLR(1'b1), ._2__Q0(Q[0]), ._3__D0(D[0]), ._4__D1(D[1]), ._5__Q1(Q[1]), ._6__Q2(Q[2]),
    ._7__D2(D[2]), ._8__D3(D[3]), ._9__Q3(Q[3]), ._19__Q7(Q[7]), ._18__D7(D[7]), ._17__D6(D[6]),
    ._16__Q6(Q[6]), ._15__Q5(Q[5]), ._14__D5(D[5]), ._13__D4(D[4]), ._12__Q4(Q[4]), ._11__CP(CP));  // open: _10__GND, _20__Vcc
endmodule

// AC register
module AC__Accumulator_register (
  input  CP,
  input  nE,
  input  [7:0] D,
  output [7:0] Q
);

  _74377 u_74377_1 (
    ._1__nE(nE), ._2__Q0(Q[0]), ._3__D0(D[0]), ._4__D1(D[1]), ._5__Q1(Q[1]), ._6__Q2(Q[2]), ._7__D2(D[2]),
    ._8__D3(D[3]), ._9__Q3(Q[3]), ._19__Q7(Q[7]), ._18__D7(D[7]), ._17__D6(D[6]), ._16__Q6(Q[6]),
    ._15__Q5(Q[5]), ._14__D5(D[5]), ._13__D4(D[4]), ._12__Q4(Q[4]), ._11__CP(CP));  // open: _10__GND, _20__Vcc
endmodule

// X
module X__X_register (
  input  CP,
  input  IX,
  input  nXL,
  input  [7:0] From_ALU,
  output [7:0] X_output
);

  wire n74161_1__15__tc;

  _74161 u_74161_1 (
    ._1__nMR(1'b1), ._2__CP(CP), ._3__D0(From_ALU[0]), ._4__D1(From_ALU[1]), ._5__D2(From_ALU[2]),
    ._6__D3(From_ALU[3]), ._7__CEP(IX), ._15__TC(n74161_1__15__tc), ._14__Q0(X_output[0]),
    ._13__Q1(X_output[1]), ._12__Q2(X_output[2]), ._11__O3(X_output[3]), ._10__CET(1'b1), ._9__nPE(nXL));  // open: _8__GND, _16__Vcc
  _74161 u_74161_2 (
    ._1__nMR(1'b1), ._2__CP(CP), ._3__D0(From_ALU[4]), ._4__D1(From_ALU[5]), ._5__D2(From_ALU[6]),
    ._6__D3(From_ALU[7]), ._7__CEP(IX), ._14__Q0(X_output[4]), ._13__Q1(X_output[5]), ._12__Q2(X_output[6]),
    ._11__O3(X_output[7]), ._10__CET(n74161_1__15__tc), ._9__nPE(nXL));  // open: _8__GND, _16__Vcc, _15__TC
endmodule

// Y
module Y__Y_register (
  input  CP,
  input  nE,
  input  [7:0] D,
  output [7:0] Q
);

  _74377 u_74377_1 (
    ._1__nE(nE), ._2__Q0(Q[0]), ._3__D0(D[0]), ._4__D1(D[1]), ._5__Q1(Q[1]), ._6__Q2(Q[2]), ._7__D2(D[2]),
    ._8__D3(D[3]), ._9__Q3(Q[3]), ._19__Q7(Q[7]), ._18__D7(D[7]), ._17__D6(D[6]), ._16__Q6(Q[6]),
    ._15__Q5(Q[5]), ._14__D5(D[5]), ._13__D4(D[4]), ._12__Q4(Q[4]), ._11__CP(CP));  // open: _10__GND, _20__Vcc
endmodule

// IOC register
module IOC__Input_Output_Control_register (
  input  CP,
  input  nE,
  input  [7:0] ALU,
  output [7:0] peripherals
);

  _74377 u_74377_1 (
    ._1__nE(nE), ._2__Q0(peripherals[0]), ._3__D0(ALU[0]), ._4__D1(ALU[1]), ._5__Q1(peripherals[1]),
    ._6__Q2(peripherals[2]), ._7__D2(ALU[2]), ._8__D3(ALU[3]), ._9__Q3(peripherals[3]),
    ._19__Q7(peripherals[7]), ._18__D7(ALU[7]), ._17__D6(ALU[6]), ._16__Q6(peripherals[6]),
    ._15__Q5(peripherals[5]), ._14__D5(ALU[5]), ._13__D4(ALU[4]), ._12__Q4(peripherals[4]), ._11__CP(CP));  // open: _10__GND, _20__Vcc
endmodule

// OUT
module OUT__Output_register (
  input  CP,
  input  nE,
  input  [7:0] D,
  output [7:0] Q
);

  _74377 u_74377_1 (
    ._1__nE(nE), ._2__Q0(Q[0]), ._3__D0(D[0]), ._4__D1(D[1]), ._5__Q1(Q[1]), ._6__Q2(Q[2]), ._7__D2(D[2]),
    ._8__D3(D[3]), ._9__Q3(Q[3]), ._19__Q7(Q[7]), ._18__D7(D[7]), ._17__D6(D[6]), ._16__Q6(Q[6]),
    ._15__Q5(Q[5]), ._14__D5(D[5]), ._13__D4(D[4]), ._12__Q4(Q[4]), ._11__CP(CP));  // open: _10__GND, _20__Vcc
endmodule

// XOUT
module XOUT__Extented_Output (
  input  CP,
  input  [7:0] D,
  output [7:0] Q
);

  _74273 u_74273_1 (
    ._1__nCLR(1'b1), ._2__Q0(Q[0]), ._3__D0(D[0]), ._4__D1(D[1]), ._5__Q1(Q[1]), ._6__Q2(Q[2]),
    ._7__D2(D[2]), ._8__D3(D[3]), ._9__Q3(Q[3]), ._19__Q7(Q[7]), ._18__D7(D[7]), ._17__D6(D[6]),
    ._16__Q6(Q[6]), ._15__Q5(Q[5]), ._14__D5(D[5]), ._13__D4(D[4]), ._12__Q4(Q[4]), ._11__CP(CP));  // open: _10__GND, _20__Vcc
endmodule

// BUS-D
module BUS_D__Tristate_Buffer (
  input  _1G,
  input  _2G,
  input  [7:0] D,
  output [7:0] Q
);

  _74244 u_74244_1 (
    ._1___1G(_1G), ._2__1A1(D[0]), ._3__2Y4(Q[7]), ._4__1A2(D[1]), ._5__2Y3(Q[6]), ._6__1A3(D[2]),
    ._7__2Y2(Q[5]), ._8__1A4(D[3]), ._9__2Y1(Q[4]), ._19___2G(_2G), ._18__1Y1(Q[0]), ._17__2A4(D[7]),
    ._16__1Y2(Q[1]), ._15__2A3(D[6]), ._14__1Y3(Q[2]), ._13__2A2(D[5]), ._12__1Y4(Q[3]), ._11__2A1(D[4]));  // open: _10__GND, _20__Vcc
endmodule

// BUS-AC
module BUS_AC__Tristate_Buffer (
  input  _1G,
  input  _2G,
  input  [7:0] D,
  output [7:0] Q
);

  _74244 u_74244_1 (
    ._1___1G(_1G), ._2__1A1(D[0]), ._3__2Y4(Q[7]), ._4__1A2(D[1]), ._5__2Y3(Q[6]), ._6__1A3(D[2]),
    ._7__2Y2(Q[5]), ._8__1A4(D[3]), ._9__2Y1(Q[4]), ._19___2G(_2G), ._18__1Y1(Q[0]), ._17__2A4(D[7]),
    ._16__1Y2(Q[1]), ._15__2A3(D[6]), ._14__1Y3(Q[2]), ._13__2A2(D[5]), ._12__1Y4(Q[3]), ._11__2A1(D[4]));  // open: _10__GND, _20__Vcc
endmodule

// BUS-IN
module BUS_IN__Tristate_Buffer (
  input  _1G,
  input  _2G,
  input  [7:0] D,
  output [7:0] Q
);

  _74244 u_74244_1 (
    ._1___1G(_1G), ._2__1A1(D[0]), ._3__2Y4(Q[7]), ._4__1A2(D[1]), ._5__2Y3(Q[6]), ._6__1A3(D[2]),
    ._7__2Y2(Q[5]), ._8__1A4(D[3]), ._9__2Y1(Q[4]), ._19___2G(_2G), ._18__1Y1(Q[0]), ._17__2A4(D[7]),
    ._16__1Y2(Q[1]), ._15__2A3(D[6]), ._14__1Y3(Q[2]), ._13__2A2(D[5]), ._12__1Y4(Q[3]), ._11__2A1(D[4]));  // open: _10__GND, _20__Vcc
endmodule

// GAMEPAD-IN
module GAMEPAD_IN__Shifter_8_bits (
  input  PCLK,
  input  CLK,
  input  nOE,
  input  SER_IN,
  output [7:0] out_5
);

  _74595 u_74595_1 (
    ._1__QB(out_5[1]), ._2__QC(out_5[2]), ._3__QD(out_5[3]), ._4__QE(out_5[4]), ._5__QF(out_5[5]),
    ._6__QG(out_5[6]), ._7__QH(out_5[7]), ._15__QA(out_5[0]), ._14__SER(SER_IN), ._13__nOE(nOE),
    ._12__RCLK(PCLK), ._11__SRCLK(CLK), ._10__nSRCLR(1'b1));  // open: _8__GND, _16__Vcc, _9__QH_prime
endmodule

// KEYBOARD-IN
module KEYBOARD_IN__Shifter_8_bits (
  input  PCLK,
  input  CLK,
  input  nOE,
  input  SER_IN,
  output [7:0] out_5
);

  _74595 u_74595_1 (
    ._1__QB(out_5[1]), ._2__QC(out_5[2]), ._3__QD(out_5[3]), ._4__QE(out_5[4]), ._5__QF(out_5[5]),
    ._6__QG(out_5[6]), ._7__QH(out_5[7]), ._15__QA(out_5[0]), ._14__SER(SER_IN), ._13__nOE(nOE),
    ._12__RCLK(PCLK), ._11__SRCLK(CLK), ._10__nSRCLR(1'b1));  // open: _8__GND, _16__Vcc, _9__QH_prime
endmodule
