// Logisim project Nes controller.circ as structural Verilog: 2 circuits, main circuit NES controller
module NES_controller (
  input  NES_Clock__2,
  input  NES_Latch__3,
  input  NES_VCC__7,
  input  NES_GND__1,
  output Controller_data__4,
  output out_6,
  output out_7,
  output out_8,
  output out_9,
  output out_10,
  output out_11,
  output out_12,
  output B,
  output A
);

  wire A_out, B_out, bas_out, droite_out, gauche_out, haut_out, n4021_1_serial_out_6bit__q6,
       n4021_1_serial_out_7bit__q7, select_out, start_out, undriven;

  Button droite (.out(droite_out));
  Button gauche (.out(gauche_out));
  Button bas (.out(bas_out));
  Button haut (.out(haut_out));
  Button start (.out(start_out));
  Button select (.out(select_out));
  Button u_B (.out(B_out));
  Button u_A (.out(A_out));
  Pull_Resistor #(.pull(1)) pull_resistor_1 (.node(bas_out));
  Pull_Resistor #(.pull(1)) pull_resistor_2 (.node(gauche_out));
  Pull_Resistor #(.pull(1)) pull_resistor_3 (.node(droite_out));
  Pull_Resistor #(.pull(1)) pull_resistor_4 (.node(B_out));
  Pull_Resistor #(.pull(1)) pull_resistor_5 (.node(start_out));
  Pull_Resistor #(.pull(1)) pull_resistor_6 (.node(select_out));
  Pull_Resistor #(.pull(1)) pull_resistor_7 (.node(haut_out));
  Pull_Resistor #(.pull(1)) pull_resistor_8 (.node(A_out));
  Pull_Resistor #(.pull(1)) pull_resistor_9 (.node(NES_Clock__2));
  Pull_Resistor #(.pull(1)) pull_resistor_10 (.node(NES_Latch__3));
  _4021 u_4021_1 (
    .clk(NES_Clock__2), .serial_in(undriven), .parallel_serial_control(NES_Latch__3),
    .parallel_1__P1(droite_out), .parallel_2__P2(gauche_out), .parallel_3__P3(bas_out),
    .parallel_4__P4(haut_out), .parallel_5__P5(start_out), .parallel_6__P6(select_out),
    .parallel_7__P7(B_out), .parallel_8__P8(A_out), .serial_out_8bit__Q8(Controller_data__4),
    .serial_out_7bit__Q7(n4021_1_serial_out_7bit__q7), .serial_out_6bit__Q6(n4021_1_serial_out_6bit__q6));

  // Notes on the sheet:
  //   GND
  //   GND
  //   GND
  //   GND
  //   GND
  //   GND
  //   GND
  //   GND
  //   1K Ohm
  //   GND
  //   3K6 Ohm
  //   pin 11
  //   S-in
  //   pin 7
  //   P1
  //   pin 6
  //   P2
  //   pin 5
  //   P3
  //   pin 4
  //   P4
  //   pin 13
  //   P5
  //   pin 14
  //   P6
  //   pin 15
  //   P7
  //   pin 1
  //   P8
  //   Q8
  //   Parallel
  //   Q7
  //   Q6
  //   To Serial
  //   Shifter
  //   (4021)
  //   pin 16 = VCC
  //   pin 8 = GND
  //   3K6 Ohm
  //   pin 3
  //   pin 12
  //   pin 2
  //   gauche
  //   Prise manette NES
  //   haut
  //   droite
  //   selcect
  //   bas
  //   start
endmodule

module _4021 (
  input  clk,
  input  serial_in,
  input  parallel_serial_control,
  input  parallel_1__P1,
  input  parallel_2__P2,
  input  parallel_3__P3,
  input  parallel_4__P4,
  input  parallel_5__P5,
  input  parallel_6__P6,
  input  parallel_7__P7,
  input  parallel_8__P8,
  output serial_out_8bit__Q8,
  output serial_out_7bit__Q7,
  output serial_out_6bit__Q6
);

  wire and_1_out, controlled_buffer_1_out, controlled_buffer_2_out, controlled_buffer_3_out,
       controlled_buffer_4_out, controlled_buffer_5_out, controlled_buffer_6_out, controlled_buffer_7_out,
       controlled_buffer_8_out, controlled_buffer_9_out, controlled_buffer_10_out, controlled_buffer_11_out,
       controlled_buffer_12_out, controlled_buffer_13_out, controlled_buffer_14_out,
       controlled_buffer_15_out, controlled_buffer_16_out, d_ff_1_q, d_ff_2_q, d_ff_3_q, d_ff_4_q, d_ff_5_q,
       not_1_out, not_2_out, not_3_out, not_4_out, not_5_out, not_6_out, not_7_out, not_8_out;

  and and_1 (and_1_out, clk, ~parallel_serial_control);  // AND_Gate
  D_Flip_Flop d_ff_1 (
    .clk(and_1_out), .D(serial_in), .Q(d_ff_1_q), .preset(controlled_buffer_2_out),
    .reset(controlled_buffer_1_out));  // open: Qn, en
  assign controlled_buffer_1_out = parallel_serial_control ? not_1_out : 1'bz;  // Controlled_Buffer controlled_buffer_1
  assign controlled_buffer_2_out = parallel_serial_control ? parallel_1__P1 : 1'bz;  // Controlled_Buffer controlled_buffer_2
  not not_1 (not_1_out, parallel_1__P1);
  D_Flip_Flop d_ff_2 (
    .clk(and_1_out), .D(d_ff_1_q), .Q(d_ff_2_q), .preset(controlled_buffer_4_out),
    .reset(controlled_buffer_3_out));  // open: Qn, en
  assign controlled_buffer_3_out = parallel_serial_control ? not_2_out : 1'bz;  // Controlled_Buffer controlled_buffer_3
  not not_2 (not_2_out, parallel_2__P2);
  assign controlled_buffer_4_out = parallel_serial_control ? parallel_2__P2 : 1'bz;  // Controlled_Buffer controlled_buffer_4
  D_Flip_Flop d_ff_3 (
    .clk(and_1_out), .D(d_ff_2_q), .Q(d_ff_3_q), .preset(controlled_buffer_6_out),
    .reset(controlled_buffer_5_out));  // open: Qn, en
  assign controlled_buffer_5_out = parallel_serial_control ? not_3_out : 1'bz;  // Controlled_Buffer controlled_buffer_5
  not not_3 (not_3_out, parallel_3__P3);
  assign controlled_buffer_6_out = parallel_serial_control ? parallel_3__P3 : 1'bz;  // Controlled_Buffer controlled_buffer_6
  assign controlled_buffer_7_out = parallel_serial_control ? parallel_4__P4 : 1'bz;  // Controlled_Buffer controlled_buffer_7
  D_Flip_Flop d_ff_4 (
    .clk(and_1_out), .D(d_ff_3_q), .Q(d_ff_4_q), .preset(controlled_buffer_7_out),
    .reset(controlled_buffer_8_out));  // open: Qn, en
  assign controlled_buffer_8_out = parallel_serial_control ? not_4_out : 1'bz;  // Controlled_Buffer controlled_buffer_8
  not not_4 (not_4_out, parallel_4__P4);
  D_Flip_Flop d_ff_5 (
    .clk(and_1_out), .D(d_ff_4_q), .Q(d_ff_5_q), .preset(controlled_buffer_10_out),
    .reset(controlled_buffer_9_out));  // open: Qn, en
  assign controlled_buffer_9_out = parallel_serial_control ? not_5_out : 1'bz;  // Controlled_Buffer controlled_buffer_9
  not not_5 (not_5_out, parallel_5__P5);
  assign controlled_buffer_10_out = parallel_serial_control ? parallel_5__P5 : 1'bz;  // Controlled_Buffer controlled_buffer_10
  D_Flip_Flop d_ff_6 (
    .clk(and_1_out), .D(d_ff_5_q), .Q(serial_out_6bit__Q6), .preset(controlled_buffer_12_out),
    .reset(controlled_buffer_11_out));  // open: Qn, en
  assign controlled_buffer_11_out = parallel_serial_control ? not_6_out : 1'bz;  // Controlled_Buffer controlled_buffer_11
  not not_6 (not_6_out, parallel_6__P6);
  assign controlled_buffer_12_out = parallel_serial_control ? parallel_6__P6 : 1'bz;  // Controlled_Buffer controlled_buffer_12
  D_Flip_Flop d_ff_7 (
    .clk(and_1_out), .D(serial_out_6bit__Q6), .Q(serial_out_7bit__Q7), .preset(controlled_buffer_14_out),
    .reset(controlled_buffer_13_out));  // open: Qn, en
  assign controlled_buffer_13_out = parallel_serial_control ? not_7_out : 1'bz;  // Controlled_Buffer controlled_buffer_13
  assign controlled_buffer_14_out = parallel_serial_control ? parallel_7__P7 : 1'bz;  // Controlled_Buffer controlled_buffer_14
  not not_7 (not_7_out, parallel_7__P7);
  assign controlled_buffer_15_out = parallel_serial_control ? parallel_8__P8 : 1'bz;  // Controlled_Buffer controlled_buffer_15
  D_Flip_Flop d_ff_8 (
    .clk(and_1_out), .D(serial_out_7bit__Q7), .Q(serial_out_8bit__Q8), .preset(controlled_buffer_15_out),
    .reset(controlled_buffer_16_out));  // open: Qn, en
  assign controlled_buffer_16_out = parallel_serial_control ? not_8_out : 1'bz;  // Controlled_Buffer controlled_buffer_16
  not not_8 (not_8_out, parallel_8__P8);
endmodule
